// Logisim project bitwright.circ as structural Verilog: 2 circuits, main circuit Bitwright
module Bitwright (
  input  Reset,
  output [15:0] PC,
  output [7:0] A,
  output [7:0] X,
  output [7:0] Y,
  output [7:0] SP,
  output [7:0] P,
  output [7:0] IR,
  output [7:0] State,
  output [15:0] Address,
  output [7:0] WriteData,
  output [7:0] ReadData,
  output Write,
  output Read,
  output Sync,
  output Fault
);

  wire Busy, IoSelect, RamWrite, Ready, SysClock;
  wire [4:0] CursorY, Origin;
  wire [5:0] CursorX;
  wire [7:0] IoData, RamData, RomData;
  wire [11:0] BankAddress;

  Clock #(.highDuration(1), .lowDuration(1)) MachineClock (.out(SysClock));
  MemoryMap memorymap_1 (
    .Address(Address), .Write(Write), .Reset(Reset), .RamData(RamData), .RomData(RomData), .IoData(IoData),
    .BankAddress(BankAddress), .RamWrite(RamWrite), .ReadData(ReadData), .IoSelect(IoSelect));
  Cpu6502 cpu6502_1 (
    .SysClock(SysClock), .Reset(Reset), .DataIn(ReadData), .IRQ(1'b0), .NMI(1'b0), .Address(Address),
    .DataOut(WriteData), .Write(Write), .Read(Read), .Sync(Sync), .Fault(Fault), .PC(PC), .A(A), .X(X),
    .Y(Y), .SP(SP), .P(P), .IR(IR), .State(State));
  Apple1Console apple1console_1 (
    .Address(Address), .DataIn(WriteData), .Write(Write), .Read(Read), .SysClock(SysClock), .Reset(Reset),
    .DataOut(IoData), .Ready(Ready), .Busy(Busy), .CursorX(CursorX), .CursorY(CursorY), .Origin(Origin));
  RAM #(.addrWidth(12), .dataWidth(8), .databus("bibus"), .enables("byte"), .asyncread("true"), .trigger("falling"), .clearpin("false")) PROGRAM_RAM (
    .addr(BankAddress), .we(RamWrite), .oe(1'b1), .clk(SysClock), .din(WriteData), .dout(RamData));
  ROM #(.addrWidth(12), .dataWidth(8)) PROGRAM_ROM (.addr(BankAddress), .data(RomData));

  // Notes on the sheet:
  //   Reset: initial=0x1
  //   BITWRIGHT / APPLE-1-INSPIRED GATE-BUILT COMPUTER
  //   Reset starts high: set it to 0, then enable ticks. Open the Console instance to type or load a .mon file.
  //   Assembly is compiled on the host; monitor firmware loads RAM; circuit CPU executes every instruction.
  //   Double-click CPU: inspect datapath and hardwired control.
  //   CPU storage is built from gates; console uses single-bit DFFs; bulk RAM/ROM are foundations.
  //   Documented 6502 encodings; functional timing. See coverage and measured compatibility limits.
  //   CONSOLE / enter this instance for keyboard, file loader and pixel screen
  //   4 KiB RAM / programs, variables and stack
  //   Firmware ROM / F000-FFFF; reset vector FFFC/FFFD
  //   contents of PROGRAM_ROM (hex, n*v repeats v):
  //   d8 78 a2 ff 9a a9 a7 8d 11 d0 8d 13 d0 a2 00 bd 5e f2 f0 06 20 2e f2 e8 d0 f5 d8 a2 ff 9a 20 37 f2
  //   a9 5c 20 2e f2 a9 20 20 2e f2 a2 00 20 23 f2 c9 20 90 21 c9 7f f0 30 e0 4f b0 f1 c9 61 90 06 c9 7b
  //   b0 02 29 5f 9d 00 02 e8 2c 12 d0 30 fb 8d 12 d0 4c 2d f0 c9 1b f0 c1 c9 08 f0 0b c9 0d f0 14 c9 0a
  //   f0 10 4c 2d f0 e0 00 f0 c1 ca a9 08 20 2e f2 4c 2d f0 a9 00 9d 00 02 20 37 f2 a0 00 a2 00 20 84 f1
  //   b9 00 02 f0 91 20 8f f1 90 1c a5 24 85 20 a5 25 85 21 20 84 f1 b9 00 02 f0 20 c9 3a f0 4a c9 52 f0
  //   0c c9 2e f0 1f a9 3f 20 2e f2 4c 1a f0 c8 20 84 f1 b9 00 02 d0 ef 6c 20 00 a5 20 85 22 a5 21 85 23
  //   4c 25 f1 c8 20 8f f1 90 db a5 24 85 22 a5 25 85 23 20 84 f1 b9 00 02 d0 cb a5 22 c5 20 a5 23 e5 21
  //   90 c1 4c 25 f1 c8 20 84 f1 b9 00 02 f0 2d 20 dd f1 90 b0 a5 21 c9 03 90 1a c9 10 b0 a6 a5 24 81 20
  //   e6 20 d0 02 e6 21 b9 00 02 f0 0f c9 20 f0 d5 4c aa f0 20 5c f1 b0 e5 4c aa f0 4c 1a f0 a5 21 20 3c
  //   f2 a5 20 20 3c f2 a9 3a 20 2e f2 a9 20 20 2e f2 a0 00 b1 20 20 3c f2 20 37 f2 a5 20 c5 22 d0 06 a5
  //   21 c5 23 f0 d3 20 55 f1 4c 25 f1 e6 20 d0 02 e6 21 60 a5 21 c9 10 b0 20 c9 01 f0 1c c9 02 d0 08 a5
  //   20 c9 50 90 12 b0 0e c9 00 d0 0a a5 20 c9 20 90 04 c9 28 90 02 38 60 18 60 b9 00 02 c9 20 d0 03 c8
  //   d0 f6 60 20 84 f1 a9 00 85 24 85 25 85 26 b9 00 02 c9 30 90 34 c9 3a 90 0e c9 41 90 2c c9 47 b0 28
  //   38 e9 37 4c b6 f1 38 e9 30 85 27 e6 26 a5 26 c9 05 b0 1b a5 24 0a 26 25 0a 26 25 0a 26 25 0a 26 25
  //   05 27 85 24 c8 d0 c5 a5 26 f0 02 38 60 18 60 a2 00 a9 00 85 24 b9 00 02 c9 30 90 2d c9 3a 90 0e c9
  //   41 90 25 c9 47 b0 21 38 e9 37 4c ff f1 38 e9 30 85 27 e8 e0 05 b0 19 a5 24 c9 10 b0 13 0a 0a 0a 0a
  //   05 27 85 24 c8 d0 cc e0 00 f0 04 a2 00 38 60 a2 00 18 60 ad 11 d0 10 fb ad 10 d0 29 7f 60 2c 12 d0
  //   30 fb 8d 12 d0 60 a9 0d 4c 2e f2 08 d8 48 4a 4a 4a 4a 20 4e f2 68 29 0f 20 4e f2 28 60 c9 0a 90 06
  //   18 69 37 4c 2e f2 18 69 30 4c 2e f2 42 49 54 57 52 49 47 48 54 20 36 35 30 32 0d 41 44 44 52 20 20
  //   41 44 44 52 2e 45 4e 44 20 20 41 44 44 52 3a 20 42 59 54 45 53 20 20 41 44 44 52 52 00 ff ff ff ff
  //   ff ff ff ff ff ff ff ff ff ff ff ff ff ff ff ff ff ff ff ff ff ff ff ff ff ff ff ff ff ff ff ff ff
  //   ff ff ff ff ff ff ff ff ff ff ff ff ff ff ff ff ff ff ff ff ff ff ff ff ff ff ff ff ff ff ff ff ff
  //   ff ff ff ff ff ff ff ff ff ff ff ff ff ff ff ff ff ff ff ff ff ff ff ff ff ff ff ff ff ff ff ff ff
  //   ff ff ff ff ff ff ff ff ff ff ff ff ff ff ff ff ff ff ff ff ff ff ff ff ff ff ff ff ff ff ff ff ff
  //   ff ff ff ff ff ff ff ff ff ff ff ff ff ff ff ff ff ff ff ff ff ff ff ff ff ff ff ff ff ff ff ff ff
  //   ff ff ff ff ff ff ff ff ff ff ff ff ff ff ff ff ff ff ff ff ff ff ff ff ff ff ff ff ff ff ff ff ff
  //   ff ff ff ff ff ff ff ff ff ff ff ff ff ff ff ff ff ff ff ff ff ff ff ff ff ff ff ff ff ff ff ff ff
  //   ff ff ff ff ff ff ff ff ff ff ff ff ff ff ff ff ff ff ff ff ff ff ff ff ff ff ff ff ff ff ff ff ff
  //   ff ff ff ff ff ff ff ff ff ff ff ff ff ff ff ff ff ff ff ff ff ff ff ff ff ff ff ff ff ff ff ff ff
  //   ff ff ff ff ff ff ff ff ff ff ff ff ff ff ff ff ff ff ff ff ff ff ff ff ff ff ff ff ff ff ff ff ff
  //   ff ff ff ff ff ff ff ff ff ff ff ff ff ff ff ff ff ff ff ff ff ff ff ff ff ff ff ff ff ff ff ff ff
  //   ff ff ff ff ff ff ff ff ff ff ff ff ff ff ff ff ff ff ff ff ff ff ff ff ff ff ff ff ff ff ff ff ff
  //   ff ff ff ff ff ff ff ff ff ff ff ff ff ff ff ff ff ff ff ff ff ff ff ff ff ff ff ff ff ff ff ff ff
  //   ff ff ff ff ff ff ff ff ff ff ff ff ff ff ff ff ff ff ff ff ff ff ff ff ff ff ff ff ff ff ff ff ff
  //   ff ff ff ff ff ff ff ff ff ff ff ff ff ff ff ff ff ff ff ff ff ff ff ff ff ff ff ff ff ff ff ff ff
  //   ff ff ff ff ff ff ff ff ff ff ff ff ff ff ff ff ff ff ff ff ff ff ff ff ff ff ff ff ff ff ff ff ff
  //   ff ff ff ff ff ff ff ff ff ff ff ff ff ff ff ff ff ff ff ff ff ff ff ff ff ff ff ff ff ff ff ff ff
  //   ff ff ff ff ff ff ff ff ff ff ff ff ff ff ff ff ff ff ff ff ff ff ff ff ff ff ff ff ff ff ff ff ff
  //   ff ff ff ff ff ff ff ff ff ff ff ff ff ff ff ff ff ff ff ff ff ff ff ff ff ff ff ff ff ff ff ff ff
  //   ff ff ff ff ff ff ff ff ff ff ff ff ff ff ff ff ff ff ff ff ff ff ff ff ff ff ff ff ff ff ff ff ff
  //   ff ff ff ff ff ff ff ff ff ff ff ff ff f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
endmodule

module MemoryMap (
  input  [15:0] Address,
  input  Write,
  input  Reset,
  input  [7:0] RamData,
  input  [7:0] RomData,
  input  [7:0] IoData,
  output [11:0] BankAddress,
  output RamWrite,
  output [7:0] ReadData,
  output IoSelect
);

  wire IoSelect_0, IoSelect_1, IoSelect_2, IoSelect_3, IoSelect_4, IoSelect_5, IoSelect_6, IoSelect_7,
       IoSelect_8, IoSelect_9, IoSelect_10, IoSelect_11, MemorySelected, n2, n3, n4, n5, n6, n7, n8, n9, n10,
       n11, n12, n13, n14, n15, NotReset, RamSelect_0, RamSelect_1, RomSelect_0, RomSelect_1, SafeWrite,
       Selected;
  wire [7:0] Bank0, Bank1, Bank2, Bank3, MemoryData, OtherData;
  wire [7:7] Mask0, Mask1, Mask3;

  not not_1 (n4, Address[4]);
  not not_2 (n8, Address[8]);
  not not_3 (n12, Address[12]);
  assign Bank0 = {8{Mask0[7]}} & RamData;  // AND_Gate and_1, 8 bits wide
  and and_2 (IoSelect_0, n2, n3);
  and and_3 (IoSelect_4, IoSelect_3, n7);
  and and_4 (IoSelect_8, IoSelect_7, n11);
  and and_5 (IoSelect, IoSelect_11, Address[15]);
  not not_4 (n5, Address[5]);
  not not_5 (n9, Address[9]);
  not not_6 (n13, Address[13]);
  assign MemoryData = Bank0 | Bank1;  // OR_Gate or_1, 8 bits wide
  not not_7 (n2, Address[2]);
  not not_8 (n6, Address[6]);
  not not_9 (n10, Address[10]);
  not not_10 (n14, Address[14]);
  and and_6 (IoSelect_1, IoSelect_0, Address[4]);
  and and_7 (IoSelect_5, IoSelect_4, n8);
  and and_8 (IoSelect_9, IoSelect_8, Address[12]);
  assign Bank1 = {8{Mask1[7]}} & RomData;  // AND_Gate and_9, 8 bits wide
  not not_11 (n3, Address[3]);
  not not_12 (n7, Address[7]);
  not not_13 (n11, Address[11]);
  not not_14 (n15, Address[15]);
  and and_10 (IoSelect_2, IoSelect_1, n5);
  and and_11 (IoSelect_6, IoSelect_5, n9);
  and and_12 (IoSelect_10, IoSelect_9, n13);
  and and_13 (RamSelect_0, n12, n13);
  and and_14 (RomSelect_0, Address[12], Address[13]);
  assign OtherData = Bank2 | Bank3;  // OR_Gate or_2, 8 bits wide
  not not_15 (NotReset, Reset);
  and and_15 (IoSelect_3, IoSelect_2, n6);
  and and_16 (IoSelect_7, IoSelect_6, n10);
  and and_17 (IoSelect_11, IoSelect_10, Address[14]);
  assign Bank2 = {8{IoSelect}} & IoData;  // AND_Gate and_18, 8 bits wide
  and and_19 (RamSelect_1, RamSelect_0, n14);
  and and_20 (RomSelect_1, RomSelect_0, Address[14]);
  and and_21 (SafeWrite, Write, NotReset);
  or or_3 (MemorySelected, Mask0[7], Mask1[7]);
  and and_22 (Mask0[7], RamSelect_1, n15);
  and and_23 (Mask1[7], RomSelect_1, Address[15]);
  and and_24 (RamWrite, SafeWrite, Mask0[7]);
  or or_4 (Selected, MemorySelected, IoSelect);
  assign ReadData = MemoryData | OtherData;  // OR_Gate or_5, 8 bits wide
  assign Bank3 = {8{Mask3[7]}} & {8{1'b1}};  // AND_Gate and_25, 8 bits wide
  not not_16 (Mask3[7], Selected);

  assign BankAddress = Address[11:0];

  // Other names for the same wires on the sheet: a12 = Address[12]; a13 = Address[13]; a14 = Address[14];
  //   a15 = Address[15]; a0 = Address[0]; a1 = Address[1]; a2 = Address[2]; a3 = Address[3]; a4 = Address[4];
  //   a5 = Address[5]; a6 = Address[6]; a7 = Address[7]; a8 = Address[8]; a9 = Address[9]; a10 = Address[10];
  //   a11 = Address[11]; Mask0[6:0] = {7{Mask0[7]}}; RamSelect = Mask0[7]; Mask1[6:0] = {7{Mask1[7]}};
  //   RomSelect = Mask1[7]; Mask2[7:0] = {8{IoSelect}}; Mask3[6:0] = {7{Mask3[7]}}; Reserved = Mask3[7]

  // Notes on the sheet:
  //   Memory map / only gates and wiring; reserved addresses return FF
endmodule
