// Logisim project cpu6502.circ as structural Verilog: 11 circuits, main circuit Cpu6502
module GateLatch (
  input  Data,
  input  Enable,
  input  Reset,
  output Q
);

  wire n1, n2, n3, n4, n5, n6, n7, n9, n10;

  not not_1 (n1, Reset);
  and and_1 (n5, Enable, n4);
  and and_2 (n2, Enable, Data);
  or or_1 (n6, Reset, n5);
  or or_2 (n9, n3, Q);
  and and_3 (n3, n2, n1);
  or or_3 (n7, n6, n10);
  not not_2 (n10, n9);
  not not_3 (n4, Data);
  not not_4 (Q, n7);

  // Other names for the same wires on the sheet: n8 = Q; Qbar = n10

  // Notes on the sheet:
  //   Gate latch: cross-coupled feedback; Reset dominates Data and Enable.
endmodule

module GateDff (
  input  Data,
  input  SysClock,
  input  Reset,
  output Q
);

  wire Master, n1, n2, n3, n4, n5, n6, n7, n8, n9, n11, n13, n14, n15, n16, n17, n18, n19, n21;

  not not_1 (n1, SysClock);
  not not_2 (n6, Data);
  not not_3 (Master, n9);
  and and_1 (n17, SysClock, n16);
  not not_4 (n3, Reset);
  and and_2 (n7, n1, n6);
  and and_3 (n14, SysClock, Master);
  or or_1 (n18, Reset, n17);
  or or_2 (n21, n15, Q);
  and and_4 (n4, n1, Data);
  or or_3 (n8, Reset, n7);
  or or_4 (n11, n5, Master);
  and and_5 (n15, n14, n3);
  or or_5 (n19, n18, n13);
  not not_5 (n13, n21);
  and and_6 (n5, n4, n3);
  or or_6 (n9, n8, n2);
  not not_6 (n2, n11);
  not not_7 (n16, Master);
  not not_8 (Q, n19);

  // Other names for the same wires on the sheet: n12 = n2; n10 = Master; n20 = Q; n22 = n13

  // Notes on the sheet:
  //   Gate DFF: transparent-low master and transparent-high slave; rising-edge capture.
endmodule

module FullAdder (
  input  A,
  input  B,
  input  CarryIn,
  output Sum,
  output CarryOut
);

  wire n1, n3, n4;

  xor xor_1 (n1, A, B);
  and and_1 (n4, n1, CarryIn);
  xor xor_2 (Sum, n1, CarryIn);
  or or_1 (CarryOut, n3, n4);
  and and_2 (n3, A, B);

  // Other names for the same wires on the sheet: n2 = Sum; n5 = CarryOut
endmodule

module Register1R0 (
  input  Data,
  input  Enable,
  input  SysClock,
  input  Reset,
  output Q
);

  wire ClockEnable, n1, n2;

  not not_1 (n1, SysClock);
  GateLatch gatelatch_1 (.Data(Enable), .Enable(n1), .Reset(Reset), .Q(ClockEnable));
  and and_1 (n2, SysClock, ClockEnable);
  GateDff gatedff_1 (.Data(Data), .SysClock(n2), .Reset(Reset), .Q(Q));

  // Other names for the same wires on the sheet: raw0 = Q
endmodule

module Register8R0 (
  input  [7:0] Data,
  input  Enable,
  input  SysClock,
  input  Reset,
  output [7:0] Q
);

  wire ClockEnable, n1, n2;

  GateDff gatedff_1 (.Data(Data[0]), .SysClock(n2), .Reset(Reset), .Q(Q[0]));
  GateDff gatedff_2 (.Data(Data[4]), .SysClock(n2), .Reset(Reset), .Q(Q[4]));
  not not_1 (n1, SysClock);
  GateDff gatedff_3 (.Data(Data[1]), .SysClock(n2), .Reset(Reset), .Q(Q[1]));
  GateDff gatedff_4 (.Data(Data[5]), .SysClock(n2), .Reset(Reset), .Q(Q[5]));
  GateLatch gatelatch_1 (.Data(Enable), .Enable(n1), .Reset(Reset), .Q(ClockEnable));
  GateDff gatedff_5 (.Data(Data[2]), .SysClock(n2), .Reset(Reset), .Q(Q[2]));
  GateDff gatedff_6 (.Data(Data[6]), .SysClock(n2), .Reset(Reset), .Q(Q[6]));
  and and_1 (n2, SysClock, ClockEnable);
  GateDff gatedff_7 (.Data(Data[3]), .SysClock(n2), .Reset(Reset), .Q(Q[3]));
  GateDff gatedff_8 (.Data(Data[7]), .SysClock(n2), .Reset(Reset), .Q(Q[7]));

  // Other names for the same wires on the sheet: Data_0 = Data[0]; Data_1 = Data[1]; Data_2 = Data[2];
  //   Data_3 = Data[3]; Data_4 = Data[4]; Data_5 = Data[5]; Data_6 = Data[6]; Data_7 = Data[7]; raw0 = Q[0];
  //   raw1 = Q[1]; raw2 = Q[2]; raw3 = Q[3]; raw4 = Q[4]; raw5 = Q[5]; raw6 = Q[6]; raw7 = Q[7]
endmodule

module Register8R253 (
  input  [7:0] Data,
  input  Enable,
  input  SysClock,
  input  Reset,
  output [7:0] Q
);

  wire ClockEnable, n1, n2, n4, n6, n8, n10, n12, n14, n16, raw0, raw2, raw3, raw4, raw5, raw6, raw7;

  not not_1 (Q[0], raw0);
  not not_2 (Q[2], raw2);
  not not_3 (n8, Data[3]);
  GateDff gatedff_1 (.Data(n10), .SysClock(n2), .Reset(Reset), .Q(raw4));
  not not_4 (Q[6], raw6);
  not not_5 (n16, Data[7]);
  not not_6 (n1, SysClock);
  not not_7 (n4, Data[0]);
  not not_8 (n6, Data[2]);
  GateDff gatedff_2 (.Data(n8), .SysClock(n2), .Reset(Reset), .Q(raw3));
  not not_9 (Q[5], raw5);
  not not_10 (n14, Data[6]);
  GateDff gatedff_3 (.Data(n16), .SysClock(n2), .Reset(Reset), .Q(raw7));
  GateLatch gatelatch_1 (.Data(Enable), .Enable(n1), .Reset(Reset), .Q(ClockEnable));
  GateDff gatedff_4 (.Data(n4), .SysClock(n2), .Reset(Reset), .Q(raw0));
  GateDff gatedff_5 (.Data(n6), .SysClock(n2), .Reset(Reset), .Q(raw2));
  not not_11 (Q[4], raw4);
  not not_12 (n12, Data[5]);
  GateDff gatedff_6 (.Data(n14), .SysClock(n2), .Reset(Reset), .Q(raw6));
  and and_1 (n2, SysClock, ClockEnable);
  GateDff gatedff_7 (.Data(Data[1]), .SysClock(n2), .Reset(Reset), .Q(Q[1]));
  not not_13 (Q[3], raw3);
  not not_14 (n10, Data[4]);
  GateDff gatedff_8 (.Data(n12), .SysClock(n2), .Reset(Reset), .Q(raw5));
  not not_15 (Q[7], raw7);

  // Other names for the same wires on the sheet: Data_0 = Data[0]; Data_1 = Data[1]; Data_2 = Data[2];
  //   Data_3 = Data[3]; Data_4 = Data[4]; Data_5 = Data[5]; Data_6 = Data[6]; Data_7 = Data[7]; n3 = Q[0];
  //   raw1 = Q[1]; n5 = Q[2]; n7 = Q[3]; n9 = Q[4]; n11 = Q[5]; n13 = Q[6]; n15 = Q[7]
endmodule

module Register8R36 (
  input  [7:0] Data,
  input  Enable,
  input  SysClock,
  input  Reset,
  output [7:0] Q
);

  wire ClockEnable, n1, n2, n4, n6, raw2, raw5;

  GateDff gatedff_1 (.Data(Data[0]), .SysClock(n2), .Reset(Reset), .Q(Q[0]));
  GateDff gatedff_2 (.Data(n4), .SysClock(n2), .Reset(Reset), .Q(raw2));
  not not_1 (n6, Data[5]);
  not not_2 (n1, SysClock);
  GateDff gatedff_3 (.Data(Data[1]), .SysClock(n2), .Reset(Reset), .Q(Q[1]));
  GateDff gatedff_4 (.Data(Data[3]), .SysClock(n2), .Reset(Reset), .Q(Q[3]));
  GateDff gatedff_5 (.Data(n6), .SysClock(n2), .Reset(Reset), .Q(raw5));
  GateLatch gatelatch_1 (.Data(Enable), .Enable(n1), .Reset(Reset), .Q(ClockEnable));
  not not_3 (Q[2], raw2);
  GateDff gatedff_6 (.Data(Data[4]), .SysClock(n2), .Reset(Reset), .Q(Q[4]));
  GateDff gatedff_7 (.Data(Data[6]), .SysClock(n2), .Reset(Reset), .Q(Q[6]));
  and and_1 (n2, SysClock, ClockEnable);
  not not_4 (n4, Data[2]);
  not not_5 (Q[5], raw5);
  GateDff gatedff_8 (.Data(Data[7]), .SysClock(n2), .Reset(Reset), .Q(Q[7]));

  // Other names for the same wires on the sheet: Data_0 = Data[0]; Data_1 = Data[1]; Data_2 = Data[2];
  //   Data_3 = Data[3]; Data_4 = Data[4]; Data_5 = Data[5]; Data_6 = Data[6]; Data_7 = Data[7]; raw0 = Q[0];
  //   raw1 = Q[1]; n3 = Q[2]; raw3 = Q[3]; raw4 = Q[4]; n5 = Q[5]; raw6 = Q[6]; raw7 = Q[7]
endmodule

module Register16R0 (
  input  [15:0] Data,
  input  Enable,
  input  SysClock,
  input  Reset,
  output [15:0] Q
);

  wire ClockEnable, n1, n2;

  GateDff gatedff_1 (.Data(Data[0]), .SysClock(n2), .Reset(Reset), .Q(Q[0]));
  GateDff gatedff_2 (.Data(Data[4]), .SysClock(n2), .Reset(Reset), .Q(Q[4]));
  GateDff gatedff_3 (.Data(Data[8]), .SysClock(n2), .Reset(Reset), .Q(Q[8]));
  GateDff gatedff_4 (.Data(Data[12]), .SysClock(n2), .Reset(Reset), .Q(Q[12]));
  not not_1 (n1, SysClock);
  GateDff gatedff_5 (.Data(Data[1]), .SysClock(n2), .Reset(Reset), .Q(Q[1]));
  GateDff gatedff_6 (.Data(Data[5]), .SysClock(n2), .Reset(Reset), .Q(Q[5]));
  GateDff gatedff_7 (.Data(Data[9]), .SysClock(n2), .Reset(Reset), .Q(Q[9]));
  GateDff gatedff_8 (.Data(Data[13]), .SysClock(n2), .Reset(Reset), .Q(Q[13]));
  GateLatch gatelatch_1 (.Data(Enable), .Enable(n1), .Reset(Reset), .Q(ClockEnable));
  GateDff gatedff_9 (.Data(Data[2]), .SysClock(n2), .Reset(Reset), .Q(Q[2]));
  GateDff gatedff_10 (.Data(Data[6]), .SysClock(n2), .Reset(Reset), .Q(Q[6]));
  GateDff gatedff_11 (.Data(Data[10]), .SysClock(n2), .Reset(Reset), .Q(Q[10]));
  GateDff gatedff_12 (.Data(Data[14]), .SysClock(n2), .Reset(Reset), .Q(Q[14]));
  and and_1 (n2, SysClock, ClockEnable);
  GateDff gatedff_13 (.Data(Data[3]), .SysClock(n2), .Reset(Reset), .Q(Q[3]));
  GateDff gatedff_14 (.Data(Data[7]), .SysClock(n2), .Reset(Reset), .Q(Q[7]));
  GateDff gatedff_15 (.Data(Data[11]), .SysClock(n2), .Reset(Reset), .Q(Q[11]));
  GateDff gatedff_16 (.Data(Data[15]), .SysClock(n2), .Reset(Reset), .Q(Q[15]));

  // Other names for the same wires on the sheet: Data_0 = Data[0]; Data_1 = Data[1]; Data_2 = Data[2];
  //   Data_3 = Data[3]; Data_4 = Data[4]; Data_5 = Data[5]; Data_6 = Data[6]; Data_7 = Data[7]; Data_8 = Data[8];
  //   Data_9 = Data[9]; Data_10 = Data[10]; Data_11 = Data[11]; Data_12 = Data[12]; Data_13 = Data[13];
  //   Data_14 = Data[14]; Data_15 = Data[15]; raw0 = Q[0]; raw1 = Q[1]; raw2 = Q[2]; raw3 = Q[3]; raw4 = Q[4];
  //   raw5 = Q[5]; raw6 = Q[6]; raw7 = Q[7]; raw8 = Q[8]; raw9 = Q[9]; raw10 = Q[10]; raw11 = Q[11]; raw12 = Q[12];
  //   raw13 = Q[13]; raw14 = Q[14]; raw15 = Q[15]
endmodule

module InstructionDecode (
  input  [7:0] IR,
  output [55:0] Mnemonics,
  output [12:0] AddressModes
);

  wire n1, n2, n3, n4, n5, n6, n7, n8, n9, n10, n11, n12, n13, n14, n15, n16, n17, n18, n19, n20, n21, n22,
       n23, n24, n25, n26, n27, n28, n29, n30, n31, n32, n33, n34, n35, n36, n37, n38, n39, n40, n41, n42,
       n43, n44, n45, n46, n47, n48, n49, n50, n51, n52, n53, n54, n55, n56, n57, n58, n59, n60, n61, n62,
       n63, n64, n65, n66, n67, n68, n69, n70, n71, n72, n73, n74, n75, n76, n77, n78, n79, n80, n81, n82,
       n83, n84, n85, n86, n87, n88, n89, n90, n91, n92, n93, n94, n95, n96, n97, n98, n99, n100, n101, n102,
       n103, n104, n105, n106, n107, n108, n109, n110, n111, n112, n113, n114, n115, n116, n117, n118, n119,
       n120, n121, n122, n123, n124, n125, n126, n127, n128, n129, n130, n131, n132, n133, n134, n135, n136,
       n137, n138, n139, n140, n141, n142, n143, n144, n145, n146, n147, n148, n149, n150, n151, n152, n153,
       n154, n155, n156, n157, n158, n159, n160, n161, n162, n163, n164, n165, n166, n167, n168, n169, n170,
       n171, n172, n173, n174, n175, n176, n177, n178, n179, n180, n181, n182, n183, n184, n185, n186, n187,
       n188, n189, n190, n191, n192, n193, n194, n195, n196, n197, n198, n199, n200, n201, n202, n203, n204,
       n205, n206, n207, n208, n209, n210, n211, n212, n213, n214, n215, n216, n217, n218, n219, n220, n221,
       n222, n223, n224, n225, n226, n227, n228, n229, n230, n231, n232, n233, n234, n235, n236, n237, n238,
       n239, n240, n241, n242, n243, n244, n245, n246, n247, n248, n249, n250, n251, n252, n253, n254, n255,
       n256, n257, n258, n259, n260, n261, n262, n263, n264, n265, n266, n269, n270, n271, n273, n274, n276,
       n278, n284, n286, n287, n288, n289, n291, n292, n293, n295, n296, n298, n299, n302, n304, n307, n309,
       n314, n315, n316, n321, n322, n330, n331, n332, n333, n334, n335, n337, n338, n339, n340, n341, n342,
       n344, n345, n346, n349, n350, n351, n352, n353, n354, n356, n358, n360, n361, n363, n364, n365, n366,
       n367, n368, n370, n371, n374, n375, n376, n377, n378, n379, n381, n382, n383, n385, n386, n387, n389,
       n390, n391, n393, n394, n395, n396, n397, n398, n400, n401, n402, n404, n405, n406, n408, n409, n410,
       n411, n412, n413, n415, n416, n417, n418, n419, n421, n423, n425, n426, n427, n428, n429, n430, n431,
       n432, n433, n434, n435, n436, n437, n438, n439, n440, n441, n442, n443, n444, n445, n447, n448, n449,
       n450, n451, n452, n453, n454, n455, n456, n457, n458, n459, n461, n462, n463, n464, n465, n466, n467,
       n469, n470, n472, n473, n474, n475, n476, n477, n478, n479, n480, n482, n483, n484, n485, n486, n487,
       n488, n489, n490, n491, n492, n493, n494, n495, n496, n497, n498, n499, n500, n501, n502, n503, n504,
       n506, n507, n508, n509, n510, n511, n513, n514, n515, n516, n517, n518, n520, n521, n522, n523, n524,
       n525, n527, n528, n529, n530, n531, n532, n533, n534, n535, n536, n537, n538, n539, n540, n541, n542,
       n543, n544, n545, n547, n548, n549, n550, n551, n552, n553, n554, n555, n556, n557, n558, n559, n560;

  not not_1 (n4, IR[5]);
  and and_1 (n8, n7, n2);
  and and_2 (n12, n11, n5);
  and and_3 (n16, n15, n14);
  and and_4 (n20, n19, n6);
  and and_5 (n24, n23, n6);
  and and_6 (n28, n27, n5);
  and and_7 (n32, n31, n5);
  and and_8 (n36, n35, n5);
  and and_9 (n40, n39, n4);
  and and_10 (n44, n43, n4);
  and and_11 (n48, n47, n5);
  and and_12 (n52, n51, n6);
  and and_13 (n56, n26, IR[5]);
  and and_14 (n60, n59, n5);
  and and_15 (n64, n63, n6);
  and and_16 (n68, n43, IR[5]);
  and and_17 (n72, n71, n6);
  and and_18 (n76, n75, n6);
  and and_19 (n80, n79, n6);
  and and_20 (n84, n83, n6);
  and and_21 (n88, n87, n6);
  and and_22 (n92, n91, n6);
  and and_23 (n96, n95, n6);
  and and_24 (n100, n99, n6);
  and and_25 (n104, n23, IR[7]);
  and and_26 (n108, n41, IR[7]);
  and and_27 (n112, n54, IR[7]);
  and and_28 (n116, n66, IR[7]);
  and and_29 (n120, n75, IR[7]);
  and and_30 (n124, n83, IR[7]);
  and and_31 (n128, n91, IR[7]);
  and and_32 (n132, n99, IR[7]);
  and and_33 (n136, n135, n2);
  and and_34 (n140, n139, n5);
  and and_35 (n144, n143, n3);
  and and_36 (n148, n143, IR[4]);
  and and_37 (n152, n142, IR[3]);
  and and_38 (n156, n155, n6);
  and and_39 (n160, n159, n6);
  and and_40 (n164, n144, IR[5]);
  and and_41 (n168, n167, n5);
  and and_42 (n172, n171, n6);
  and and_43 (n176, n139, IR[6]);
  and and_44 (n180, n149, IR[6]);
  and and_45 (n184, n158, IR[6]);
  and and_46 (n188, n164, IR[6]);
  and and_47 (n192, n170, IR[6]);
  and and_48 (n196, n146, IR[7]);
  and and_49 (n200, n199, IR[2]);
  and and_50 (n204, n203, n5);
  and and_51 (n208, n207, n5);
  and and_52 (n212, n211, n4);
  and and_53 (n216, n215, n3);
  and and_54 (n220, n165, IR[7]);
  and and_55 (n224, n199, n2);
  and and_56 (n228, n227, n5);
  and and_57 (n232, n231, IR[7]);
  and and_58 (n236, n211, IR[5]);
  and and_59 (n240, n239, IR[5]);
  and and_60 (n244, n243, IR[7]);
  and and_61 (n248, n247, IR[7]);
  and and_62 (n252, n203, IR[6]);
  and and_63 (n256, n188, IR[7]);
  and and_64 (n260, n178, IR[7]);
  and and_65 (n264, n231, n6);
  and and_66 (Mnemonics[28], n228, n6);
  and and_67 (Mnemonics[9], n271, n6);
  and and_68 (n276, n270, IR[6]);
  and and_69 (Mnemonics[3], n271, IR[7]);
  and and_70 (n284, n249, n5);
  and and_71 (n288, n287, n4);
  and and_72 (n292, n291, n4);
  and and_73 (n296, n295, n5);
  and and_74 (Mnemonics[44], n299, n6);
  and and_75 (n304, n292, IR[6]);
  and and_76 (Mnemonics[37], n307, n6);
  and and_77 (Mnemonics[53], n140, IR[7]);
  and and_78 (n316, n315, n5);
  and and_79 (Mnemonics[16], n299, IR[7]);
  and and_80 (Mnemonics[26], n302, IR[7]);
  and and_81 (Mnemonics[33], n186, IR[7]);
  or or_1 (n332, n331, n94);
  or or_2 (Mnemonics[0], n335, n102);
  or or_3 (n340, n339, n61);
  or or_4 (n344, n141, n147);
  or or_5 (Mnemonics[6], n264, n265);
  or or_6 (n352, n351, n122);
  or or_7 (n356, n244, n246);
  or or_8 (n360, n260, n261);
  or or_9 (n364, n363, n76);
  or or_10 (n368, n367, n84);
  or or_11 (Mnemonics[24], n371, n259);
  or or_12 (n376, n375, n113);
  or or_13 (Mnemonics[29], n379, n117);
  or or_14 (Mnemonics[30], n383, n223);
  or or_15 (Mnemonics[31], n387, n242);
  or or_16 (Mnemonics[32], n391, n185);
  or or_17 (n396, n395, n33);
  or or_18 (n400, n163, n166);
  or or_19 (n404, n187, n189);
  or or_20 (n408, n126, n127);
  or or_21 (n412, n411, n131);
  or or_22 (n416, n415, n105);
  or or_23 (Mnemonics[47], n419, n109);
  or or_24 (Mnemonics[49], n423, n214);
  or or_25 (n427, n426, n94);
  or or_26 (n431, n430, n129);
  or or_27 (n435, n434, n193);
  or or_28 (n439, n438, n238);
  or or_29 (n443, n442, n262);
  or or_30 (n447, n33, n61);
  or or_31 (n451, n450, n114);
  or or_32 (n455, n454, n175);
  or or_33 (n459, n458, n259);
  or or_34 (n463, n462, n98);
  or or_35 (n467, n466, n131);
  or or_36 (AddressModes[3], n470, n187);
  or or_37 (n475, n474, n110);
  or or_38 (n479, n478, n229);
  or or_39 (n483, n482, Mnemonics[13]);
  or or_40 (n487, n486, Mnemonics[35]);
  or or_41 (n491, n490, Mnemonics[46]);
  or or_42 (n495, n494, Mnemonics[54]);
  or or_43 (n499, n498, Mnemonics[52]);
  or or_44 (n503, n502, Mnemonics[25]);
  or or_45 (n507, n506, n84);
  or or_46 (n511, n510, n124);
  or or_47 (n515, n514, n102);
  or or_48 (AddressModes[8], n518, n133);
  or or_49 (n523, n522, Mnemonics[3]);
  or or_50 (n527, n20, n52);
  or or_51 (n531, n530, n111);
  or or_52 (n535, n534, n166);
  or or_53 (n539, n538, n205);
  or or_54 (n543, n542, n253);
  or or_55 (n547, n24, n55);
  or or_56 (n551, n550, n112);
  or or_57 (n555, n554, n169);
  or or_58 (n559, n558, n235);
  not not_2 (n1, IR[1]);
  not not_3 (n5, IR[6]);
  and and_82 (n9, n8, IR[3]);
  and and_83 (n13, n12, n6);
  and and_84 (n17, n16, n3);
  and and_85 (n21, n16, IR[4]);
  and and_86 (n25, n15, IR[3]);
  and and_87 (n29, n28, n6);
  and and_88 (n33, n32, n6);
  and and_89 (n37, n36, n6);
  and and_90 (n41, n40, n5);
  and and_91 (n45, n44, n5);
  and and_92 (n49, n48, n6);
  and and_93 (n53, n21, IR[5]);
  and and_94 (n57, n56, n5);
  and and_95 (n61, n60, n6);
  and and_96 (n65, n39, IR[5]);
  and and_97 (n69, n68, n5);
  and and_98 (n73, n18, IR[6]);
  and and_99 (n77, n27, IR[6]);
  and and_100 (n81, n35, IR[6]);
  and and_101 (n85, n44, IR[6]);
  and and_102 (n89, n50, IR[6]);
  and and_103 (n93, n56, IR[6]);
  and and_104 (n97, n62, IR[6]);
  and and_105 (n101, n68, IR[6]);
  and and_106 (n105, n28, IR[7]);
  and and_107 (n109, n45, IR[7]);
  and and_108 (n113, n57, IR[7]);
  and and_109 (n117, n69, IR[7]);
  and and_110 (n121, n77, IR[7]);
  and and_111 (n125, n85, IR[7]);
  and and_112 (n129, n93, IR[7]);
  and and_113 (n133, n101, IR[7]);
  and and_114 (n137, n136, IR[3]);
  and and_115 (n141, n140, n6);
  and and_116 (n145, n144, n4);
  and and_117 (n149, n148, n4);
  and and_118 (n153, n152, n3);
  and and_119 (n157, n152, IR[4]);
  and and_120 (n161, n138, IR[5]);
  and and_121 (n165, n164, n5);
  and and_122 (n169, n168, n6);
  and and_123 (n173, n157, IR[5]);
  and and_124 (n177, n176, n6);
  and and_125 (n181, n180, n6);
  and and_126 (n185, n184, n6);
  and and_127 (n189, n188, n6);
  and and_128 (n193, n192, n6);
  and and_129 (n197, n150, IR[7]);
  and and_130 (n201, n200, n14);
  and and_131 (n205, n204, IR[7]);
  and and_132 (n209, n208, IR[7]);
  and and_133 (n213, n212, n5);
  and and_134 (n217, n216, IR[5]);
  and and_135 (n221, n168, IR[7]);
  and and_136 (n225, n224, n14);
  and and_137 (n229, n228, IR[7]);
  and and_138 (n233, n206, IR[5]);
  and and_139 (n237, n236, n5);
  and and_140 (n241, n240, n5);
  and and_141 (n245, n230, IR[6]);
  and and_142 (n249, n226, n4);
  and and_143 (n253, n252, IR[7]);
  and and_144 (n257, n190, IR[7]);
  and and_145 (n261, n180, IR[7]);
  and and_146 (n265, n237, n6);
  and and_147 (n269, n225, IR[4]);
  and and_148 (n273, n269, IR[5]);
  and and_149 (Mnemonics[11], n276, n6);
  and and_150 (Mnemonics[4], n274, IR[7]);
  and and_151 (Mnemonics[10], n284, n6);
  and and_152 (n289, n288, n5);
  and and_153 (n293, n292, n5);
  and and_154 (Mnemonics[38], n296, n6);
  and and_155 (Mnemonics[41], n250, n6);
  and and_156 (Mnemonics[15], n304, n6);
  and and_157 (n309, n298, IR[6]);
  and and_158 (Mnemonics[55], n293, IR[7]);
  and and_159 (Mnemonics[54], n316, IR[7]);
  and and_160 (n321, n314, IR[5]);
  and and_161 (Mnemonics[21], n176, IR[7]);
  and and_162 (Mnemonics[45], n309, IR[7]);
  or or_59 (n333, n332, n96);
  or or_60 (n337, n49, n52);
  or or_61 (n341, n340, n64);
  or or_62 (n345, n344, n151);
  or or_63 (n349, n118, n119);
  or or_64 (n353, n352, n123);
  or or_65 (Mnemonics[18], n356, n248);
  or or_66 (n361, n360, n262);
  or or_67 (n365, n364, n78);
  or or_68 (Mnemonics[23], n368, n86);
  or or_69 (Mnemonics[27], n266, AddressModes[6]);
  or or_70 (n377, n376, n114);
  or or_71 (n381, n219, n220);
  or or_72 (n385, n229, n232);
  or or_73 (n389, n177, n179);
  or or_74 (n393, n13, n20);
  or or_75 (n397, n396, n37);
  or or_76 (n401, n400, n169);
  or or_77 (n405, n404, n191);
  or or_78 (n409, n408, n128);
  or or_79 (n413, n412, n132);
  or or_80 (n417, n416, n106);
  or or_81 (n421, n196, n197);
  or or_82 (n428, n427, n105);
  or or_83 (n432, n431, n156);
  or or_84 (n436, n435, n198);
  or or_85 (n440, n439, n248);
  or or_86 (n444, n443, n265);
  or or_87 (n448, n447, n80);
  or or_88 (n452, n451, n122);
  or or_89 (n456, n455, n185);
  or or_90 (AddressModes[1], n459, n263);
  or or_91 (n464, n463, n107);
  or or_92 (AddressModes[2], n467, n223);
  or or_93 (n472, n13, n49);
  or or_94 (n476, n475, n118);
  or or_95 (n480, n479, n244);
  or or_96 (n484, n483, Mnemonics[38]);
  or or_97 (n488, n487, Mnemonics[15]);
  or or_98 (n492, n491, Mnemonics[22]);
  or or_99 (n496, n495, Mnemonics[51]);
  or or_100 (n500, n499, Mnemonics[26]);
  or or_101 (n504, n503, Mnemonics[33]);
  or or_102 (n508, n507, n100);
  or or_103 (AddressModes[7], n511, n132);
  or or_104 (n516, n515, n109);
  or or_105 (n520, Mnemonics[9], Mnemonics[7]);
  or or_106 (n524, n523, Mnemonics[4]);
  or or_107 (n528, n527, n74);
  or or_108 (n532, n531, n119);
  or or_109 (n536, n535, n179);
  or or_110 (n540, n539, n220);
  or or_111 (n544, n543, n256);
  or or_112 (n548, n547, n76);
  or or_113 (n552, n551, n120);
  or or_114 (n556, n555, n181);
  or or_115 (n560, n559, n257);
  not not_4 (n2, IR[2]);
  not not_5 (n6, IR[7]);
  and and_163 (n10, n9, n3);
  not not_6 (n14, IR[3]);
  and and_164 (n18, n17, n4);
  and and_165 (n22, n21, n4);
  and and_166 (n26, n25, n3);
  and and_167 (n30, n25, IR[4]);
  and and_168 (n34, n9, IR[4]);
  and and_169 (n38, n8, n14);
  and and_170 (n42, n41, n6);
  and and_171 (n46, n45, n6);
  and and_172 (n50, n17, IR[5]);
  and and_173 (n54, n53, n5);
  and and_174 (n58, n57, n6);
  and and_175 (n62, n34, IR[5]);
  and and_176 (n66, n65, n5);
  and and_177 (n70, n69, n6);
  and and_178 (n74, n73, n6);
  and and_179 (n78, n77, n6);
  and and_180 (n82, n81, n6);
  and and_181 (n86, n85, n6);
  and and_182 (n90, n89, n6);
  and and_183 (n94, n93, n6);
  and and_184 (n98, n97, n6);
  and and_185 (n102, n101, n6);
  and and_186 (n106, n32, IR[7]);
  and and_187 (n110, n48, IR[7]);
  and and_188 (n114, n60, IR[7]);
  and and_189 (n118, n71, IR[7]);
  and and_190 (n122, n79, IR[7]);
  and and_191 (n126, n87, IR[7]);
  and and_192 (n130, n95, IR[7]);
  not not_7 (n134, IR[0]);
  and and_193 (n138, n137, n3);
  and and_194 (n142, n135, IR[2]);
  and and_195 (n146, n145, n5);
  and and_196 (n150, n149, n5);
  and and_197 (n154, n153, n4);
  and and_198 (n158, n157, n4);
  and and_199 (n162, n161, n5);
  and and_200 (n166, n165, n6);
  and and_201 (n170, n153, IR[5]);
  and and_202 (n174, n173, n5);
  and and_203 (n178, n145, IR[6]);
  and and_204 (n182, n154, IR[6]);
  and and_205 (n186, n161, IR[6]);
  and and_206 (n190, n167, IR[6]);
  and and_207 (n194, n173, IR[6]);
  and and_208 (n198, n155, IR[7]);
  and and_209 (n202, n201, n3);
  and and_210 (n206, n201, IR[4]);
  and and_211 (n210, n200, IR[3]);
  and and_212 (n214, n213, IR[7]);
  and and_213 (n218, n217, n5);
  and and_214 (n222, n171, IR[7]);
  and and_215 (n226, n225, n3);
  and and_216 (n230, n202, IR[5]);
  and and_217 (n234, n233, n5);
  and and_218 (n238, n237, IR[7]);
  and and_219 (n242, n241, IR[7]);
  and and_220 (n246, n245, IR[7]);
  and and_221 (n250, n249, IR[6]);
  and and_222 (n254, n212, IR[6]);
  and and_223 (n258, n192, IR[7]);
  and and_224 (n262, n182, IR[7]);
  and and_225 (n266, n254, n6);
  and and_226 (n270, n269, n4);
  and and_227 (n274, n273, n5);
  and and_228 (n278, n273, IR[6]);
  and and_229 (Mnemonics[8], n276, IR[7]);
  and and_230 (n286, n224, IR[3]);
  and and_231 (Mnemonics[36], n289, n6);
  and and_232 (Mnemonics[13], n293, n6);
  and and_233 (n298, n291, IR[5]);
  and and_234 (n302, n288, IR[6]);
  and and_235 (Mnemonics[42], n243, n6);
  and and_236 (Mnemonics[46], n309, n6);
  and and_237 (n314, n137, IR[4]);
  and and_238 (Mnemonics[51], n296, IR[7]);
  and and_239 (n322, n321, n5);
  and and_240 (Mnemonics[14], n304, IR[7]);
  or or_116 (n330, n88, n90);
  or or_117 (n334, n333, n98);
  or or_118 (n338, n337, n55);
  or or_119 (n342, n341, n67);
  or or_120 (n346, n345, n156);
  or or_121 (n350, n349, n120);
  or or_122 (n354, n353, n124);
  or or_123 (n358, n251, n253);
  or or_124 (Mnemonics[20], n361, n263);
  or or_125 (n366, n365, n80);
  or or_126 (n370, n256, n257);
  or or_127 (n374, n110, n111);
  or or_128 (n378, n377, n115);
  or or_129 (n382, n381, n221);
  or or_130 (n386, n385, n235);
  or or_131 (n390, n389, n181);
  or or_132 (n394, n393, n24);
  or or_133 (n398, n397, n42);
  or or_134 (n402, n401, n172);
  or or_135 (n406, n405, n193);
  or or_136 (n410, n409, n129);
  or or_137 (Mnemonics[43], n413, n133);
  or or_138 (n418, n417, n107);
  or or_139 (Mnemonics[48], n421, n198);
  or or_140 (n425, n29, n58);
  or or_141 (n429, n428, n113);
  or or_142 (n433, n432, n172);
  or or_143 (n437, n436, n214);
  or or_144 (n441, n440, n255);
  or or_145 (n445, n444, n266);
  or or_146 (n449, n448, n96);
  or or_147 (n453, n452, n130);
  or or_148 (n457, n456, n195);
  or or_149 (n461, n37, n64);
  or or_150 (n465, n464, n115);
  or or_151 (n469, n141, n163);
  or or_152 (n473, n472, n72);
  or or_153 (n477, n476, n126);
  or or_154 (AddressModes[4], n480, n251);
  or or_155 (n485, n484, Mnemonics[44]);
  or or_156 (n489, n488, Mnemonics[42]);
  or or_157 (n493, n492, Mnemonics[53]);
  or or_158 (n497, n496, Mnemonics[50]);
  or or_159 (n501, n500, Mnemonics[21]);
  or or_160 (AddressModes[5], n504, Mnemonics[45]);
  or or_161 (n509, n508, n108);
  or or_162 (n513, n46, n70);
  or or_163 (n517, n516, n117);
  or or_164 (n521, n520, Mnemonics[11]);
  or or_165 (n525, n524, Mnemonics[8]);
  or or_166 (n529, n528, n90);
  or or_167 (n533, n532, n127);
  or or_168 (n537, n536, n189);
  or or_169 (n541, n540, n232);
  or or_170 (n545, n544, n260);
  or or_171 (n549, n548, n92);
  or or_172 (n553, n552, n128);
  or or_173 (n557, n556, n191);
  or or_174 (AddressModes[11], n560, n261);
  not not_8 (n3, IR[4]);
  and and_241 (n7, IR[0], n1);
  and and_242 (n11, n10, n4);
  and and_243 (n15, n7, IR[2]);
  and and_244 (n19, n18, n5);
  and and_245 (n23, n22, n5);
  and and_246 (n27, n26, n4);
  and and_247 (n31, n30, n4);
  and and_248 (n35, n34, n4);
  and and_249 (n39, n38, n3);
  and and_250 (n43, n38, IR[4]);
  and and_251 (n47, n10, IR[5]);
  and and_252 (n51, n50, n5);
  and and_253 (n55, n54, n6);
  and and_254 (n59, n30, IR[5]);
  and and_255 (n63, n62, n5);
  and and_256 (n67, n66, n6);
  and and_257 (n71, n11, IR[6]);
  and and_258 (n75, n22, IR[6]);
  and and_259 (n79, n31, IR[6]);
  and and_260 (n83, n40, IR[6]);
  and and_261 (n87, n47, IR[6]);
  and and_262 (n91, n53, IR[6]);
  and and_263 (n95, n59, IR[6]);
  and and_264 (n99, n65, IR[6]);
  and and_265 (n103, n19, IR[7]);
  and and_266 (n107, n36, IR[7]);
  and and_267 (n111, n51, IR[7]);
  and and_268 (n115, n63, IR[7]);
  and and_269 (n119, n73, IR[7]);
  and and_270 (n123, n81, IR[7]);
  and and_271 (n127, n89, IR[7]);
  and and_272 (n131, n97, IR[7]);
  and and_273 (n135, n134, IR[1]);
  and and_274 (n139, n138, n4);
  and and_275 (n143, n142, n14);
  and and_276 (n147, n146, n6);
  and and_277 (n151, n150, n6);
  and and_278 (n155, n154, n5);
  and and_279 (n159, n158, n5);
  and and_280 (n163, n162, n6);
  and and_281 (n167, n148, IR[5]);
  and and_282 (n171, n170, n5);
  and and_283 (n175, n174, n6);
  and and_284 (n179, n178, n6);
  and and_285 (n183, n182, n6);
  and and_286 (n187, n186, n6);
  and and_287 (n191, n190, n6);
  and and_288 (n195, n194, n6);
  and and_289 (n199, n134, n1);
  and and_290 (n203, n202, n4);
  and and_291 (n207, n206, n4);
  and and_292 (n211, n210, n3);
  and and_293 (n215, n136, n14);
  and and_294 (n219, n218, IR[7]);
  and and_295 (n223, n174, IR[7]);
  and and_296 (n227, n226, IR[5]);
  and and_297 (n231, n230, n5);
  and and_298 (n235, n234, IR[7]);
  and and_299 (n239, n210, IR[4]);
  and and_300 (n243, n227, IR[6]);
  and and_301 (n247, n236, IR[6]);
  and and_302 (n251, n250, IR[7]);
  and and_303 (n255, n254, IR[7]);
  and and_304 (n259, n194, IR[7]);
  and and_305 (n263, n184, IR[7]);
  and and_306 (AddressModes[6], n247, n6);
  and and_307 (n271, n270, n5);
  and and_308 (Mnemonics[7], n274, n6);
  and and_309 (Mnemonics[12], n278, n6);
  and and_310 (Mnemonics[5], n278, IR[7]);
  and and_311 (n287, n286, n3);
  and and_312 (n291, n286, IR[4]);
  and and_313 (n295, n287, IR[5]);
  and and_314 (n299, n298, n5);
  and and_315 (Mnemonics[35], n302, n6);
  and and_316 (n307, n295, IR[6]);
  and and_317 (Mnemonics[22], n289, IR[7]);
  and and_318 (n315, n314, n4);
  and and_319 (Mnemonics[50], n162, IR[7]);
  and and_320 (Mnemonics[52], n322, IR[7]);
  and and_321 (Mnemonics[25], n307, IR[7]);
  or or_175 (n331, n330, n92);
  or or_176 (n335, n334, n100);
  or or_177 (n339, n338, n58);
  or or_178 (Mnemonics[1], n342, n70);
  or or_179 (Mnemonics[2], n346, n160);
  or or_180 (n351, n350, n121);
  or or_181 (Mnemonics[17], n354, n125);
  or or_182 (Mnemonics[19], n358, n255);
  or or_183 (n363, n72, n74);
  or or_184 (n367, n366, n82);
  or or_185 (n371, n370, n258);
  or or_186 (n375, n374, n112);
  or or_187 (n379, n378, n116);
  or or_188 (n383, n382, n222);
  or or_189 (n387, n386, n238);
  or or_190 (n391, n390, n183);
  or or_191 (n395, n394, n29);
  or or_192 (Mnemonics[34], n398, n46);
  or or_193 (Mnemonics[39], n402, n175);
  or or_194 (Mnemonics[40], n406, n195);
  or or_195 (n411, n410, n130);
  or or_196 (n415, n103, n104);
  or or_197 (n419, n418, n108);
  or or_198 (n423, n205, n209);
  or or_199 (n426, n425, n78);
  or or_200 (n430, n429, n121);
  or or_201 (n434, n433, n183);
  or or_202 (n438, n437, n222);
  or or_203 (n442, n441, n258);
  or or_204 (AddressModes[0], n445, Mnemonics[28]);
  or or_205 (n450, n449, n106);
  or or_206 (n454, n453, n160);
  or or_207 (n458, n457, n242);
  or or_208 (n462, n461, n82);
  or or_209 (n466, n465, n123);
  or or_210 (n470, n469, n177);
  or or_211 (n474, n473, n88);
  or or_212 (n478, n477, n219);
  or or_213 (n482, Mnemonics[10], Mnemonics[36]);
  or or_214 (n486, n485, Mnemonics[41]);
  or or_215 (n490, n489, Mnemonics[37]);
  or or_216 (n494, n493, Mnemonics[55]);
  or or_217 (n498, n497, Mnemonics[16]);
  or or_218 (n502, n501, Mnemonics[14]);
  or or_219 (n506, n42, n67);
  or or_220 (n510, n509, n116);
  or or_221 (n514, n513, n86);
  or or_222 (n518, n517, n125);
  or or_223 (n522, n521, Mnemonics[12]);
  or or_224 (AddressModes[9], n525, Mnemonics[5]);
  or or_225 (n530, n529, n103);
  or or_226 (n534, n533, n147);
  or or_227 (n538, n537, n196);
  or or_228 (n542, n541, n246);
  or or_229 (AddressModes[10], n545, n264);
  or or_230 (n550, n549, n104);
  or or_231 (n554, n553, n151);
  or or_232 (n558, n557, n209);
  or or_233 (AddressModes[12], n197, n221);

  // Other names for the same wires on the sheet: n446 = AddressModes[0]; n460 = AddressModes[1];
  //   n468 = AddressModes[2]; n471 = AddressModes[3]; n481 = AddressModes[4]; n505 = AddressModes[5];
  //   n267 = AddressModes[6]; n512 = AddressModes[7]; n519 = AddressModes[8]; n526 = AddressModes[9];
  //   n546 = AddressModes[10]; n561 = AddressModes[11]; n562 = AddressModes[12]; IR_0 = IR[0]; IR_1 = IR[1];
  //   IR_2 = IR[2]; IR_3 = IR[3]; IR_4 = IR[4]; IR_5 = IR[5]; IR_6 = IR[6]; IR_7 = IR[7]; n336 = Mnemonics[0];
  //   n343 = Mnemonics[1]; n347 = Mnemonics[2]; n280 = Mnemonics[3]; n281 = Mnemonics[4]; n283 = Mnemonics[5];
  //   n348 = Mnemonics[6]; n275 = Mnemonics[7]; n282 = Mnemonics[8]; n272 = Mnemonics[9]; n285 = Mnemonics[10];
  //   n277 = Mnemonics[11]; n279 = Mnemonics[12]; n294 = Mnemonics[13]; n326 = Mnemonics[14]; n305 = Mnemonics[15];
  //   n320 = Mnemonics[16]; n355 = Mnemonics[17]; n357 = Mnemonics[18]; n359 = Mnemonics[19]; n362 = Mnemonics[20];
  //   n325 = Mnemonics[21]; n311 = Mnemonics[22]; n369 = Mnemonics[23]; n372 = Mnemonics[24]; n327 = Mnemonics[25];
  //   n324 = Mnemonics[26]; n373 = Mnemonics[27]; n268 = Mnemonics[28]; n380 = Mnemonics[29]; n384 = Mnemonics[30];
  //   n388 = Mnemonics[31]; n392 = Mnemonics[32]; n328 = Mnemonics[33]; n399 = Mnemonics[34]; n303 = Mnemonics[35];
  //   n290 = Mnemonics[36]; n308 = Mnemonics[37]; n297 = Mnemonics[38]; n403 = Mnemonics[39]; n407 = Mnemonics[40];
  //   n301 = Mnemonics[41]; n306 = Mnemonics[42]; n414 = Mnemonics[43]; n300 = Mnemonics[44]; n329 = Mnemonics[45];
  //   n310 = Mnemonics[46]; n420 = Mnemonics[47]; n422 = Mnemonics[48]; n424 = Mnemonics[49]; n319 = Mnemonics[50];
  //   n318 = Mnemonics[51]; n323 = Mnemonics[52]; n312 = Mnemonics[53]; n317 = Mnemonics[54]; n313 = Mnemonics[55]

  // Notes on the sheet:
  //   0=ADC, 1=AND, 2=ASL, 3=BCC, 4=BCS, 5=BEQ, 6=BIT
  //   7=BMI, 8=BNE, 9=BPL, 10=BRK, 11=BVC, 12=BVS, 13=CLC
  //   14=CLD, 15=CLI, 16=CLV, 17=CMP, 18=CPX, 19=CPY, 20=DEC
  //   21=DEX, 22=DEY, 23=EOR, 24=INC, 25=INX, 26=INY, 27=JMP
  //   28=JSR, 29=LDA, 30=LDX, 31=LDY, 32=LSR, 33=NOP, 34=ORA
  //   35=PHA, 36=PHP, 37=PLA, 38=PLP, 39=ROL, 40=ROR, 41=RTI
  //   42=RTS, 43=SBC, 44=SEC, 45=SED, 46=SEI, 47=STA, 48=STX
  //   49=STY, 50=TAX, 51=TAY, 52=TSX, 53=TXA, 54=TXS, 55=TYA
  //   0=abs, 1=absx, 2=absy, 3=acc, 4=imm
  //   5=imp, 6=ind, 7=indx, 8=indy, 9=rel
  //   10=zp, 11=zpx, 12=zpy
  //   Hardwired instruction decoder: no ROM; one decoded mnemonic and one addressing mode.
endmodule

module Alu6502 (
  input  [7:0] A,
  input  [7:0] B,
  input  [7:0] X,
  input  [7:0] Y,
  input  [7:0] SP,
  input  [7:0] P,
  input  [55:0] Mnemonics,
  input  [12:0] AddressModes,
  output [7:0] Result,
  output [7:0] NextP
);

  wire n1, n2, n3, n4, n5, n6, n7, n8, n9, n10, n11, n12, n13, n14, n15, n16, n17, n18, n19, n20, n21, n22,
       n23, n24, n25, n26, n27, n28, n29, n30, n31, n32, n33, n34, n35, n36, n37, n38, n39, n40, n41, n42,
       n43, n44, n45, n46, n47, n48, n49, n50, n51, n52, n53, n54, n55, n56, n57, n73, n74, n75, n76, n77,
       n78, n79, n80, n81, n82, n83, n84, n85, n86, n87, n88, n89, n90, n91, n92, n93, n94, n95, n96, n97,
       n98, n99, n100, n101, n102, n103, n104, n105, n106, n107, n108, n109, n110, n111, n112, n113, n114,
       n115, n116, n117, n118, n119, n120, n121, n122, n123, n124, n134, n135, n136, n137, n138, n139, n140,
       n141, n142, n143, n144, n145, n146, n147, n148, n149, n150, n151, n152, n153, n163, n164, n165, n166,
       n167, n168, n169, n170, n171, n172, n173, n174, n175, n176, n177, n178, n179, n180, n181, n182, n183,
       n184, n185, n186, n187, n188, n189, n190, n191, n192, n193, n194, n195, n196, n197, n198, n199, n200,
       n201, n202, n203, n213, n223, n233, n234, n244, n254, n255, n256, n272, n273, n274, n284, n285, n286,
       n287, n288, n289, n290, n291, n292, n293, n294, n295, n296, n297, n298, n299, n300, n301, n302, n303,
       n304, n305, n306, n307, n308, n309, n310, n311, n312, n313, n314, n315, n316, n317, n318, n319, n320,
       n321, n322, n323, n324, n325, n326, n327, n328, n329, n330, n331, n332, n333, n334, n416, n417, n418,
       n419, n420, n421, n422, n423, n424, n425, n426, n427, n428, n429, n430, n431, n432, n433, n434, n435,
       n436, n437, n438, n439, n440, n441, n442, n443, n444, n445, n446, n447, n448, n449, n450, n451, n452,
       n453, n454, n455, n456, n457, n458, n459, n460, n461, n462, n463, n464, n465, n466, n467, n468, n469,
       n470, n471, n472, n473, n474, n475, n476, n477, n478, n479, n480, n481, n482, n483, n484, n485, n486,
       n487, n488, n489, n490, n491, n493, n494, n496, n497, n498, n499, n500, n501, n502, n503, n504, n505,
       n506, n508, n509, n510, n511, n512, n514, n515, n516, n517, n518, n519, n520, n521, n522, n524;
  wire [3:0] n127, n130, n133, n156, n159, n162, n206, n209, n212, n216, n219, n222;
  wire [7:0] n60, n63, n66, n69, n72, n226, n229, n232, n237, n240, n243, n247, n250, n253, n259, n262, n265,
       n268, n271, n277, n280, n283, n337, n340, n343, n346, n349, n352, n355, n358, n361, n364, n367, n370,
       n373, n376, n379, n382, n385, n388, n391, n394, n397, n400, n403, n406, n409, n412;

  or or_1 (n1, Mnemonics[0], Mnemonics[1]);
  or or_2 (n5, n4, Mnemonics[5]);
  or or_3 (n9, n8, Mnemonics[9]);
  or or_4 (n13, n12, Mnemonics[13]);
  or or_5 (n17, n16, Mnemonics[17]);
  or or_6 (n21, n20, Mnemonics[21]);
  or or_7 (n25, n24, Mnemonics[25]);
  or or_8 (n29, n28, Mnemonics[29]);
  or or_9 (n33, n32, Mnemonics[33]);
  or or_10 (n37, n36, Mnemonics[37]);
  or or_11 (n41, n40, Mnemonics[41]);
  or or_12 (n45, n44, Mnemonics[45]);
  or or_13 (n49, n48, Mnemonics[49]);
  or or_14 (n53, n52, Mnemonics[53]);
  or or_15 (n56, Mnemonics[18], Mnemonics[19]);
  assign n60 = X & {8{Mnemonics[18]}};  // AND_Gate and_1, 8 bits wide
  assign n63 = Y & {8{Mnemonics[19]}};  // AND_Gate and_2, 8 bits wide
  assign n66 = A & {8{n57}};  // AND_Gate and_3, 8 bits wide
  assign n69 = n60 | n63;  // OR_Gate or_16, 8 bits wide
  assign n72 = n69 | n66;  // OR_Gate or_17, 8 bits wide
  or or_18 (n75, n74, Mnemonics[19]);
  xor xor_1 (n79, B[3], n75);
  xor xor_2 (n83, B[7], n75);
  or or_19 (n87, n86, Mnemonics[19]);
  FullAdder fulladder_1 (.A(n72[2]), .B(n78), .CarryIn(n92), .Sum(n93), .CarryOut(n94));
  FullAdder fulladder_2 (.A(n72[6]), .B(n82), .CarryIn(n100), .Sum(n101), .CarryOut(n102));
  FullAdder fulladder_3 (.A(A[0]), .B(B[0]), .CarryIn(P[0]), .Sum(n105), .CarryOut(n106));
  or or_20 (n113, n109, n107);
  FullAdder fulladder_4 (.A(n107), .B(1'b1), .CarryIn(n117), .Sum(n118), .CarryOut(n119));
  FullAdder fulladder_5 (.A(A[4]), .B(B[4]), .CarryIn(n115), .Sum(n134), .CarryOut(n135));
  or or_21 (n142, n138, n136);
  FullAdder fulladder_6 (.A(n136), .B(1'b1), .CarryIn(n146), .Sum(n147), .CarryOut(n148));
  not not_1 (n163, B[0]);
  FullAdder fulladder_7 (.A(A[0]), .B(n163), .CarryIn(P[0]), .Sum(n167), .CarryOut(n168));
  FullAdder fulladder_8 (.A(n167), .B(1'b0), .CarryIn(1'b0), .Sum(n175), .CarryOut(n176));
  not not_2 (n183, B[4]);
  FullAdder fulladder_9 (.A(A[4]), .B(n183), .CarryIn(n174), .Sum(n187), .CarryOut(n188));
  FullAdder fulladder_10 (.A(n187), .B(1'b0), .CarryIn(1'b0), .Sum(n195), .CarryOut(n196));
  not not_3 (n203, n174);
  assign n216 = {n193, n191, n189, n187} & {4{n194}};  // AND_Gate and_4, 4 bits wide
  assign n219 = {n201, n199, n197, n195} & {4{n213}};  // AND_Gate and_5, 4 bits wide
  assign n222 = n216 | n219;  // OR_Gate or_22, 4 bits wide
  not not_4 (n234, n233);
  not not_5 (n244, AddressModes[3]);
  or or_23 (n272, Mnemonics[21], Mnemonics[22]);
  FullAdder fulladder_11 (.A(n271[1]), .B(n283[1]), .CarryIn(n285), .Sum(n286), .CarryOut(n287));
  FullAdder fulladder_12 (.A(n271[5]), .B(n283[5]), .CarryIn(n293), .Sum(n294), .CarryOut(n295));
  and and_6 (n301, A[1], B[1]);
  and and_7 (n305, A[5], B[5]);
  or or_24 (n309, A[1], B[1]);
  or or_25 (n313, A[5], B[5]);
  xor xor_3 (n317, A[1], B[1]);
  xor xor_4 (n321, A[5], B[5]);
  or or_26 (n325, n324, Mnemonics[31]);
  or or_27 (n329, Mnemonics[1], Mnemonics[6]);
  or or_28 (n333, n332, Mnemonics[22]);
  assign n337 = B & {8{n325}};  // AND_Gate and_8, 8 bits wide
  assign n340 = n243 & {8{n328}};  // AND_Gate and_9, 8 bits wide
  assign n343 = {n307, n306, n305, n304, n303, n302, n301, n300} & {8{n329}};  // AND_Gate and_10, 8 bits wide
  assign n346 = {n315, n314, n313, n312, n311, n310, n309, n308} & {8{Mnemonics[34]}};  // AND_Gate and_11, 8 bits wide
  assign n349 = {n323, n322, n321, n320, n319, n318, n317, n316} & {8{Mnemonics[23]}};  // AND_Gate and_12, 8 bits wide
  assign n352 = {n253[6:0], 1'b0} & {8{Mnemonics[2]}};  // AND_Gate and_13, 8 bits wide
  assign n355 = {1'b0, n253[7:1]} & {8{Mnemonics[32]}};  // AND_Gate and_14, 8 bits wide
  assign n358 = {n253[6:0], P[0]} & {8{Mnemonics[39]}};  // AND_Gate and_15, 8 bits wide
  assign n361 = {P[0], n253[7:1]} & {8{Mnemonics[40]}};  // AND_Gate and_16, 8 bits wide
  assign n364 = {n298, n296, n294, n292, n290, n288, n286, n284} & {8{n333}};  // AND_Gate and_17, 8 bits wide
  assign n367 = A & {8{n334}};  // AND_Gate and_18, 8 bits wide
  assign n370 = X & {8{Mnemonics[53]}};  // AND_Gate and_19, 8 bits wide
  assign n373 = Y & {8{Mnemonics[55]}};  // AND_Gate and_20, 8 bits wide
  assign n376 = SP & {8{Mnemonics[52]}};  // AND_Gate and_21, 8 bits wide
  assign n379 = n337 | n340;  // OR_Gate or_29, 8 bits wide
  assign n382 = n343 | n346;  // OR_Gate or_30, 8 bits wide
  assign n385 = n349 | n352;  // OR_Gate or_31, 8 bits wide
  assign n388 = n355 | n358;  // OR_Gate or_32, 8 bits wide
  assign n391 = n361 | n364;  // OR_Gate or_33, 8 bits wide
  assign n394 = n367 | n370;  // OR_Gate or_34, 8 bits wide
  assign n397 = n373 | n376;  // OR_Gate or_35, 8 bits wide
  assign n400 = n379 | n382;  // OR_Gate or_36, 8 bits wide
  assign n403 = n385 | n388;  // OR_Gate or_37, 8 bits wide
  assign n406 = n391 | n394;  // OR_Gate or_38, 8 bits wide
  assign n409 = n400 | n403;  // OR_Gate or_39, 8 bits wide
  assign n412 = n406 | n397;  // OR_Gate or_40, 8 bits wide
  assign Result = n409 | n412;  // OR_Gate or_41, 8 bits wide
  or or_42 (n418, n417, Mnemonics[40]);
  or or_43 (n419, n325, Mnemonics[0]);
  or or_44 (n423, n422, Mnemonics[23]);
  or or_45 (n427, n426, Mnemonics[2]);
  or or_46 (n431, n430, Mnemonics[24]);
  or or_47 (n435, n434, Mnemonics[26]);
  or or_48 (n439, n438, Mnemonics[53]);
  or or_49 (n443, Result[0], Result[1]);
  or or_50 (n447, n446, Result[5]);
  and and_22 (n451, n442, n450);
  and and_23 (n455, Mnemonics[6], B[7]);
  and and_24 (n459, n442, n458);
  and and_25 (n463, n462, n253[7]);
  and and_26 (n467, n328, n104);
  or or_51 (n471, n328, n418);
  or or_52 (n475, n472, n474);
  and and_27 (n479, n476, n478);
  and and_28 (n483, n84, n479);
  not not_6 (n487, Mnemonics[13]);
  and and_29 (n491, n490, P[2]);
  or or_53 (NextP[3], Mnemonics[45], n494);
  or or_54 (n499, n498, n95);
  or or_55 (n503, n502, n103);
  or or_56 (NextP[1], n505, n506);
  and and_30 (n511, n233, n510);
  xor xor_5 (n515, A[7], n140);
  and and_31 (n519, n518, n486);
  or or_57 (NextP[0], n521, n522);
  or or_58 (n2, n1, Mnemonics[2]);
  or or_59 (n6, n5, Mnemonics[6]);
  or or_60 (n10, n9, Mnemonics[10]);
  or or_61 (n14, n13, Mnemonics[14]);
  or or_62 (n18, n17, Mnemonics[18]);
  or or_63 (n22, n21, Mnemonics[22]);
  or or_64 (n26, n25, Mnemonics[26]);
  or or_65 (n30, n29, Mnemonics[30]);
  or or_66 (n34, n33, Mnemonics[34]);
  or or_67 (n38, n37, Mnemonics[38]);
  or or_68 (n42, n41, Mnemonics[42]);
  or or_69 (n46, n45, Mnemonics[46]);
  or or_70 (n50, n49, Mnemonics[50]);
  or or_71 (n54, n53, Mnemonics[54]);
  not not_7 (n57, n56);
  xor xor_6 (n76, B[0], n75);
  xor xor_7 (n80, B[4], n75);
  or or_72 (n84, Mnemonics[0], Mnemonics[43]);
  or or_73 (n88, n85, n87);
  FullAdder fulladder_13 (.A(n72[3]), .B(n79), .CarryIn(n94), .Sum(n95), .CarryOut(n96));
  FullAdder fulladder_14 (.A(n72[7]), .B(n83), .CarryIn(n102), .Sum(n103), .CarryOut(n104));
  FullAdder fulladder_15 (.A(A[1]), .B(B[1]), .CarryIn(n106), .Sum(n107), .CarryOut(n108));
  and and_32 (n114, n111, n113);
  FullAdder fulladder_16 (.A(n109), .B(1'b1), .CarryIn(n119), .Sum(n120), .CarryOut(n121));
  FullAdder fulladder_17 (.A(A[5]), .B(B[5]), .CarryIn(n135), .Sum(n136), .CarryOut(n137));
  and and_33 (n143, n140, n142);
  FullAdder fulladder_18 (.A(n138), .B(1'b1), .CarryIn(n148), .Sum(n149), .CarryOut(n150));
  not not_8 (n164, B[1]);
  FullAdder fulladder_19 (.A(A[1]), .B(n164), .CarryIn(n168), .Sum(n169), .CarryOut(n170));
  FullAdder fulladder_20 (.A(n169), .B(1'b1), .CarryIn(n176), .Sum(n177), .CarryOut(n178));
  not not_9 (n184, B[5]);
  FullAdder fulladder_21 (.A(A[5]), .B(n184), .CarryIn(n188), .Sum(n189), .CarryOut(n190));
  FullAdder fulladder_22 (.A(n189), .B(1'b1), .CarryIn(n196), .Sum(n197), .CarryOut(n198));
  not not_10 (n213, n194);
  assign n226 = {n162, n133} & {8{Mnemonics[0]}};  // AND_Gate and_34, 8 bits wide
  assign n229 = {n222, n212} & {8{n223}};  // AND_Gate and_35, 8 bits wide
  assign n232 = n226 | n229;  // OR_Gate or_74, 8 bits wide
  or or_75 (n254, Mnemonics[25], Mnemonics[21]);
  or or_76 (n273, n272, Mnemonics[20]);
  assign n277 = {8{1'b1}} & {8{n273}};  // AND_Gate and_36, 8 bits wide
  assign n280 = 8'h1 & {8{n274}};  // AND_Gate and_37, 8 bits wide
  assign n283 = n277 | n280;  // OR_Gate or_77, 8 bits wide
  FullAdder fulladder_23 (.A(n271[2]), .B(n283[2]), .CarryIn(n287), .Sum(n288), .CarryOut(n289));
  FullAdder fulladder_24 (.A(n271[6]), .B(n283[6]), .CarryIn(n295), .Sum(n296), .CarryOut(n297));
  and and_38 (n302, A[2], B[2]);
  and and_39 (n306, A[6], B[6]);
  or or_78 (n310, A[2], B[2]);
  or or_79 (n314, A[6], B[6]);
  xor xor_8 (n318, A[2], B[2]);
  xor xor_9 (n322, A[6], B[6]);
  or or_80 (n326, n84, Mnemonics[17]);
  or or_81 (n330, n256, Mnemonics[25]);
  or or_82 (n334, Mnemonics[50], Mnemonics[51]);
  or or_83 (n420, n419, Mnemonics[43]);
  or or_84 (n424, n423, Mnemonics[17]);
  or or_85 (n428, n427, Mnemonics[32]);
  or or_86 (n432, n431, Mnemonics[20]);
  or or_87 (n436, n435, Mnemonics[22]);
  or or_88 (n440, n439, Mnemonics[55]);
  or or_89 (n444, n443, Result[2]);
  or or_90 (n448, n447, Result[6]);
  not not_11 (n452, n442);
  not not_12 (n456, Mnemonics[6]);
  and and_40 (n460, n452, P[7]);
  not not_13 (n464, n462);
  not not_14 (n468, n328);
  and and_41 (n472, n471, n470);
  xor xor_10 (n476, n72[7], n103);
  and and_42 (n480, Mnemonics[6], B[6]);
  not not_15 (n484, n84);
  and and_43 (n488, n487, n475);
  or or_91 (NextP[2], Mnemonics[46], n491);
  and and_44 (n496, P[3], Mnemonics[0]);
  or or_92 (n500, n499, n97);
  not not_16 (n504, n503);
  and and_45 (n508, Mnemonics[0], n140);
  and and_46 (n512, n234, n461);
  and and_47 (n516, n514, n515);
  or or_93 (n520, n517, n519);
  not not_17 (n524, Mnemonics[16]);
  or or_94 (n3, n2, Mnemonics[3]);
  or or_95 (n7, n6, Mnemonics[7]);
  or or_96 (n11, n10, Mnemonics[11]);
  or or_97 (n15, n14, Mnemonics[15]);
  or or_98 (n19, n18, Mnemonics[19]);
  or or_99 (n23, n22, Mnemonics[23]);
  or or_100 (n27, n26, Mnemonics[27]);
  or or_101 (n31, n30, Mnemonics[31]);
  or or_102 (n35, n34, Mnemonics[35]);
  or or_103 (n39, n38, Mnemonics[39]);
  or or_104 (n43, n42, Mnemonics[43]);
  or or_105 (n47, n46, Mnemonics[47]);
  or or_106 (n51, n50, Mnemonics[51]);
  or or_107 (n55, n54, Mnemonics[55]);
  or or_108 (n73, Mnemonics[43], Mnemonics[17]);
  xor xor_11 (n77, B[1], n75);
  xor xor_12 (n81, B[5], n75);
  and and_48 (n85, n84, P[0]);
  FullAdder fulladder_25 (.A(n72[0]), .B(n76), .CarryIn(n88), .Sum(n89), .CarryOut(n90));
  FullAdder fulladder_26 (.A(n72[4]), .B(n80), .CarryIn(n96), .Sum(n97), .CarryOut(n98));
  FullAdder fulladder_27 (.A(A[2]), .B(B[2]), .CarryIn(n108), .Sum(n109), .CarryOut(n110));
  or or_109 (n115, n112, n114);
  FullAdder fulladder_28 (.A(n111), .B(1'b0), .CarryIn(n121), .Sum(n122), .CarryOut(n123));
  assign n127 = {n122, n120, n118, n116} & {4{n115}};  // AND_Gate and_49, 4 bits wide
  assign n130 = {n111, n109, n107, n105} & {4{n124}};  // AND_Gate and_50, 4 bits wide
  assign n133 = n127 | n130;  // OR_Gate or_110, 4 bits wide
  FullAdder fulladder_29 (.A(A[6]), .B(B[6]), .CarryIn(n137), .Sum(n138), .CarryOut(n139));
  or or_111 (n144, n141, n143);
  FullAdder fulladder_30 (.A(n140), .B(1'b0), .CarryIn(n150), .Sum(n151), .CarryOut(n152));
  assign n156 = {n151, n149, n147, n145} & {4{n144}};  // AND_Gate and_51, 4 bits wide
  assign n159 = {n140, n138, n136, n134} & {4{n153}};  // AND_Gate and_52, 4 bits wide
  assign n162 = n156 | n159;  // OR_Gate or_112, 4 bits wide
  not not_18 (n165, B[2]);
  FullAdder fulladder_31 (.A(A[2]), .B(n165), .CarryIn(n170), .Sum(n171), .CarryOut(n172));
  FullAdder fulladder_32 (.A(n171), .B(1'b0), .CarryIn(n178), .Sum(n179), .CarryOut(n180));
  not not_19 (n185, B[6]);
  FullAdder fulladder_33 (.A(A[6]), .B(n185), .CarryIn(n190), .Sum(n191), .CarryOut(n192));
  FullAdder fulladder_34 (.A(n191), .B(1'b0), .CarryIn(n198), .Sum(n199), .CarryOut(n200));
  not not_20 (n223, Mnemonics[0]);
  or or_113 (n255, Mnemonics[26], Mnemonics[22]);
  assign n259 = X & {8{n254}};  // AND_Gate and_53, 8 bits wide
  assign n262 = Y & {8{n255}};  // AND_Gate and_54, 8 bits wide
  assign n265 = B & {8{n256}};  // AND_Gate and_55, 8 bits wide
  assign n268 = n259 | n262;  // OR_Gate or_114, 8 bits wide
  assign n271 = n268 | n265;  // OR_Gate or_115, 8 bits wide
  not not_21 (n274, n273);
  FullAdder fulladder_35 (.A(n271[3]), .B(n283[3]), .CarryIn(n289), .Sum(n290), .CarryOut(n291));
  FullAdder fulladder_36 (.A(n271[7]), .B(n283[7]), .CarryIn(n297), .Sum(n298), .CarryOut(n299));
  and and_56 (n303, A[3], B[3]);
  and and_57 (n307, A[7], B[7]);
  or or_116 (n311, A[3], B[3]);
  or or_117 (n315, A[7], B[7]);
  xor xor_13 (n319, A[3], B[3]);
  xor xor_14 (n323, A[7], B[7]);
  or or_118 (n327, n326, Mnemonics[18]);
  or or_119 (n331, n330, Mnemonics[21]);
  or or_120 (n416, Mnemonics[2], Mnemonics[32]);
  or or_121 (n421, n420, Mnemonics[1]);
  or or_122 (n425, n424, Mnemonics[18]);
  or or_123 (n429, n428, Mnemonics[39]);
  or or_124 (n433, n432, Mnemonics[25]);
  or or_125 (n437, n436, Mnemonics[50]);
  or or_126 (n441, n440, Mnemonics[52]);
  or or_127 (n445, n444, Result[3]);
  or or_128 (n449, n448, Result[7]);
  and and_58 (n453, n452, P[1]);
  and and_59 (n457, n456, Result[7]);
  or or_129 (n461, n459, n460);
  and and_60 (n465, n464, n253[0]);
  and and_61 (n469, n468, n466);
  not not_22 (n473, n471);
  xor xor_15 (n477, n72[7], n83);
  and and_62 (n481, n456, P[6]);
  and and_63 (n485, n484, n482);
  or or_130 (n489, Mnemonics[44], n488);
  not not_23 (n493, Mnemonics[14]);
  or or_131 (n497, n89, n91);
  or or_132 (n501, n500, n99);
  and and_64 (n505, n233, n504);
  and and_65 (n509, n223, n103);
  or or_133 (NextP[7], n511, n512);
  and and_66 (n517, n496, n516);
  and and_67 (n521, n496, n144);
  and and_68 (NextP[6], n520, n524);
  or or_134 (n4, n3, Mnemonics[4]);
  or or_135 (n8, n7, Mnemonics[8]);
  or or_136 (n12, n11, Mnemonics[12]);
  or or_137 (n16, n15, Mnemonics[16]);
  or or_138 (n20, n19, Mnemonics[20]);
  or or_139 (n24, n23, Mnemonics[24]);
  or or_140 (n28, n27, Mnemonics[28]);
  or or_141 (n32, n31, Mnemonics[32]);
  or or_142 (n36, n35, Mnemonics[36]);
  or or_143 (n40, n39, Mnemonics[40]);
  or or_144 (n44, n43, Mnemonics[44]);
  or or_145 (n48, n47, Mnemonics[48]);
  or or_146 (n52, n51, Mnemonics[52]);
  or or_147 (n74, n73, Mnemonics[18]);
  xor xor_16 (n78, B[2], n75);
  xor xor_17 (n82, B[6], n75);
  or or_148 (n86, Mnemonics[17], Mnemonics[18]);
  FullAdder fulladder_37 (.A(n72[1]), .B(n77), .CarryIn(n90), .Sum(n91), .CarryOut(n92));
  FullAdder fulladder_38 (.A(n72[5]), .B(n81), .CarryIn(n98), .Sum(n99), .CarryOut(n100));
  FullAdder fulladder_39 (.A(A[3]), .B(B[3]), .CarryIn(n110), .Sum(n111), .CarryOut(n112));
  FullAdder fulladder_40 (.A(n105), .B(1'b0), .CarryIn(1'b0), .Sum(n116), .CarryOut(n117));
  not not_24 (n124, n115);
  FullAdder fulladder_41 (.A(A[7]), .B(B[7]), .CarryIn(n139), .Sum(n140), .CarryOut(n141));
  FullAdder fulladder_42 (.A(n134), .B(1'b0), .CarryIn(1'b0), .Sum(n145), .CarryOut(n146));
  not not_25 (n153, n144);
  not not_26 (n166, B[3]);
  FullAdder fulladder_43 (.A(A[3]), .B(n166), .CarryIn(n172), .Sum(n173), .CarryOut(n174));
  FullAdder fulladder_44 (.A(n173), .B(1'b1), .CarryIn(n180), .Sum(n181), .CarryOut(n182));
  not not_27 (n186, B[7]);
  FullAdder fulladder_45 (.A(A[7]), .B(n186), .CarryIn(n192), .Sum(n193), .CarryOut(n194));
  FullAdder fulladder_46 (.A(n193), .B(1'b1), .CarryIn(n200), .Sum(n201), .CarryOut(n202));
  assign n206 = {n173, n171, n169, n167} & {4{n174}};  // AND_Gate and_69, 4 bits wide
  assign n209 = {n181, n179, n177, n175} & {4{n203}};  // AND_Gate and_70, 4 bits wide
  assign n212 = n206 | n209;  // OR_Gate or_149, 4 bits wide
  and and_71 (n233, P[3], n84);
  assign n237 = n232 & {8{n233}};  // AND_Gate and_72, 8 bits wide
  assign n240 = {n103, n101, n99, n97, n95, n93, n91, n89} & {8{n234}};  // AND_Gate and_73, 8 bits wide
  assign n243 = n237 | n240;  // OR_Gate or_150, 8 bits wide
  assign n247 = A & {8{AddressModes[3]}};  // AND_Gate and_74, 8 bits wide
  assign n250 = B & {8{n244}};  // AND_Gate and_75, 8 bits wide
  assign n253 = n247 | n250;  // OR_Gate or_151, 8 bits wide
  or or_152 (n256, Mnemonics[24], Mnemonics[20]);
  FullAdder fulladder_47 (.A(n271[0]), .B(n283[0]), .CarryIn(1'b0), .Sum(n284), .CarryOut(n285));
  FullAdder fulladder_48 (.A(n271[4]), .B(n283[4]), .CarryIn(n291), .Sum(n292), .CarryOut(n293));
  and and_76 (n300, A[0], B[0]);
  and and_77 (n304, A[4], B[4]);
  or or_153 (n308, A[0], B[0]);
  or or_154 (n312, A[4], B[4]);
  xor xor_18 (n316, A[0], B[0]);
  xor xor_19 (n320, A[4], B[4]);
  or or_155 (n324, Mnemonics[29], Mnemonics[30]);
  or or_156 (n328, n327, Mnemonics[19]);
  or or_157 (n332, n331, Mnemonics[26]);
  or or_158 (n417, n416, Mnemonics[39]);
  or or_159 (n422, n421, Mnemonics[34]);
  or or_160 (n426, n425, Mnemonics[19]);
  or or_161 (n430, n429, Mnemonics[40]);
  or or_162 (n434, n433, Mnemonics[21]);
  or or_163 (n438, n437, Mnemonics[51]);
  or or_164 (n442, n441, Mnemonics[6]);
  or or_165 (n446, n445, Result[4]);
  not not_28 (n450, n449);
  or or_166 (n454, n451, n453);
  or or_167 (n458, n455, n457);
  or or_168 (n462, Mnemonics[2], Mnemonics[39]);
  or or_169 (n466, n463, n465);
  or or_170 (n470, n467, n469);
  and and_78 (n474, n473, P[0]);
  not not_29 (n478, n477);
  or or_171 (n482, n480, n481);
  or or_172 (n486, n483, n485);
  not not_30 (n490, Mnemonics[15]);
  and and_79 (n494, n493, P[3]);
  or or_173 (n498, n497, n93);
  or or_174 (n502, n501, n101);
  and and_80 (n506, n234, n454);
  or or_175 (n510, n508, n509);
  not not_31 (n514, n323);
  not not_32 (n518, n496);
  and and_81 (n522, n518, n489);

  assign NextP[5:4] = 2'b10;

  // Other names for the same wires on the sheet: AddressModes_0 = AddressModes[0]; AddressModes_1 = AddressModes[1];
  //   AddressModes_2 = AddressModes[2]; AddressModes_3 = AddressModes[3]; n246[7:0] = {8{AddressModes[3]}};
  //   AddressModes_4 = AddressModes[4]; AddressModes_5 = AddressModes[5]; AddressModes_6 = AddressModes[6];
  //   AddressModes_7 = AddressModes[7]; AddressModes_8 = AddressModes[8]; AddressModes_9 = AddressModes[9];
  //   AddressModes_10 = AddressModes[10]; AddressModes_11 = AddressModes[11]; AddressModes_12 = AddressModes[12];
  //   Mnemonics_0 = Mnemonics[0]; n225[7:0] = {8{Mnemonics[0]}}; Mnemonics_1 = Mnemonics[1];
  //   Mnemonics_3 = Mnemonics[3]; Mnemonics_4 = Mnemonics[4]; Mnemonics_5 = Mnemonics[5]; Mnemonics_6 = Mnemonics[6];
  //   Mnemonics_7 = Mnemonics[7]; Mnemonics_8 = Mnemonics[8]; Mnemonics_9 = Mnemonics[9];
  //   Mnemonics_10 = Mnemonics[10]; Mnemonics_11 = Mnemonics[11]; Mnemonics_12 = Mnemonics[12];
  //   Mnemonics_13 = Mnemonics[13]; Mnemonics_14 = Mnemonics[14]; Mnemonics_15 = Mnemonics[15];
  //   Mnemonics_16 = Mnemonics[16]; Mnemonics_17 = Mnemonics[17]; Mnemonics_20 = Mnemonics[20];
  //   Mnemonics_21 = Mnemonics[21]; Mnemonics_22 = Mnemonics[22]; Mnemonics_24 = Mnemonics[24];
  //   Mnemonics_25 = Mnemonics[25]; Mnemonics_26 = Mnemonics[26]; Mnemonics_27 = Mnemonics[27];
  //   Mnemonics_28 = Mnemonics[28]; Mnemonics_29 = Mnemonics[29]; Mnemonics_30 = Mnemonics[30];
  //   Mnemonics_31 = Mnemonics[31]; Mnemonics_33 = Mnemonics[33]; Mnemonics_35 = Mnemonics[35];
  //   Mnemonics_36 = Mnemonics[36]; Mnemonics_37 = Mnemonics[37]; Mnemonics_38 = Mnemonics[38];
  //   Mnemonics_41 = Mnemonics[41]; Mnemonics_42 = Mnemonics[42]; Mnemonics_43 = Mnemonics[43];
  //   Mnemonics_44 = Mnemonics[44]; Mnemonics_45 = Mnemonics[45]; Mnemonics_46 = Mnemonics[46];
  //   Mnemonics_47 = Mnemonics[47]; Mnemonics_48 = Mnemonics[48]; Mnemonics_49 = Mnemonics[49];
  //   Mnemonics_50 = Mnemonics[50]; Mnemonics_51 = Mnemonics[51]; Mnemonics_54 = Mnemonics[54];
  //   Mnemonics_18 = Mnemonics[18]; n59[7:0] = {8{Mnemonics[18]}}; Mnemonics_19 = Mnemonics[19];
  //   n62[7:0] = {8{Mnemonics[19]}}; n65[7:0] = {8{n57}}; n60_0 = n60[0]; n67[7:0] = n60; n60_1 = n60[1];
  //   n60_2 = n60[2]; n60_3 = n60[3]; n60_4 = n60[4]; n60_5 = n60[5]; n60_6 = n60[6]; n60_7 = n60[7]; n63_0 = n63[0];
  //   n68[7:0] = n63; n63_1 = n63[1]; n63_2 = n63[2]; n63_3 = n63[3]; n63_4 = n63[4]; n63_5 = n63[5]; n63_6 = n63[6];
  //   n63_7 = n63[7]; n69_0 = n69[0]; n70[7:0] = n69; n69_1 = n69[1]; n69_2 = n69[2]; n69_3 = n69[3]; n69_4 = n69[4];
  //   n69_5 = n69[5]; n69_6 = n69[6]; n69_7 = n69[7]; n66_0 = n66[0]; n71[7:0] = n66; n66_1 = n66[1]; n66_2 = n66[2];
  //   n66_3 = n66[3]; n66_4 = n66[4]; n66_5 = n66[5]; n66_6 = n66[6]; n66_7 = n66[7]; n72_0 = n72[0]; n72_1 = n72[1];
  //   n72_2 = n72[2]; n72_3 = n72[3]; n72_4 = n72[4]; n72_5 = n72[5]; n72_6 = n72[6]; n72_7 = n72[7];
  //   n125[3:0] = {n122, n120, n118, n116}; n126[3:0] = {4{n115}}; n127_0 = n127[0]; n131[3:0] = n127;
  //   n127_1 = n127[1]; n127_2 = n127[2]; n127_3 = n127[3]; n128[3:0] = {n111, n109, n107, n105};
  //   n129[3:0] = {4{n124}}; n130_0 = n130[0]; n132[3:0] = n130; n130_1 = n130[1]; n130_2 = n130[2]; n130_3 = n130[3];
  //   n154[3:0] = {n151, n149, n147, n145}; n155[3:0] = {4{n144}}; n156_0 = n156[0]; n160[3:0] = n156;
  //   n156_1 = n156[1]; n156_2 = n156[2]; n156_3 = n156[3]; n157[3:0] = {n140, n138, n136, n134};
  //   n158[3:0] = {4{n153}}; n159_0 = n159[0]; n161[3:0] = n159; n159_1 = n159[1]; n159_2 = n159[2]; n159_3 = n159[3];
  //   n204[3:0] = {n173, n171, n169, n167}; n205[3:0] = {4{n174}}; n207[3:0] = {n181, n179, n177, n175};
  //   n208[3:0] = {4{n203}}; n206_0 = n206[0]; n210[3:0] = n206; n206_1 = n206[1]; n206_2 = n206[2]; n206_3 = n206[3];
  //   n209_0 = n209[0]; n211[3:0] = n209; n209_1 = n209[1]; n209_2 = n209[2]; n209_3 = n209[3];
  //   n214[3:0] = {n193, n191, n189, n187}; n215[3:0] = {4{n194}}; n217[3:0] = {n201, n199, n197, n195};
  //   n218[3:0] = {4{n213}}; n216_0 = n216[0]; n220[3:0] = n216; n216_1 = n216[1]; n216_2 = n216[2]; n216_3 = n216[3];
  //   n219_0 = n219[0]; n221[3:0] = n219; n219_1 = n219[1]; n219_2 = n219[2]; n219_3 = n219[3]; n133_0 = n133[0];
  //   n224[7:0] = {n162, n133}; n133_1 = n133[1]; n133_2 = n133[2]; n133_3 = n133[3]; n162_0 = n162[0];
  //   n162_1 = n162[1]; n162_2 = n162[2]; n162_3 = n162[3]; n212_0 = n212[0]; n227[7:0] = {n222, n212};
  //   n212_1 = n212[1]; n212_2 = n212[2]; n212_3 = n212[3]; n222_0 = n222[0]; n222_1 = n222[1]; n222_2 = n222[2];
  //   n222_3 = n222[3]; n228[7:0] = {8{n223}}; n229_0 = n229[0]; n231[7:0] = n229; n229_1 = n229[1]; n229_2 = n229[2];
  //   n229_3 = n229[3]; n229_4 = n229[4]; n229_5 = n229[5]; n229_6 = n229[6]; n229_7 = n229[7]; n226_0 = n226[0];
  //   n230[7:0] = n226; n226_1 = n226[1]; n226_2 = n226[2]; n226_3 = n226[3]; n226_4 = n226[4]; n226_5 = n226[5];
  //   n226_6 = n226[6]; n226_7 = n226[7]; n232_0 = n232[0]; n235[7:0] = n232; n232_1 = n232[1]; n232_2 = n232[2];
  //   n232_3 = n232[3]; n232_4 = n232[4]; n232_5 = n232[5]; n232_6 = n232[6]; n232_7 = n232[7]; n236[7:0] = {8{n233}};
  //   n238[7:0] = {n103, n101, n99, n97, n95, n93, n91, n89}; n239[7:0] = {8{n234}}; n237_0 = n237[0];
  //   n241[7:0] = n237; n237_1 = n237[1]; n237_2 = n237[2]; n237_3 = n237[3]; n237_4 = n237[4]; n237_5 = n237[5];
  //   n237_6 = n237[6]; n237_7 = n237[7]; n240_0 = n240[0]; n242[7:0] = n240; n240_1 = n240[1]; n240_2 = n240[2];
  //   n240_3 = n240[3]; n240_4 = n240[4]; n240_5 = n240[5]; n240_6 = n240[6]; n240_7 = n240[7]; n249[7:0] = {8{n244}};
  //   n247_0 = n247[0]; n251[7:0] = n247; n247_1 = n247[1]; n247_2 = n247[2]; n247_3 = n247[3]; n247_4 = n247[4];
  //   n247_5 = n247[5]; n247_6 = n247[6]; n247_7 = n247[7]; n250_0 = n250[0]; n252[7:0] = n250; n250_1 = n250[1];
  //   n250_2 = n250[2]; n250_3 = n250[3]; n250_4 = n250[4]; n250_5 = n250[5]; n250_6 = n250[6]; n250_7 = n250[7];
  //   n258[7:0] = {8{n254}}; n259_0 = n259[0]; n266[7:0] = n259; n259_1 = n259[1]; n259_2 = n259[2]; n259_3 = n259[3];
  //   n259_4 = n259[4]; n259_5 = n259[5]; n259_6 = n259[6]; n259_7 = n259[7]; n261[7:0] = {8{n255}}; n262_0 = n262[0];
  //   n267[7:0] = n262; n262_1 = n262[1]; n262_2 = n262[2]; n262_3 = n262[3]; n262_4 = n262[4]; n262_5 = n262[5];
  //   n262_6 = n262[6]; n262_7 = n262[7]; n264[7:0] = {8{n256}}; n265_0 = n265[0]; n270[7:0] = n265; n265_1 = n265[1];
  //   n265_2 = n265[2]; n265_3 = n265[3]; n265_4 = n265[4]; n265_5 = n265[5]; n265_6 = n265[6]; n265_7 = n265[7];
  //   n268_0 = n268[0]; n269[7:0] = n268; n268_1 = n268[1]; n268_2 = n268[2]; n268_3 = n268[3]; n268_4 = n268[4];
  //   n268_5 = n268[5]; n268_6 = n268[6]; n268_7 = n268[7]; n271_0 = n271[0]; n271_1 = n271[1]; n271_2 = n271[2];
  //   n271_3 = n271[3]; n271_4 = n271[4]; n271_5 = n271[5]; n271_6 = n271[6]; n271_7 = n271[7]; n276[7:0] = {8{n273}};
  //   n279[7:0] = {8{n274}}; n280_0 = n280[0]; n282[7:0] = n280; n280_1 = n280[1]; n280_2 = n280[2]; n280_3 = n280[3];
  //   n280_4 = n280[4]; n280_5 = n280[5]; n280_6 = n280[6]; n280_7 = n280[7]; n277_0 = n277[0]; n281[7:0] = n277;
  //   n277_1 = n277[1]; n277_2 = n277[2]; n277_3 = n277[3]; n277_4 = n277[4]; n277_5 = n277[5]; n277_6 = n277[6];
  //   n277_7 = n277[7]; n283_0 = n283[0]; n283_1 = n283[1]; n283_2 = n283[2]; n283_3 = n283[3]; n283_4 = n283[4];
  //   n283_5 = n283[5]; n283_6 = n283[6]; n283_7 = n283[7]; B_0 = B[0]; n248[7:0] = B; n263[7:0] = B; n335[7:0] = B;
  //   B_1 = B[1]; B_2 = B[2]; B_3 = B[3]; B_4 = B[4]; B_5 = B[5]; B_6 = B[6]; B_7 = B[7]; n336[7:0] = {8{n325}};
  //   n243_0 = n243[0]; n338[7:0] = n243; n243_1 = n243[1]; n243_2 = n243[2]; n243_3 = n243[3]; n243_4 = n243[4];
  //   n243_5 = n243[5]; n243_6 = n243[6]; n243_7 = n243[7]; n339[7:0] = {8{n328}};
  //   n341[7:0] = {n307, n306, n305, n304, n303, n302, n301, n300}; n342[7:0] = {8{n329}};
  //   n344[7:0] = {n315, n314, n313, n312, n311, n310, n309, n308}; Mnemonics_34 = Mnemonics[34];
  //   n345[7:0] = {8{Mnemonics[34]}}; n347[7:0] = {n323, n322, n321, n320, n319, n318, n317, n316};
  //   Mnemonics_23 = Mnemonics[23]; n348[7:0] = {8{Mnemonics[23]}}; Mnemonics_2 = Mnemonics[2];
  //   n351[7:0] = {8{Mnemonics[2]}}; Mnemonics_32 = Mnemonics[32]; n354[7:0] = {8{Mnemonics[32]}}; n253_0 = n253[0];
  //   n350[7:1] = n253[6:0]; n356[7:0] = {n253[6:0], P[0]}; Mnemonics_39 = Mnemonics[39];
  //   n357[7:0] = {8{Mnemonics[39]}}; n253_1 = n253[1]; n353[6:0] = n253[7:1]; n359[7:0] = {P[0], n253[7:1]};
  //   n253_2 = n253[2]; n253_3 = n253[3]; n253_4 = n253[4]; n253_5 = n253[5]; n253_6 = n253[6]; n253_7 = n253[7];
  //   P_0 = P[0]; Mnemonics_40 = Mnemonics[40]; n360[7:0] = {8{Mnemonics[40]}};
  //   n362[7:0] = {n298, n296, n294, n292, n290, n288, n286, n284}; n363[7:0] = {8{n333}}; A_0 = A[0]; n64[7:0] = A;
  //   n245[7:0] = A; n365[7:0] = A; A_1 = A[1]; A_2 = A[2]; A_3 = A[3]; A_4 = A[4]; A_5 = A[5]; A_6 = A[6];
  //   A_7 = A[7]; n366[7:0] = {8{n334}}; n58[7:0] = X; n257[7:0] = X; n368[7:0] = X; X_0 = X[0]; X_1 = X[1];
  //   X_2 = X[2]; X_3 = X[3]; X_4 = X[4]; X_5 = X[5]; X_6 = X[6]; X_7 = X[7]; Mnemonics_53 = Mnemonics[53];
  //   n369[7:0] = {8{Mnemonics[53]}}; Mnemonics_55 = Mnemonics[55]; n372[7:0] = {8{Mnemonics[55]}}; n374[7:0] = SP;
  //   SP_0 = SP[0]; SP_1 = SP[1]; SP_2 = SP[2]; SP_3 = SP[3]; SP_4 = SP[4]; SP_5 = SP[5]; SP_6 = SP[6]; SP_7 = SP[7];
  //   Mnemonics_52 = Mnemonics[52]; n375[7:0] = {8{Mnemonics[52]}}; n337_0 = n337[0]; n377[7:0] = n337;
  //   n337_1 = n337[1]; n337_2 = n337[2]; n337_3 = n337[3]; n337_4 = n337[4]; n337_5 = n337[5]; n337_6 = n337[6];
  //   n337_7 = n337[7]; n340_0 = n340[0]; n378[7:0] = n340; n340_1 = n340[1]; n340_2 = n340[2]; n340_3 = n340[3];
  //   n340_4 = n340[4]; n340_5 = n340[5]; n340_6 = n340[6]; n340_7 = n340[7]; n343_0 = n343[0]; n380[7:0] = n343;
  //   n343_1 = n343[1]; n343_2 = n343[2]; n343_3 = n343[3]; n343_4 = n343[4]; n343_5 = n343[5]; n343_6 = n343[6];
  //   n343_7 = n343[7]; n346_0 = n346[0]; n381[7:0] = n346; n346_1 = n346[1]; n346_2 = n346[2]; n346_3 = n346[3];
  //   n346_4 = n346[4]; n346_5 = n346[5]; n346_6 = n346[6]; n346_7 = n346[7]; n349_0 = n349[0]; n383[7:0] = n349;
  //   n349_1 = n349[1]; n349_2 = n349[2]; n349_3 = n349[3]; n349_4 = n349[4]; n349_5 = n349[5]; n349_6 = n349[6];
  //   n349_7 = n349[7]; n352_0 = n352[0]; n384[7:0] = n352; n352_1 = n352[1]; n352_2 = n352[2]; n352_3 = n352[3];
  //   n352_4 = n352[4]; n352_5 = n352[5]; n352_6 = n352[6]; n352_7 = n352[7]; n355_0 = n355[0]; n386[7:0] = n355;
  //   n355_1 = n355[1]; n355_2 = n355[2]; n355_3 = n355[3]; n355_4 = n355[4]; n355_5 = n355[5]; n355_6 = n355[6];
  //   n355_7 = n355[7]; n358_0 = n358[0]; n387[7:0] = n358; n358_1 = n358[1]; n358_2 = n358[2]; n358_3 = n358[3];
  //   n358_4 = n358[4]; n358_5 = n358[5]; n358_6 = n358[6]; n358_7 = n358[7]; n361_0 = n361[0]; n389[7:0] = n361;
  //   n361_1 = n361[1]; n361_2 = n361[2]; n361_3 = n361[3]; n361_4 = n361[4]; n361_5 = n361[5]; n361_6 = n361[6];
  //   n361_7 = n361[7]; n364_0 = n364[0]; n390[7:0] = n364; n364_1 = n364[1]; n364_2 = n364[2]; n364_3 = n364[3];
  //   n364_4 = n364[4]; n364_5 = n364[5]; n364_6 = n364[6]; n364_7 = n364[7]; n367_0 = n367[0]; n392[7:0] = n367;
  //   n367_1 = n367[1]; n367_2 = n367[2]; n367_3 = n367[3]; n367_4 = n367[4]; n367_5 = n367[5]; n367_6 = n367[6];
  //   n367_7 = n367[7]; n370_0 = n370[0]; n393[7:0] = n370; n370_1 = n370[1]; n370_2 = n370[2]; n370_3 = n370[3];
  //   n370_4 = n370[4]; n370_5 = n370[5]; n370_6 = n370[6]; n370_7 = n370[7]; n373_0 = n373[0]; n395[7:0] = n373;
  //   n373_1 = n373[1]; n373_2 = n373[2]; n373_3 = n373[3]; n373_4 = n373[4]; n373_5 = n373[5]; n373_6 = n373[6];
  //   n373_7 = n373[7]; n376_0 = n376[0]; n396[7:0] = n376; n376_1 = n376[1]; n376_2 = n376[2]; n376_3 = n376[3];
  //   n376_4 = n376[4]; n376_5 = n376[5]; n376_6 = n376[6]; n376_7 = n376[7]; n379_0 = n379[0]; n398[7:0] = n379;
  //   n379_1 = n379[1]; n379_2 = n379[2]; n379_3 = n379[3]; n379_4 = n379[4]; n379_5 = n379[5]; n379_6 = n379[6];
  //   n379_7 = n379[7]; n382_0 = n382[0]; n399[7:0] = n382; n382_1 = n382[1]; n382_2 = n382[2]; n382_3 = n382[3];
  //   n382_4 = n382[4]; n382_5 = n382[5]; n382_6 = n382[6]; n382_7 = n382[7]; n385_0 = n385[0]; n401[7:0] = n385;
  //   n385_1 = n385[1]; n385_2 = n385[2]; n385_3 = n385[3]; n385_4 = n385[4]; n385_5 = n385[5]; n385_6 = n385[6];
  //   n385_7 = n385[7]; n388_0 = n388[0]; n402[7:0] = n388; n388_1 = n388[1]; n388_2 = n388[2]; n388_3 = n388[3];
  //   n388_4 = n388[4]; n388_5 = n388[5]; n388_6 = n388[6]; n388_7 = n388[7]; n391_0 = n391[0]; n404[7:0] = n391;
  //   n391_1 = n391[1]; n391_2 = n391[2]; n391_3 = n391[3]; n391_4 = n391[4]; n391_5 = n391[5]; n391_6 = n391[6];
  //   n391_7 = n391[7]; n394_0 = n394[0]; n405[7:0] = n394; n394_1 = n394[1]; n394_2 = n394[2]; n394_3 = n394[3];
  //   n394_4 = n394[4]; n394_5 = n394[5]; n394_6 = n394[6]; n394_7 = n394[7]; n400_0 = n400[0]; n407[7:0] = n400;
  //   n400_1 = n400[1]; n400_2 = n400[2]; n400_3 = n400[3]; n400_4 = n400[4]; n400_5 = n400[5]; n400_6 = n400[6];
  //   n400_7 = n400[7]; n403_0 = n403[0]; n408[7:0] = n403; n403_1 = n403[1]; n403_2 = n403[2]; n403_3 = n403[3];
  //   n403_4 = n403[4]; n403_5 = n403[5]; n403_6 = n403[6]; n403_7 = n403[7]; n406_0 = n406[0]; n410[7:0] = n406;
  //   n406_1 = n406[1]; n406_2 = n406[2]; n406_3 = n406[3]; n406_4 = n406[4]; n406_5 = n406[5]; n406_6 = n406[6];
  //   n406_7 = n406[7]; n397_0 = n397[0]; n411[7:0] = n397; n397_1 = n397[1]; n397_2 = n397[2]; n397_3 = n397[3];
  //   n397_4 = n397[4]; n397_5 = n397[5]; n397_6 = n397[6]; n397_7 = n397[7]; n409_0 = n409[0]; n413[7:0] = n409;
  //   n409_1 = n409[1]; n409_2 = n409[2]; n409_3 = n409[3]; n409_4 = n409[4]; n409_5 = n409[5]; n409_6 = n409[6];
  //   n409_7 = n409[7]; n412_0 = n412[0]; n414[7:0] = n412; n412_1 = n412[1]; n412_2 = n412[2]; n412_3 = n412[3];
  //   n412_4 = n412[4]; n412_5 = n412[5]; n412_6 = n412[6]; n412_7 = n412[7]; n523 = NextP[0]; n507 = NextP[1];
  //   n492 = NextP[2]; n495 = NextP[3]; n525 = NextP[6]; n513 = NextP[7]; P_1 = P[1]; P_2 = P[2]; P_3 = P[3];
  //   P_4 = P[4]; P_5 = P[5]; P_6 = P[6]; P_7 = P[7]; n415[7:0] = Result; n415_0 = Result[0]; n415_1 = Result[1];
  //   n415_2 = Result[2]; n415_3 = Result[3]; n415_4 = Result[4]; n415_5 = Result[5]; n415_6 = Result[6];
  //   n415_7 = Result[7]; n61[7:0] = Y; n260[7:0] = Y; n371[7:0] = Y; Y_0 = Y[0]; Y_1 = Y[1]; Y_2 = Y[2]; Y_3 = Y[3];
  //   Y_4 = Y[4]; Y_5 = Y[5]; Y_6 = Y[6]; Y_7 = Y[7]

  // Notes on the sheet:
  //   Binary add / subtract / compare
  //   Decimal nibble carry and correction
  //   Shifts, rotates, Boolean logic and increments
  //   6502 condition flags
  //   Gate-built 6502 ALU and flags: ripple add/subtract, Boolean/shift, increment, BCD corrections.
endmodule
module Cpu6502 (
  input  SysClock,
  input  Reset,
  input  [7:0] DataIn,
  input  IRQ,
  input  NMI,
  output [15:0] Address,
  output [7:0] DataOut,
  output Write,
  output Read,
  output Sync,
  output Fault,
  output [15:0] PC,
  output [7:0] A,
  output [7:0] X,
  output [7:0] Y,
  output [7:0] SP,
  output [7:0] P,
  output [7:0] IR,
  output [7:0] State
);

  wire n1, n2, n3, n4, n5, n6, n7, n8, n9, n10, n11, n12, n13, n14, n15, n16, n17, n18, n19, n20, n21, n22,
       n23, n24, n25, n26, n27, n28, n29, n30, n31, n32, n33, n34, n35, n36, n37, n38, n39, n40, n41, n42,
       n43, n44, n45, n46, n47, n48, n49, n50, n51, n52, n53, n54, n55, n56, n57, n58, n59, n60, n61, n62,
       n63, n64, n65, n66, n67, n68, n69, n70, n71, n72, n73, n74, n75, n76, n77, n78, n79, n80, n81, n82,
       n83, n84, n85, n86, n87, n88, n89, n90, n91, n92, n93, n94, n95, n96, n97, n98, n99, n100, n101, n102,
       n103, n104, n105, n106, n107, n108, n109, n110, n111, n112, n113, n114, n115, n116, n117, n118, n119,
       n120, n121, n122, n123, n124, n125, n126, n127, n128, n129, n130, n131, n132, n133, n134, n135, n136,
       n137, n138, n139, n140, n141, n142, n143, n144, n145, n146, n147, n148, n149, n150, n151, n152, n153,
       n154, n155, n156, n157, n158, n159, n160, n161, n162, n163, n164, n165, n166, n167, n168, n169, n170,
       n171, n172, n173, n174, n175, n176, n177, n178, n179, n180, n181, n182, n183, n184, n185, n186, n187,
       n188, n189, n190, n191, n192, n193, n194, n196, n197, n198, n199, n200, n201, n202, n203, n204, n205,
       n206, n207, n208, n209, n210, n211, n212, n213, n214, n215, n216, n217, n218, n219, n220, n221, n222,
       n223, n224, n225, n226, n227, n228, n229, n230, n231, n232, n233, n234, n235, n236, n237, n238, n239,
       n240, n241, n242, n243, n244, n245, n246, n247, n248, n249, n250, n251, n252, n253, n254, n255, n256,
       n257, n258, n259, n260, n261, n262, n263, n264, n265, n266, n267, n268, n269, n270, n271, n272, n273,
       n274, n275, n276, n277, n278, n279, n280, n281, n282, n283, n284, n285, n286, n287, n288, n289, n290,
       n291, n292, n293, n294, n295, n296, n297, n298, n299, n300, n301, n302, n303, n304, n305, n306, n307,
       n308, n309, n310, n311, n312, n313, n314, n315, n316, n317, n318, n319, n320, n321, n322, n323, n324,
       n325, n326, n327, n328, n329, n330, n331, n332, n333, n334, n335, n336, n337, n338, n348, n349, n350,
       n351, n352, n353, n354, n355, n356, n357, n358, n359, n360, n361, n362, n363, n364, n365, n366, n367,
       n368, n369, n370, n371, n381, n382, n383, n384, n385, n386, n387, n388, n389, n390, n391, n392, n393,
       n394, n395, n396, n397, n398, n399, n400, n401, n402, n403, n404, n405, n406, n407, n408, n409, n410,
       n411, n412, n413, n414, n415, n416, n417, n418, n419, n420, n421, n422, n423, n424, n425, n426, n427,
       n428, n429, n430, n431, n432, n433, n434, n435, n436, n437, n438, n442, n443, n444, n445, n446, n447,
       n448, n449, n450, n451, n452, n453, n454, n455, n456, n457, n458, n459, n460, n461, n462, n463, n464,
       n465, n466, n467, n468, n469, n470, n471, n472, n473, n474, n475, n476, n477, n478, n479, n480, n481,
       n482, n483, n484, n485, n486, n487, n488, n489, n490, n491, n492, n493, n494, n495, n496, n497, n498,
       n499, n500, n501, n502, n503, n504, n505, n506, n507, n508, n509, n510, n511, n512, n513, n514, n515,
       n516, n517, n518, n519, n520, n521, n522, n523, n524, n525, n526, n527, n528, n529, n530, n531, n532,
       n533, n534, n535, n536, n537, n538, n539, n540, n541, n542, n543, n544, n545, n546, n547, n548, n549,
       n550, n551, n552, n553, n554, n555, n556, n557, n558, n559, n560, n561, n562, n563, n564, n565, n566,
       n567, n568, n569, n570, n571, n572, n573, n574, n575, n576, n577, n578, n579, n580, n581, n582, n583,
       n584, n585, n586, n587, n588, n589, n590, n591, n592, n593, n594, n595, n596, n597, n598, n599, n600,
       n601, n602, n603, n604, n605, n606, n607, n608, n609, n610, n611, n612, n613, n683, n684, n685, n686,
       n687, n688, n689, n690, n748, n749, n751, n752, n753, n754, n755, n756, n757, n758, n761, n780, n781,
       n798, n799, n800, n823, n824, n825, n826, n827, n828, n829, n830, n831, n832, n901, n902, n903, n904,
       n905, n906, n907, n908, n909, n910, n911, n912, n913, n914, n915, n916, n917, n918, n919, n920, n921,
       n922, n923, n924, n925, n926, n927, n928, n929, n930, n931, n932, n933, n934, n935, n936, n937, n938,
       n939, n940, n941, n942, n943, n944, n1213, n1214, n1215, n1238, n1249, n1250, n1251, n1252, n1285,
       NmiPending, NmiPrevious;
  wire [7:0] AluFlags, AluResult, B, InterruptKind, n341, n344, n347, n374, n377, n380, n441, n693, n696,
       n699, n700, n702, n705, n708, n711, n714, n717, n720, n723, n726, n729, n732, n735, n738, n741, n744,
       n764, n767, n770, n774, n778, n784, n787, n790, n793, n796, n803, n806, n809, n812, n815, n818, n821,
       n833, n899, n947, n950, n953, n956, n959, n962, n965, n968, n971, n974, n977, n980, n983, n986, n989,
       n992, n995, n998, n1001, n1004, n1007, n1010, n1013, n1016, n1019, n1022, n1025, n1028, n1031, n1034,
       n1037, n1040, n1043, n1046, n1049, n1052, n1055, n1058, n1061, n1064, n1067, n1070, n1073, n1076,
       n1079, n1082, n1085, n1088, n1091, n1094, n1097, n1100, n1103, n1106, n1109, n1112, n1115, n1118,
       n1121, n1124, n1127, n1130, n1133, n1136, n1139, n1142, n1145, n1148, n1151, n1154, n1157, n1160,
       n1163, n1166, n1169, n1172, n1175, n1178, n1181, n1184, n1187, n1190, n1193, n1196, n1199, n1202,
       n1205, n1208, n1211, n1241, n1244, n1247, n1255, n1258, n1261, n1264, n1267, n1270, n1273, n1276,
       n1279, n1283, n1288, n1291, n1294;
  wire [12:0] AddressModes;
  wire [15:0] EA, n616, n619, n622, n625, n628, n631, n634, n637, n640, n643, n646, n649, n652, n655, n658,
       n661, n664, n667, n670, n673, n676, n679, n835, n838, n841, n844, n847, n850, n853, n856, n859, n862,
       n865, n868, n871, n874, n877, n880, n883, n886, n889, n892, n895, n1218, n1221, n1224, n1227, n1230,
       n1233, n1236;
  wire [55:0] Mnemonics;

  or or_1 (n8, n7, Mnemonics[8]);
  or or_2 (n16, n15, Mnemonics[16]);
  or or_3 (n24, n23, Mnemonics[24]);
  or or_4 (n32, n31, Mnemonics[32]);
  or or_5 (n40, n39, Mnemonics[40]);
  or or_6 (n48, n47, Mnemonics[48]);
  not not_1 (n56, State[0]);
  and and_1 (n64, n56, n57);
  and and_2 (n72, n71, n58);
  and and_3 (n80, n79, n59);
  and and_4 (n88, n87, n60);
  and and_5 (n96, n95, n62);
  and and_6 (n104, n78, State[2]);
  and and_7 (n112, n111, n60);
  and and_8 (n120, n119, n63);
  and and_9 (n128, n127, n61);
  and and_10 (n136, n92, State[3]);
  and and_11 (n144, n143, n62);
  and and_12 (n152, n151, n60);
  and and_13 (n160, n73, State[4]);
  and and_14 (n168, n87, State[4]);
  and and_15 (n176, n99, State[4]);
  and and_16 (n184, n111, State[4]);
  and and_17 (n192, n121, State[4]);
  FullAdder fulladder_1 (.A(PC[0]), .B(1'b1), .CarryIn(1'b0), .Sum(n196), .CarryOut(n197));
  FullAdder fulladder_2 (.A(PC[8]), .B(1'b0), .CarryIn(n211), .Sum(n212), .CarryOut(n213));
  FullAdder fulladder_3 (.A(SP[0]), .B(1'b1), .CarryIn(1'b0), .Sum(n228), .CarryOut(n229));
  FullAdder fulladder_4 (.A(SP[0]), .B(1'b1), .CarryIn(1'b0), .Sum(n244), .CarryOut(n245));
  FullAdder fulladder_5 (.A(PC[0]), .B(1'b1), .CarryIn(1'b0), .Sum(n260), .CarryOut(n261));
  FullAdder fulladder_6 (.A(PC[8]), .B(1'b1), .CarryIn(n275), .Sum(n276), .CarryOut(n277));
  or or_7 (n292, Mnemonics[47], Mnemonics[48]);
  and and_18 (n300, n298, n299);
  not not_2 (n301, NmiPrevious);
  and and_19 (n309, n303, n308);
  or or_8 (n317, n316, Mnemonics[41]);
  and and_20 (n325, n324, n55);
  or or_9 (n332, AddressModes[4], AddressModes[9]);
  FullAdder fulladder_7 (.A(DataIn[5]), .B(n347[5]), .CarryIn(n357), .Sum(n358), .CarryOut(n359));
  and and_21 (n369, n366, n368);
  FullAdder fulladder_8 (.A(n833[1]), .B(n380[1]), .CarryIn(n382), .Sum(n383), .CarryOut(n384));
  FullAdder fulladder_9 (.A(DataIn[1]), .B(1'b0), .CarryIn(n398), .Sum(n399), .CarryOut(n400));
  not not_3 (n414, AddressModes[6]);
  and and_22 (n422, n420, n368);
  FullAdder fulladder_10 (.A(EA[7]), .B(1'b0), .CarryIn(n436), .Sum(n437), .CarryOut(n438));
  FullAdder fulladder_11 (.A(n833[3]), .B(n441[3]), .CarryIn(n447), .Sum(n448), .CarryOut(n449));
  FullAdder fulladder_12 (.A(DataIn[3]), .B(1'b0), .CarryIn(n463), .Sum(n464), .CarryOut(n465));
  and and_23 (n477, n476, n293);
  or or_10 (n487, n486, Mnemonics[53]);
  or or_11 (n495, n494, Mnemonics[21]);
  not not_4 (n502, P[7]);
  and and_24 (n510, Mnemonics[4], P[0]);
  or or_12 (n518, n517, n510);
  FullAdder fulladder_13 (.A(PC[5]), .B(B[5]), .CarryIn(n530), .Sum(n531), .CarryOut(n532));
  FullAdder fulladder_14 (.A(PC[13]), .B(B[7]), .CarryIn(n546), .Sum(n547), .CarryOut(n548));
  or or_13 (n555, n135, n145);
  or or_14 (n563, n562, n167);
  or or_15 (n571, n570, DataIn[6]);
  FullAdder fulladder_15 (.A(n833[2]), .B(1'b0), .CarryIn(n580), .Sum(n581), .CarryOut(n582));
  FullAdder fulladder_16 (.A(DataIn[2]), .B(1'b0), .CarryIn(n596), .Sum(n597), .CarryOut(n598));
  or or_16 (n609, n84, n97);
  and and_25 (n689, n135, Mnemonics[35]);
  assign n696 = X & {8{n686}};  // AND_Gate and_26, 8 bits wide
  assign n702 = n700 & {8{n688}};  // AND_Gate and_27, 8 bits wide
  assign n708 = {P[7:6], 1'b1, n684, P[3:0]} & {8{n690}};  // AND_Gate and_28, 8 bits wide
  assign n714 = {n274, n272, n270, n268, n266, n264, n262, n260} & {8{n150}};  // AND_Gate and_29, 8 bits wide
  assign n720 = PC[7:0] & {8{n179}};  // AND_Gate and_30, 8 bits wide
  assign n726 = n699 | n702;  // OR_Gate or_17, 8 bits wide
  assign n732 = n711 | n714;  // OR_Gate or_18, 8 bits wide
  assign n738 = n723 | n726;  // OR_Gate or_19, 8 bits wide
  assign n744 = n738 | n741;  // OR_Gate or_20, 8 bits wide
  or or_21 (n749, n130, n559);
  or or_22 (n756, n755, n77);
  or or_23 (n761, n491, n565);
  assign n803 = AluFlags & {8{n125}};  // AND_Gate and_31, 8 bits wide
  assign n809 = {DataIn[7:6], 2'b10, DataIn[3:0]} & {8{n575}};  // AND_Gate and_32, 8 bits wide
  assign n815 = n803 | n806;  // OR_Gate or_24, 8 bits wide
  assign n821 = n815 | n818;  // OR_Gate or_25, 8 bits wide
  or or_26 (n827, n826, n553);
  assign n835 = {DataIn, n833} & {16{n77}};  // AND_Gate and_33, 16 bits wide
  assign n841 = {n226, n224, n222, n220, n218, n216, n214, n212, n210, n208, n206, n204, n202, n200, n198, n196} & {16{n331}};  // AND_Gate and_34, 16 bits wide
  assign n847 = {n226, n224, n222, n220, n218, n216, n214, n212, n210, n208, n206, n204, n202, n200, n198, n196} & {16{n103}};  // AND_Gate and_35, 16 bits wide
  assign n853 = EA & {16{n554}};  // AND_Gate and_36, 16 bits wide
  assign n859 = {n607, n605, n603, n601, n599, n597, n595, n593, n591, n589, n587, n585, n583, n581, n579, n577} & {16{n159}};  // AND_Gate and_37, 16 bits wide
  assign n865 = {DataIn, n833} & {16{n191}};  // AND_Gate and_38, 16 bits wide
  assign n871 = n841 | n844;  // OR_Gate or_27, 16 bits wide
  assign n877 = n853 | n856;  // OR_Gate or_28, 16 bits wide
  assign n883 = n868 | n871;  // OR_Gate or_29, 16 bits wide
  assign n889 = n880 | n865;  // OR_Gate or_30, 16 bits wide
  assign n895 = n892 | n889;  // OR_Gate or_31, 16 bits wide
  Register8R0 register8r0_1 (.Data(n899), .Enable(n310), .SysClock(SysClock), .Reset(Reset), .Q(IR));
  or or_32 (n907, n906, n326);
  or or_33 (n915, n914, n369);
  or or_34 (n923, n922, n474);
  or or_35 (n931, n930, n145);
  or or_36 (n939, n938, n175);
  assign n947 = 8'h1 & {8{n70}};  // AND_Gate and_39, 8 bits wide
  assign n953 = 8'h14 & {8{n307}};  // AND_Gate and_40, 8 bits wide
  assign n959 = 8'h19 & {8{n312}};  // AND_Gate and_41, 8 bits wide
  assign n965 = 8'h4 & {8{n325}};  // AND_Gate and_42, 8 bits wide
  assign n971 = 8'hc & {8{n328}};  // AND_Gate and_43, 8 bits wide
  assign n977 = 8'h11 & {8{n330}};  // AND_Gate and_44, 8 bits wide
  assign n983 = 8'h9 & {8{n333}};  // AND_Gate and_45, 8 bits wide
  assign n989 = 8'ha & {8{n367}};  // AND_Gate and_46, 8 bits wide
  assign n995 = 8'h6 & {8{n371}};  // AND_Gate and_47, 8 bits wide
  assign n1001 = 8'h9 & {8{n416}};  // AND_Gate and_48, 8 bits wide
  assign n1007 = 8'ha & {8{n421}};  // AND_Gate and_49, 8 bits wide
  assign n1013 = 8'h7 & {8{n109}};  // AND_Gate and_50, 8 bits wide
  assign n1019 = 8'ha & {8{n477}};  // AND_Gate and_51, 8 bits wide
  assign n1025 = 8'h9 & {8{n120}};  // AND_Gate and_52, 8 bits wide
  assign n1031 = 8'ha & {8{n479}};  // AND_Gate and_53, 8 bits wide
  assign n1037 = 8'h2 & {8{n135}};  // AND_Gate and_54, 8 bits wide
  assign n1043 = 8'h2 & {8{n150}};  // AND_Gate and_55, 8 bits wide
  assign n1049 = 8'h10 & {8{n155}};  // AND_Gate and_56, 8 bits wide
  assign n1055 = 8'h12 & {8{n163}};  // AND_Gate and_57, 8 bits wide
  assign n1061 = 8'h2 & {8{n171}};  // AND_Gate and_58, 8 bits wide
  assign n1067 = 8'h16 & {8{n179}};  // AND_Gate and_59, 8 bits wide
  assign n1073 = 8'h18 & {8{n187}};  // AND_Gate and_60, 8 bits wide
  assign n1079 = 8'h19 & {8{Fault}};  // AND_Gate and_61, 8 bits wide
  assign n1085 = n953 | n956;  // OR_Gate or_37, 8 bits wide
  assign n1091 = n965 | n968;  // OR_Gate or_38, 8 bits wide
  assign n1097 = n977 | n980;  // OR_Gate or_39, 8 bits wide
  assign n1103 = n989 | n992;  // OR_Gate or_40, 8 bits wide
  assign n1109 = n1001 | n1004;  // OR_Gate or_41, 8 bits wide
  assign n1115 = n1013 | n1016;  // OR_Gate or_42, 8 bits wide
  assign n1121 = n1025 | n1028;  // OR_Gate or_43, 8 bits wide
  assign n1127 = n1037 | n1040;  // OR_Gate or_44, 8 bits wide
  assign n1133 = n1049 | n1052;  // OR_Gate or_45, 8 bits wide
  assign n1139 = n1061 | n1064;  // OR_Gate or_46, 8 bits wide
  assign n1145 = n1073 | n1076;  // OR_Gate or_47, 8 bits wide
  assign n1151 = n1088 | n1091;  // OR_Gate or_48, 8 bits wide
  assign n1157 = n1100 | n1103;  // OR_Gate or_49, 8 bits wide
  assign n1163 = n1112 | n1115;  // OR_Gate or_50, 8 bits wide
  assign n1169 = n1124 | n1127;  // OR_Gate or_51, 8 bits wide
  assign n1175 = n1136 | n1139;  // OR_Gate or_52, 8 bits wide
  assign n1181 = n1148 | n1151;  // OR_Gate or_53, 8 bits wide
  assign n1187 = n1160 | n1163;  // OR_Gate or_54, 8 bits wide
  assign n1193 = n1172 | n1175;  // OR_Gate or_55, 8 bits wide
  assign n1199 = n1181 | n1184;  // OR_Gate or_56, 8 bits wide
  assign n1205 = n1193 | n1196;  // OR_Gate or_57, 8 bits wide
  assign n1211 = n1208 | n1205;  // OR_Gate or_58, 8 bits wide
  assign n1241 = DataIn & {8{n333}};  // AND_Gate and_62, 8 bits wide
  assign n1247 = n1241 | n1244;  // OR_Gate or_59, 8 bits wide
  assign n1283 = AluResult & {8{n479}};  // AND_Gate and_63, 8 bits wide
  or or_60 (n1, Mnemonics[0], Mnemonics[1]);
  or or_61 (n9, n8, Mnemonics[9]);
  or or_62 (n17, n16, Mnemonics[17]);
  or or_63 (n25, n24, Mnemonics[25]);
  or or_64 (n33, n32, Mnemonics[33]);
  or or_65 (n41, n40, Mnemonics[41]);
  or or_66 (n49, n48, Mnemonics[49]);
  not not_5 (n57, State[1]);
  and and_64 (n65, n64, n58);
  and and_65 (n73, n72, n59);
  and and_66 (n81, n80, n60);
  and and_67 (n89, n88, n61);
  and and_68 (n97, n96, n63);
  and and_69 (n105, n104, n59);
  and and_70 (n113, n112, n61);
  and and_71 (n121, n72, State[3]);
  and and_72 (n129, n128, n62);
  and and_73 (n137, n136, n60);
  and and_74 (n145, n144, n63);
  and and_75 (n153, n152, n61);
  and and_76 (n161, n160, n61);
  and and_77 (n169, n168, n61);
  and and_78 (n177, n176, n61);
  and and_79 (n185, n184, n61);
  and and_80 (n193, n192, n61);
  FullAdder fulladder_17 (.A(PC[1]), .B(1'b0), .CarryIn(n197), .Sum(n198), .CarryOut(n199));
  FullAdder fulladder_18 (.A(PC[9]), .B(1'b0), .CarryIn(n213), .Sum(n214), .CarryOut(n215));
  FullAdder fulladder_19 (.A(SP[1]), .B(1'b0), .CarryIn(n229), .Sum(n230), .CarryOut(n231));
  FullAdder fulladder_20 (.A(SP[1]), .B(1'b1), .CarryIn(n245), .Sum(n246), .CarryOut(n247));
  FullAdder fulladder_21 (.A(PC[1]), .B(1'b1), .CarryIn(n261), .Sum(n262), .CarryOut(n263));
  FullAdder fulladder_22 (.A(PC[9]), .B(1'b1), .CarryIn(n277), .Sum(n278), .CarryOut(n279));
  or or_67 (n293, n292, Mnemonics[49]);
  and and_81 (n302, NMI, n301);
  and and_82 (n310, n84, n308);
  or or_68 (n318, n317, Mnemonics[10]);
  and and_83 (n326, n91, n313);
  and and_84 (n333, n97, n332);
  assign n341 = X & {8{n338}};  // AND_Gate and_85, 8 bits wide
  assign n347 = n341 | n344;  // OR_Gate or_69, 8 bits wide
  FullAdder fulladder_23 (.A(DataIn[6]), .B(n347[6]), .CarryIn(n359), .Sum(n360), .CarryOut(n361));
  or or_70 (n370, AddressModes[7], AddressModes[8]);
  assign n377 = Y & {8{AddressModes[2]}};  // AND_Gate and_86, 8 bits wide
  FullAdder fulladder_24 (.A(n833[2]), .B(n380[2]), .CarryIn(n384), .Sum(n385), .CarryOut(n386));
  FullAdder fulladder_25 (.A(DataIn[2]), .B(1'b0), .CarryIn(n400), .Sum(n401), .CarryOut(n402));
  and and_87 (n415, n103, n414);
  FullAdder fulladder_26 (.A(EA[0]), .B(1'b1), .CarryIn(1'b0), .Sum(n423), .CarryOut(n424));
  FullAdder fulladder_27 (.A(n833[4]), .B(n441[4]), .CarryIn(n449), .Sum(n450), .CarryOut(n451));
  FullAdder fulladder_28 (.A(DataIn[4]), .B(1'b0), .CarryIn(n465), .Sum(n466), .CarryOut(n467));
  and and_88 (n478, n476, n368);
  or or_71 (n488, n487, Mnemonics[55]);
  and and_89 (n496, n125, n495);
  and and_90 (n503, Mnemonics[9], n502);
  not not_6 (n511, P[1]);
  or or_72 (n519, n518, n512);
  FullAdder fulladder_29 (.A(PC[6]), .B(B[6]), .CarryIn(n532), .Sum(n533), .CarryOut(n534));
  FullAdder fulladder_30 (.A(PC[14]), .B(B[7]), .CarryIn(n548), .Sum(n549), .CarryOut(n550));
  or or_73 (n556, n555, n150);
  or or_74 (n564, n563, n171);
  or or_75 (n572, n571, DataIn[7]);
  FullAdder fulladder_31 (.A(n833[3]), .B(1'b0), .CarryIn(n582), .Sum(n583), .CarryOut(n584));
  FullAdder fulladder_32 (.A(DataIn[3]), .B(1'b0), .CarryIn(n598), .Sum(n599), .CarryOut(n600));
  or or_76 (n610, n609, n103);
  or or_77 (n690, n683, n183);
  and and_91 (Write, n748, n749);
  or or_78 (n757, n756, n187);
  assign n774 = AluResult & {8{n496}};  // AND_Gate and_92, 8 bits wide
  Register8R0 register8r0_2 (.Data(n778), .Enable(n500), .SysClock(SysClock), .Reset(Reset), .Q(Y));
  Register8R253 register8r253_1 (.Data(n796), .Enable(n781), .SysClock(SysClock), .Reset(Reset), .Q(SP));
  or or_79 (n828, n827, n554);
  or or_80 (n908, n907, n328);
  or or_81 (n916, n915, n371);
  or or_82 (n924, n923, n477);
  or or_83 (n932, n931, n150);
  or or_84 (n940, n939, n179);
  assign n1218 = {{8{1'b0}}, n362, n360, n358, n356, n354, n352, n350, n348} & {16{n366}};  // AND_Gate and_93, 16 bits wide
  assign n1224 = {n411, n409, n407, n405, n403, n401, n399, n397, n395, n393, n391, n389, n387, n385, n383, n381} & {16{n103}};  // AND_Gate and_94, 16 bits wide
  assign n1230 = n1218 | n1221;  // OR_Gate or_85, 16 bits wide
  assign n1236 = n1230 | n1233;  // OR_Gate or_86, 16 bits wide
  Register8R0 register8r0_3 (.Data(n1294), .Enable(n1285), .SysClock(SysClock), .Reset(Reset), .Q(InterruptKind));
  or or_87 (n2, n1, Mnemonics[2]);
  or or_88 (n10, n9, Mnemonics[10]);
  or or_89 (n18, n17, Mnemonics[18]);
  or or_90 (n26, n25, Mnemonics[26]);
  or or_91 (n34, n33, Mnemonics[34]);
  or or_92 (n42, n41, Mnemonics[42]);
  or or_93 (n50, n49, Mnemonics[50]);
  not not_7 (n58, State[2]);
  and and_95 (n66, n65, n59);
  and and_96 (n74, n73, n60);
  and and_97 (n82, n81, n61);
  and and_98 (n90, n89, n62);
  and and_99 (n98, n71, State[2]);
  and and_100 (n106, n105, n60);
  and and_101 (n114, n113, n62);
  and and_102 (n122, n121, n60);
  and and_103 (n130, n129, n63);
  and and_104 (n138, n137, n61);
  and and_105 (n146, n104, State[3]);
  and and_106 (n154, n153, n62);
  and and_107 (n162, n161, n62);
  and and_108 (n170, n169, n62);
  and and_109 (n178, n177, n62);
  and and_110 (n186, n185, n62);
  and and_111 (n194, n193, n62);
  FullAdder fulladder_33 (.A(PC[2]), .B(1'b0), .CarryIn(n199), .Sum(n200), .CarryOut(n201));
  FullAdder fulladder_34 (.A(PC[10]), .B(1'b0), .CarryIn(n215), .Sum(n216), .CarryOut(n217));
  FullAdder fulladder_35 (.A(SP[2]), .B(1'b0), .CarryIn(n231), .Sum(n232), .CarryOut(n233));
  FullAdder fulladder_36 (.A(SP[2]), .B(1'b1), .CarryIn(n247), .Sum(n248), .CarryOut(n249));
  FullAdder fulladder_37 (.A(PC[2]), .B(1'b1), .CarryIn(n263), .Sum(n264), .CarryOut(n265));
  FullAdder fulladder_38 (.A(PC[10]), .B(1'b1), .CarryIn(n279), .Sum(n280), .CarryOut(n281));
  or or_94 (n294, Mnemonics[2], Mnemonics[32]);
  or or_95 (n303, n302, NmiPending);
  not not_8 (n311, n55);
  or or_96 (n319, AddressModes[5], AddressModes[3]);
  or or_97 (n327, Mnemonics[37], Mnemonics[38]);
  or or_98 (n334, AddressModes[0], AddressModes[1]);
  FullAdder fulladder_39 (.A(DataIn[7]), .B(n347[7]), .CarryIn(n361), .Sum(n362), .CarryOut(n363));
  and and_112 (n371, n97, n370);
  FullAdder fulladder_40 (.A(n833[3]), .B(n380[3]), .CarryIn(n386), .Sum(n387), .CarryOut(n388));
  FullAdder fulladder_41 (.A(DataIn[3]), .B(1'b0), .CarryIn(n402), .Sum(n403), .CarryOut(n404));
  and and_113 (n416, n415, Mnemonics[27]);
  FullAdder fulladder_42 (.A(EA[1]), .B(1'b0), .CarryIn(n424), .Sum(n425), .CarryOut(n426));
  FullAdder fulladder_43 (.A(n833[5]), .B(n441[5]), .CarryIn(n451), .Sum(n452), .CarryOut(n453));
  FullAdder fulladder_44 (.A(DataIn[5]), .B(1'b0), .CarryIn(n467), .Sum(n468), .CarryOut(n469));
  and and_114 (n479, n125, n300);
  Alu6502 alu6502_1 (
    .A(A), .B(B), .X(X), .Y(Y), .SP(SP), .P(P), .Mnemonics(Mnemonics), .AddressModes(AddressModes),
    .Result(AluResult), .NextP(AluFlags));
  and and_115 (n489, n296, AddressModes[3]);
  or or_99 (n497, Mnemonics[31], Mnemonics[51]);
  and and_116 (n504, Mnemonics[7], P[7]);
  and and_117 (n512, Mnemonics[8], n511);
  or or_100 (n520, n519, n513);
  FullAdder fulladder_45 (.A(PC[7]), .B(B[7]), .CarryIn(n534), .Sum(n535), .CarryOut(n536));
  FullAdder fulladder_46 (.A(PC[15]), .B(B[7]), .CarryIn(n550), .Sum(n551), .CarryOut(n552));
  or or_101 (n557, n556, n175);
  and and_118 (n565, n140, Mnemonics[37]);
  not not_9 (n573, n572);
  FullAdder fulladder_47 (.A(n833[4]), .B(1'b0), .CarryIn(n584), .Sum(n585), .CarryOut(n586));
  FullAdder fulladder_48 (.A(DataIn[4]), .B(1'b0), .CarryIn(n600), .Sum(n601), .CarryOut(n602));
  or or_102 (n611, n120, n130);
  and and_119 (n683, n135, Mnemonics[36]);
  or or_103 (n758, n757, n191);
  Register8R36 register8r36_1 (.Data(n821), .Enable(n800), .SysClock(SysClock), .Reset(Reset), .Q(P));
  or or_104 (n829, n828, n150);
  Register16R0 register16r0_1 (.Data(n895), .Enable(n832), .SysClock(SysClock), .Reset(Reset), .Q(PC));
  or or_105 (n901, n70, n77);
  or or_106 (n909, n908, n329);
  or or_107 (n917, n916, n413);
  or or_108 (n925, n924, n478);
  or or_109 (n933, n932, n140);
  or or_110 (n941, n940, n183);
  Register8R0 register8r0_4 (.Data(n1211), .Enable(n944), .SysClock(SysClock), .Reset(Reset), .Q(State));
  Register8R0 register8r0_5 (.Data(n1247), .Enable(n1238), .SysClock(SysClock), .Reset(Reset), .Q(B));
  assign n1255 = DataIn & {8{n70}};  // AND_Gate and_120, 8 bits wide
  assign n1261 = DataIn & {8{n109}};  // AND_Gate and_121, 8 bits wide
  assign n1267 = DataIn & {8{n187}};  // AND_Gate and_122, 8 bits wide
  assign n1273 = n1261 | n1264;  // OR_Gate or_111, 8 bits wide
  assign n1279 = n1276 | n1267;  // OR_Gate or_112, 8 bits wide
  Register8R0 register8r0_6 (.Data(n1283), .Enable(n479), .SysClock(SysClock), .Reset(Reset), .Q(n700));
  or or_113 (n3, n2, Mnemonics[3]);
  or or_114 (n11, n10, Mnemonics[11]);
  or or_115 (n19, n18, Mnemonics[19]);
  or or_116 (n27, n26, Mnemonics[27]);
  or or_117 (n35, n34, Mnemonics[35]);
  or or_118 (n43, n42, Mnemonics[43]);
  or or_119 (n51, n50, Mnemonics[51]);
  not not_10 (n59, State[3]);
  and and_123 (n67, n66, n60);
  and and_124 (n75, n74, n61);
  and and_125 (n83, n82, n62);
  and and_126 (n91, n90, n63);
  and and_127 (n99, n98, n59);
  and and_128 (n107, n106, n61);
  and and_129 (n115, n114, n63);
  and and_130 (n123, n122, n61);
  and and_131 (n131, n86, State[3]);
  and and_132 (n139, n138, n62);
  and and_133 (n147, n146, n60);
  and and_134 (n155, n154, n63);
  and and_135 (n163, n162, n63);
  and and_136 (n171, n170, n63);
  and and_137 (n179, n178, n63);
  and and_138 (n187, n186, n63);
  and and_139 (Fault, n194, n63);
  FullAdder fulladder_49 (.A(PC[3]), .B(1'b0), .CarryIn(n201), .Sum(n202), .CarryOut(n203));
  FullAdder fulladder_50 (.A(PC[11]), .B(1'b0), .CarryIn(n217), .Sum(n218), .CarryOut(n219));
  FullAdder fulladder_51 (.A(SP[3]), .B(1'b0), .CarryIn(n233), .Sum(n234), .CarryOut(n235));
  FullAdder fulladder_52 (.A(SP[3]), .B(1'b1), .CarryIn(n249), .Sum(n250), .CarryOut(n251));
  FullAdder fulladder_53 (.A(PC[3]), .B(1'b1), .CarryIn(n265), .Sum(n266), .CarryOut(n267));
  FullAdder fulladder_54 (.A(PC[11]), .B(1'b1), .CarryIn(n281), .Sum(n282), .CarryOut(n283));
  or or_120 (n295, n294, Mnemonics[39]);
  not not_11 (n304, P[2]);
  and and_140 (n312, n91, n311);
  not not_12 (n320, n318);
  and and_141 (n328, n91, n327);
  or or_121 (n335, n334, AddressModes[2]);
  FullAdder fulladder_55 (.A(DataIn[0]), .B(n347[0]), .CarryIn(1'b0), .Sum(n348), .CarryOut(n349));
  or or_122 (n364, AddressModes[10], AddressModes[11]);
  FullAdder fulladder_56 (.A(n833[4]), .B(n380[4]), .CarryIn(n388), .Sum(n389), .CarryOut(n390));
  FullAdder fulladder_57 (.A(DataIn[4]), .B(1'b0), .CarryIn(n404), .Sum(n405), .CarryOut(n406));
  and and_142 (n417, n103, Mnemonics[28]);
  FullAdder fulladder_58 (.A(EA[2]), .B(1'b0), .CarryIn(n426), .Sum(n427), .CarryOut(n428));
  assign n441 = Y & {8{AddressModes[8]}};  // AND_Gate and_143, 8 bits wide
  FullAdder fulladder_59 (.A(n833[6]), .B(n441[6]), .CarryIn(n453), .Sum(n454), .CarryOut(n455));
  FullAdder fulladder_60 (.A(DataIn[6]), .B(1'b0), .CarryIn(n469), .Sum(n470), .CarryOut(n471));
  not not_13 (n480, n300);
  or or_123 (n482, Mnemonics[29], Mnemonics[0]);
  or or_124 (n490, n488, n489);
  or or_125 (n498, n497, Mnemonics[26]);
  not not_14 (n505, P[6]);
  and and_144 (n513, Mnemonics[5], P[1]);
  FullAdder fulladder_61 (.A(PC[0]), .B(B[0]), .CarryIn(1'b0), .Sum(n521), .CarryOut(n522));
  FullAdder fulladder_62 (.A(PC[8]), .B(B[7]), .CarryIn(n536), .Sum(n537), .CarryOut(n538));
  and and_145 (n553, n125, n520);
  or or_126 (n558, n557, n179);
  or or_127 (n566, DataIn[0], DataIn[1]);
  and and_146 (n574, n140, Mnemonics[38]);
  FullAdder fulladder_63 (.A(n833[5]), .B(1'b0), .CarryIn(n586), .Sum(n587), .CarryOut(n588));
  FullAdder fulladder_64 (.A(DataIn[5]), .B(1'b0), .CarryIn(n602), .Sum(n603), .CarryOut(n604));
  or or_128 (n612, n611, n109);
  assign n619 = 16'hfffe & {16{n613}};  // AND_Gate and_147, 16 bits wide
  assign n625 = 16'hfffb & {16{InterruptKind[0]}};  // AND_Gate and_148, 16 bits wide
  assign n631 = n625 | n628;  // OR_Gate or_129, 16 bits wide
  assign n637 = 16'hfffd & {16{n77}};  // AND_Gate and_149, 16 bits wide
  assign n643 = EA & {16{n612}};  // AND_Gate and_150, 16 bits wide
  assign n649 = {8'h1, SP} & {16{n559}};  // AND_Gate and_151, 16 bits wide
  assign n655 = n622 & {16{n187}};  // AND_Gate and_152, 16 bits wide
  assign n661 = n634 | n637;  // OR_Gate or_130, 16 bits wide
  assign n667 = n646 | n649;  // OR_Gate or_131, 16 bits wide
  assign n673 = n661 | n664;  // OR_Gate or_132, 16 bits wide
  assign n679 = n673 | n676;  // OR_Gate or_133, 16 bits wide
  or or_134 (n684, n683, InterruptKind[1]);
  or or_135 (n751, n610, n120);
  and and_153 (Read, n748, n758);
  assign n764 = AluResult & {8{n491}};  // AND_Gate and_154, 8 bits wide
  assign n770 = n764 | n767;  // OR_Gate or_136, 8 bits wide
  Register8R0 register8r0_7 (.Data(n774), .Enable(n496), .SysClock(SysClock), .Reset(Reset), .Q(X));
  or or_137 (n780, n501, n559);
  assign n787 = {n258, n256, n254, n252, n250, n248, n246, n244} & {8{n559}};  // AND_Gate and_155, 8 bits wide
  assign n793 = n784 | n787;  // OR_Gate or_138, 8 bits wide
  or or_139 (n798, n125, n565);
  or or_140 (n830, n829, n159);
  or or_141 (n902, n901, n307);
  or or_142 (n910, n909, n330);
  or or_143 (n918, n917, n416);
  or or_144 (n926, n925, n120);
  or or_145 (n934, n933, n155);
  or or_146 (n942, n941, n187);
  Register16R0 register16r0_2 (.Data(n1236), .Enable(n1215), .SysClock(SysClock), .Reset(Reset), .Q(EA));
  assign n1291 = 8'h2 & {8{n331}};  // AND_Gate and_156, 8 bits wide
  Register1R0 register1r0_1 (.Data(NMI), .Enable(1'b1), .SysClock(SysClock), .Reset(Reset), .Q(NmiPrevious));
  or or_147 (n4, n3, Mnemonics[4]);
  or or_148 (n12, n11, Mnemonics[12]);
  or or_149 (n20, n19, Mnemonics[20]);
  or or_150 (n28, n27, Mnemonics[28]);
  or or_151 (n36, n35, Mnemonics[36]);
  or or_152 (n44, n43, Mnemonics[44]);
  or or_153 (n52, n51, Mnemonics[52]);
  not not_15 (n60, State[4]);
  and and_157 (n68, n67, n61);
  and and_158 (n76, n75, n62);
  and and_159 (n84, n83, n63);
  and and_160 (n92, n64, State[2]);
  and and_161 (n100, n99, n60);
  and and_162 (n108, n107, n62);
  and and_163 (n116, n65, State[3]);
  and and_164 (n124, n123, n62);
  and and_165 (n132, n131, n60);
  and and_166 (n140, n139, n63);
  and and_167 (n148, n147, n61);
  and and_168 (n156, n66, State[4]);
  and and_169 (n164, n80, State[4]);
  and and_170 (n172, n93, State[4]);
  and and_171 (n180, n105, State[4]);
  and and_172 (n188, n116, State[4]);
  FullAdder fulladder_65 (.A(PC[4]), .B(1'b0), .CarryIn(n203), .Sum(n204), .CarryOut(n205));
  FullAdder fulladder_66 (.A(PC[12]), .B(1'b0), .CarryIn(n219), .Sum(n220), .CarryOut(n221));
  FullAdder fulladder_67 (.A(SP[4]), .B(1'b0), .CarryIn(n235), .Sum(n236), .CarryOut(n237));
  FullAdder fulladder_68 (.A(SP[4]), .B(1'b1), .CarryIn(n251), .Sum(n252), .CarryOut(n253));
  FullAdder fulladder_69 (.A(PC[4]), .B(1'b1), .CarryIn(n267), .Sum(n268), .CarryOut(n269));
  FullAdder fulladder_70 (.A(PC[12]), .B(1'b1), .CarryIn(n283), .Sum(n284), .CarryOut(n285));
  or or_154 (n296, n295, Mnemonics[40]);
  and and_173 (n305, IRQ, n304);
  or or_155 (n313, Mnemonics[35], Mnemonics[36]);
  and and_174 (n321, n91, n319);
  and and_175 (n329, n91, Mnemonics[42]);
  or or_156 (n336, n335, AddressModes[6]);
  FullAdder fulladder_71 (.A(DataIn[1]), .B(n347[1]), .CarryIn(n349), .Sum(n350), .CarryOut(n351));
  or or_157 (n365, n364, AddressModes[12]);
  FullAdder fulladder_72 (.A(n833[5]), .B(n380[5]), .CarryIn(n390), .Sum(n391), .CarryOut(n392));
  FullAdder fulladder_73 (.A(DataIn[5]), .B(1'b0), .CarryIn(n406), .Sum(n407), .CarryOut(n408));
  or or_158 (n418, Mnemonics[27], Mnemonics[28]);
  FullAdder fulladder_74 (.A(EA[3]), .B(1'b0), .CarryIn(n428), .Sum(n429), .CarryOut(n430));
  FullAdder fulladder_75 (.A(n833[7]), .B(n441[7]), .CarryIn(n455), .Sum(n456), .CarryOut(n457));
  FullAdder fulladder_76 (.A(DataIn[7]), .B(1'b0), .CarryIn(n471), .Sum(n472), .CarryOut(n473));
  and and_176 (n481, n125, n480);
  or or_159 (n483, n482, Mnemonics[43]);
  and and_177 (n491, n125, n490);
  or or_160 (n499, n498, Mnemonics[22]);
  and and_178 (n506, Mnemonics[11], n505);
  or or_161 (n514, n503, n504);
  FullAdder fulladder_77 (.A(PC[1]), .B(B[1]), .CarryIn(n522), .Sum(n523), .CarryOut(n524));
  FullAdder fulladder_78 (.A(PC[9]), .B(B[7]), .CarryIn(n538), .Sum(n539), .CarryOut(n540));
  and and_179 (n554, n125, Mnemonics[27]);
  or or_162 (n559, n558, n183);
  or or_163 (n567, n566, DataIn[2]);
  or or_164 (n575, n574, n163);
  FullAdder fulladder_79 (.A(n833[6]), .B(1'b0), .CarryIn(n588), .Sum(n589), .CarryOut(n590));
  FullAdder fulladder_80 (.A(DataIn[6]), .B(1'b0), .CarryIn(n604), .Sum(n605), .CarryOut(n606));
  not not_16 (n613, InterruptKind[0]);
  and and_180 (n685, n130, Mnemonics[47]);
  assign n693 = A & {8{n685}};  // AND_Gate and_181, 8 bits wide
  assign n699 = Y & {8{n687}};  // AND_Gate and_182, 8 bits wide
  assign n705 = A & {8{n689}};  // AND_Gate and_183, 8 bits wide
  assign n711 = {n290, n288, n286, n284, n282, n280, n278, n276} & {8{n145}};  // AND_Gate and_184, 8 bits wide
  assign n717 = PC[15:8] & {8{n175}};  // AND_Gate and_185, 8 bits wide
  assign n723 = n693 | n696;  // OR_Gate or_165, 8 bits wide
  assign n729 = n705 | n708;  // OR_Gate or_166, 8 bits wide
  assign n735 = n717 | n720;  // OR_Gate or_167, 8 bits wide
  assign n741 = n729 | n732;  // OR_Gate or_168, 8 bits wide
  assign DataOut = n744 | n735;  // OR_Gate or_169, 8 bits wide
  or or_170 (n752, n751, n109);
  or or_171 (n781, n780, n564);
  or or_172 (n799, n798, n575);
  assign n806 = {DataIn[7], P[6:2], n573, P[0]} & {8{n565}};  // AND_Gate and_186, 8 bits wide
  assign n812 = {P[7:3], 1'b1, P[1:0]} & {8{n183}};  // AND_Gate and_187, 8 bits wide
  assign n818 = n809 | n812;  // OR_Gate or_173, 8 bits wide
  or or_174 (n823, n77, n310);
  or or_175 (n831, n830, n171);
  assign n838 = {n226, n224, n222, n220, n218, n216, n214, n212, n210, n208, n206, n204, n202, n200, n198, n196} & {16{n310}};  // AND_Gate and_188, 16 bits wide
  assign n844 = {n226, n224, n222, n220, n218, n216, n214, n212, n210, n208, n206, n204, n202, n200, n198, n196} & {16{n97}};  // AND_Gate and_189, 16 bits wide
  assign n850 = {n551, n549, n547, n545, n543, n541, n539, n537, n535, n533, n531, n529, n527, n525, n523, n521} & {16{n553}};  // AND_Gate and_190, 16 bits wide
  assign n856 = EA & {16{n150}};  // AND_Gate and_191, 16 bits wide
  assign n862 = {DataIn, n833} & {16{n171}};  // AND_Gate and_192, 16 bits wide
  assign n868 = n835 | n838;  // OR_Gate or_176, 16 bits wide
  assign n874 = n847 | n850;  // OR_Gate or_177, 16 bits wide
  assign n880 = n859 | n862;  // OR_Gate or_178, 16 bits wide
  assign n886 = n874 | n877;  // OR_Gate or_179, 16 bits wide
  assign n892 = n883 | n886;  // OR_Gate or_180, 16 bits wide
  or or_181 (n903, n902, n310);
  or or_182 (n911, n910, n331);
  or or_183 (n919, n918, n417);
  or or_184 (n927, n926, n130);
  or or_185 (n935, n934, n159);
  or or_186 (n943, n942, n191);
  assign n950 = 8'h2 & {8{n77}};  // AND_Gate and_193, 8 bits wide
  assign n956 = 8'h3 & {8{n310}};  // AND_Gate and_194, 8 bits wide
  assign n962 = 8'h9 & {8{n322}};  // AND_Gate and_195, 8 bits wide
  assign n968 = 8'hb & {8{n326}};  // AND_Gate and_196, 8 bits wide
  assign n974 = 8'hf & {8{n329}};  // AND_Gate and_197, 8 bits wide
  assign n980 = 8'h14 & {8{n331}};  // AND_Gate and_198, 8 bits wide
  assign n986 = 8'h5 & {8{n337}};  // AND_Gate and_199, 8 bits wide
  assign n992 = 8'h8 & {8{n369}};  // AND_Gate and_200, 8 bits wide
  assign n998 = 8'h6 & {8{n413}};  // AND_Gate and_201, 8 bits wide
  assign n1004 = 8'hd & {8{n417}};  // AND_Gate and_202, 8 bits wide
  assign n1010 = 8'h8 & {8{n422}};  // AND_Gate and_203, 8 bits wide
  assign n1016 = 8'h9 & {8{n474}};  // AND_Gate and_204, 8 bits wide
  assign n1022 = 8'h8 & {8{n478}};  // AND_Gate and_205, 8 bits wide
  assign n1028 = 8'h2 & {8{n130}};  // AND_Gate and_206, 8 bits wide
  assign n1034 = 8'h2 & {8{n481}};  // AND_Gate and_207, 8 bits wide
  assign n1040 = 8'he & {8{n145}};  // AND_Gate and_208, 8 bits wide
  assign n1046 = 8'h2 & {8{n140}};  // AND_Gate and_209, 8 bits wide
  assign n1052 = 8'h2 & {8{n159}};  // AND_Gate and_210, 8 bits wide
  assign n1058 = 8'h13 & {8{n167}};  // AND_Gate and_211, 8 bits wide
  assign n1064 = 8'h15 & {8{n175}};  // AND_Gate and_212, 8 bits wide
  assign n1070 = 8'h17 & {8{n183}};  // AND_Gate and_213, 8 bits wide
  assign n1076 = 8'h2 & {8{n191}};  // AND_Gate and_214, 8 bits wide
  assign n1082 = n947 | n950;  // OR_Gate or_187, 8 bits wide
  assign n1088 = n959 | n962;  // OR_Gate or_188, 8 bits wide
  assign n1094 = n971 | n974;  // OR_Gate or_189, 8 bits wide
  assign n1100 = n983 | n986;  // OR_Gate or_190, 8 bits wide
  assign n1106 = n995 | n998;  // OR_Gate or_191, 8 bits wide
  assign n1112 = n1007 | n1010;  // OR_Gate or_192, 8 bits wide
  assign n1118 = n1019 | n1022;  // OR_Gate or_193, 8 bits wide
  assign n1124 = n1031 | n1034;  // OR_Gate or_194, 8 bits wide
  assign n1130 = n1043 | n1046;  // OR_Gate or_195, 8 bits wide
  assign n1136 = n1055 | n1058;  // OR_Gate or_196, 8 bits wide
  assign n1142 = n1067 | n1070;  // OR_Gate or_197, 8 bits wide
  assign n1148 = n1082 | n1085;  // OR_Gate or_198, 8 bits wide
  assign n1154 = n1094 | n1097;  // OR_Gate or_199, 8 bits wide
  assign n1160 = n1106 | n1109;  // OR_Gate or_200, 8 bits wide
  assign n1166 = n1118 | n1121;  // OR_Gate or_201, 8 bits wide
  assign n1172 = n1130 | n1133;  // OR_Gate or_202, 8 bits wide
  assign n1178 = n1142 | n1145;  // OR_Gate or_203, 8 bits wide
  assign n1184 = n1154 | n1157;  // OR_Gate or_204, 8 bits wide
  assign n1190 = n1166 | n1169;  // OR_Gate or_205, 8 bits wide
  assign n1196 = n1178 | n1079;  // OR_Gate or_206, 8 bits wide
  assign n1202 = n1187 | n1190;  // OR_Gate or_207, 8 bits wide
  assign n1208 = n1199 | n1202;  // OR_Gate or_208, 8 bits wide
  or or_209 (n1213, n366, n371);
  assign n1244 = DataIn & {8{n120}};  // AND_Gate and_215, 8 bits wide
  or or_210 (n1249, n70, n337);
  Register8R0 register8r0_8 (.Data(n1279), .Enable(n1252), .SysClock(SysClock), .Reset(Reset), .Q(n833));
  or or_211 (n1285, n307, n331);
  or or_212 (n5, n4, Mnemonics[5]);
  or or_213 (n13, n12, Mnemonics[13]);
  or or_214 (n21, n20, Mnemonics[21]);
  or or_215 (n29, n28, Mnemonics[29]);
  or or_216 (n37, n36, Mnemonics[37]);
  or or_217 (n45, n44, Mnemonics[45]);
  or or_218 (n53, n52, Mnemonics[53]);
  not not_17 (n61, State[5]);
  and and_216 (n69, n68, n62);
  and and_217 (n77, n76, n63);
  and and_218 (n85, State[0], State[1]);
  and and_219 (n93, n92, n59);
  and and_220 (n101, n100, n61);
  and and_221 (n109, n108, n63);
  and and_222 (n117, n116, n60);
  and and_223 (n125, n124, n63);
  and and_224 (n133, n132, n61);
  and and_225 (n141, n98, State[3]);
  and and_226 (n149, n148, n62);
  and and_227 (n157, n156, n61);
  and and_228 (n165, n164, n61);
  and and_229 (n173, n172, n61);
  and and_230 (n181, n180, n61);
  and and_231 (n189, n188, n61);
  FullAdder fulladder_81 (.A(PC[5]), .B(1'b0), .CarryIn(n205), .Sum(n206), .CarryOut(n207));
  FullAdder fulladder_82 (.A(PC[13]), .B(1'b0), .CarryIn(n221), .Sum(n222), .CarryOut(n223));
  FullAdder fulladder_83 (.A(SP[5]), .B(1'b0), .CarryIn(n237), .Sum(n238), .CarryOut(n239));
  FullAdder fulladder_84 (.A(SP[5]), .B(1'b1), .CarryIn(n253), .Sum(n254), .CarryOut(n255));
  FullAdder fulladder_85 (.A(PC[5]), .B(1'b1), .CarryIn(n269), .Sum(n270), .CarryOut(n271));
  FullAdder fulladder_86 (.A(PC[13]), .B(1'b1), .CarryIn(n285), .Sum(n286), .CarryOut(n287));
  or or_219 (n297, n296, Mnemonics[24]);
  or or_220 (n306, n303, n305);
  or or_221 (n314, n313, Mnemonics[37]);
  and and_232 (n322, n321, n320);
  and and_233 (n330, n91, Mnemonics[41]);
  and and_234 (n337, n97, n336);
  assign n344 = Y & {8{AddressModes[12]}};  // AND_Gate and_235, 8 bits wide
  FullAdder fulladder_87 (.A(DataIn[2]), .B(n347[2]), .CarryIn(n351), .Sum(n352), .CarryOut(n353));
  and and_236 (n366, n97, n365);
  assign n374 = X & {8{AddressModes[1]}};  // AND_Gate and_237, 8 bits wide
  assign n380 = n374 | n377;  // OR_Gate or_222, 8 bits wide
  FullAdder fulladder_88 (.A(n833[6]), .B(n380[6]), .CarryIn(n392), .Sum(n393), .CarryOut(n394));
  FullAdder fulladder_89 (.A(DataIn[6]), .B(1'b0), .CarryIn(n408), .Sum(n409), .CarryOut(n410));
  not not_18 (n419, n418);
  FullAdder fulladder_90 (.A(EA[4]), .B(1'b0), .CarryIn(n430), .Sum(n431), .CarryOut(n432));
  FullAdder fulladder_91 (.A(n833[0]), .B(n441[0]), .CarryIn(1'b0), .Sum(n442), .CarryOut(n443));
  FullAdder fulladder_92 (.A(DataIn[0]), .B(1'b0), .CarryIn(n457), .Sum(n458), .CarryOut(n459));
  and and_238 (n474, n115, Mnemonics[27]);
  or or_223 (n484, n483, Mnemonics[1]);
  or or_224 (n492, Mnemonics[30], Mnemonics[50]);
  and and_239 (n500, n125, n499);
  and and_240 (n507, Mnemonics[12], P[6]);
  or or_225 (n515, n514, n506);
  FullAdder fulladder_93 (.A(PC[2]), .B(B[2]), .CarryIn(n524), .Sum(n525), .CarryOut(n526));
  FullAdder fulladder_94 (.A(PC[10]), .B(B[7]), .CarryIn(n540), .Sum(n541), .CarryOut(n542));
  or or_226 (n560, n140, n155);
  or or_227 (n568, n567, DataIn[3]);
  or or_228 (n576, n155, n167);
  FullAdder fulladder_95 (.A(n833[7]), .B(1'b0), .CarryIn(n590), .Sum(n591), .CarryOut(n592));
  FullAdder fulladder_96 (.A(DataIn[7]), .B(1'b0), .CarryIn(n606), .Sum(n607), .CarryOut(n608));
  and and_241 (n686, n130, Mnemonics[48]);
  or or_229 (n753, n752, n115);
  and and_242 (Sync, n748, n84);
  Register8R0 register8r0_9 (.Data(n770), .Enable(n761), .SysClock(SysClock), .Reset(Reset), .Q(A));
  or or_230 (n800, n799, n183);
  or or_231 (n824, n823, n331);
  or or_232 (n832, n831, n191);
  or or_233 (n904, n903, n312);
  or or_234 (n912, n911, n333);
  or or_235 (n920, n919, n421);
  or or_236 (n928, n927, n479);
  or or_237 (n936, n935, n163);
  or or_238 (n944, n943, Fault);
  or or_239 (n1214, n1213, n103);
  assign n1221 = {{8{1'b0}}, n362, n360, n358, n356, n354, n352, n350, n348} & {16{n371}};  // AND_Gate and_243, 16 bits wide
  assign n1227 = {n472, n470, n468, n466, n464, n462, n460, n458, n456, n454, n452, n450, n448, n446, n444, n442} & {16{n115}};  // AND_Gate and_244, 16 bits wide
  assign n1233 = n1224 | n1227;  // OR_Gate or_240, 16 bits wide
  or or_241 (n1238, n333, n120);
  or or_242 (n1250, n1249, n109);
  Register1R0 register1r0_2 (.Data(n309), .Enable(1'b1), .SysClock(SysClock), .Reset(Reset), .Q(NmiPending));
  InstructionDecode instructiondecode_1 (.IR(IR), .Mnemonics(Mnemonics), .AddressModes(AddressModes));
  or or_243 (n6, n5, Mnemonics[6]);
  or or_244 (n14, n13, Mnemonics[14]);
  or or_245 (n22, n21, Mnemonics[22]);
  or or_246 (n30, n29, Mnemonics[30]);
  or or_247 (n38, n37, Mnemonics[38]);
  or or_248 (n46, n45, Mnemonics[46]);
  or or_249 (n54, n53, Mnemonics[54]);
  not not_19 (n62, State[6]);
  and and_245 (n70, n69, n63);
  and and_246 (n78, n56, State[1]);
  and and_247 (n86, n85, n58);
  and and_248 (n94, n93, n60);
  and and_249 (n102, n101, n62);
  and and_250 (n110, n85, State[2]);
  and and_251 (n118, n117, n61);
  and and_252 (n126, n79, State[3]);
  and and_253 (n134, n133, n62);
  and and_254 (n142, n141, n60);
  and and_255 (n150, n149, n63);
  and and_256 (n158, n157, n62);
  and and_257 (n166, n165, n62);
  and and_258 (n174, n173, n62);
  and and_259 (n182, n181, n62);
  and and_260 (n190, n189, n62);
  FullAdder fulladder_97 (.A(PC[6]), .B(1'b0), .CarryIn(n207), .Sum(n208), .CarryOut(n209));
  FullAdder fulladder_98 (.A(PC[14]), .B(1'b0), .CarryIn(n223), .Sum(n224), .CarryOut(n225));
  FullAdder fulladder_99 (.A(SP[6]), .B(1'b0), .CarryIn(n239), .Sum(n240), .CarryOut(n241));
  FullAdder fulladder_100 (.A(SP[6]), .B(1'b1), .CarryIn(n255), .Sum(n256), .CarryOut(n257));
  FullAdder fulladder_101 (.A(PC[6]), .B(1'b1), .CarryIn(n271), .Sum(n272), .CarryOut(n273));
  FullAdder fulladder_102 (.A(PC[14]), .B(1'b1), .CarryIn(n287), .Sum(n288), .CarryOut(n289));
  or or_250 (n298, n297, Mnemonics[20]);
  and and_261 (n307, n84, n306);
  or or_251 (n315, n314, Mnemonics[38]);
  not not_20 (n323, n319);
  and and_262 (n331, n91, Mnemonics[10]);
  or or_252 (n338, AddressModes[11], AddressModes[7]);
  FullAdder fulladder_103 (.A(DataIn[3]), .B(n347[3]), .CarryIn(n353), .Sum(n354), .CarryOut(n355));
  and and_263 (n367, n366, n293);
  FullAdder fulladder_104 (.A(n833[7]), .B(n380[7]), .CarryIn(n394), .Sum(n395), .CarryOut(n396));
  FullAdder fulladder_105 (.A(DataIn[7]), .B(1'b0), .CarryIn(n410), .Sum(n411), .CarryOut(n412));
  and and_264 (n420, n415, n419);
  FullAdder fulladder_106 (.A(EA[5]), .B(1'b0), .CarryIn(n432), .Sum(n433), .CarryOut(n434));
  FullAdder fulladder_107 (.A(n833[1]), .B(n441[1]), .CarryIn(n443), .Sum(n444), .CarryOut(n445));
  FullAdder fulladder_108 (.A(DataIn[1]), .B(1'b0), .CarryIn(n459), .Sum(n460), .CarryOut(n461));
  not not_21 (n475, Mnemonics[27]);
  or or_253 (n485, n484, Mnemonics[34]);
  or or_254 (n493, n492, Mnemonics[52]);
  and and_265 (n501, n125, Mnemonics[54]);
  not not_22 (n508, P[0]);
  or or_255 (n516, n515, n507);
  FullAdder fulladder_109 (.A(PC[3]), .B(B[3]), .CarryIn(n526), .Sum(n527), .CarryOut(n528));
  FullAdder fulladder_110 (.A(PC[11]), .B(B[7]), .CarryIn(n542), .Sum(n543), .CarryOut(n544));
  or or_256 (n561, n560, n159);
  or or_257 (n569, n568, DataIn[4]);
  FullAdder fulladder_111 (.A(n833[0]), .B(1'b1), .CarryIn(1'b0), .Sum(n577), .CarryOut(n578));
  FullAdder fulladder_112 (.A(DataIn[0]), .B(1'b0), .CarryIn(n592), .Sum(n593), .CarryOut(n594));
  and and_266 (n687, n130, Mnemonics[49]);
  or or_258 (n754, n753, n564);
  or or_259 (n825, n824, n97);
  assign n899 = DataIn & {8{n310}};  // AND_Gate and_267, 8 bits wide
  or or_260 (n905, n904, n322);
  or or_261 (n913, n912, n337);
  or or_262 (n921, n920, n422);
  or or_263 (n929, n928, n481);
  or or_264 (n937, n936, n167);
  or or_265 (n1215, n1214, n115);
  or or_266 (n1251, n1250, n576);
  assign n1258 = DataIn & {8{n337}};  // AND_Gate and_268, 8 bits wide
  assign n1264 = DataIn & {8{n576}};  // AND_Gate and_269, 8 bits wide
  assign n1270 = n1255 | n1258;  // OR_Gate or_267, 8 bits wide
  assign n1276 = n1270 | n1273;  // OR_Gate or_268, 8 bits wide
  or or_269 (n7, n6, Mnemonics[7]);
  or or_270 (n15, n14, Mnemonics[15]);
  or or_271 (n23, n22, Mnemonics[23]);
  or or_272 (n31, n30, Mnemonics[31]);
  or or_273 (n39, n38, Mnemonics[39]);
  or or_274 (n47, n46, Mnemonics[47]);
  or or_275 (n55, n54, Mnemonics[55]);
  not not_23 (n63, State[7]);
  and and_270 (n71, State[0], n57);
  and and_271 (n79, n78, n58);
  and and_272 (n87, n86, n59);
  and and_273 (n95, n94, n61);
  and and_274 (n103, n102, n63);
  and and_275 (n111, n110, n59);
  and and_276 (n119, n118, n62);
  and and_277 (n127, n126, n60);
  and and_278 (n135, n134, n63);
  and and_279 (n143, n142, n61);
  and and_280 (n151, n110, State[3]);
  and and_281 (n159, n158, n63);
  and and_282 (n167, n166, n63);
  and and_283 (n175, n174, n63);
  and and_284 (n183, n182, n63);
  and and_285 (n191, n190, n63);
  FullAdder fulladder_113 (.A(PC[7]), .B(1'b0), .CarryIn(n209), .Sum(n210), .CarryOut(n211));
  FullAdder fulladder_114 (.A(PC[15]), .B(1'b0), .CarryIn(n225), .Sum(n226), .CarryOut(n227));
  FullAdder fulladder_115 (.A(SP[7]), .B(1'b0), .CarryIn(n241), .Sum(n242), .CarryOut(n243));
  FullAdder fulladder_116 (.A(SP[7]), .B(1'b1), .CarryIn(n257), .Sum(n258), .CarryOut(n259));
  FullAdder fulladder_117 (.A(PC[7]), .B(1'b1), .CarryIn(n273), .Sum(n274), .CarryOut(n275));
  FullAdder fulladder_118 (.A(PC[15]), .B(1'b1), .CarryIn(n289), .Sum(n290), .CarryOut(n291));
  not not_24 (n299, AddressModes[3]);
  not not_25 (n308, n307);
  or or_276 (n316, n315, Mnemonics[42]);
  and and_286 (n324, n91, n323);
  FullAdder fulladder_119 (.A(DataIn[4]), .B(n347[4]), .CarryIn(n355), .Sum(n356), .CarryOut(n357));
  not not_26 (n368, n293);
  FullAdder fulladder_120 (.A(n833[0]), .B(n380[0]), .CarryIn(1'b0), .Sum(n381), .CarryOut(n382));
  FullAdder fulladder_121 (.A(DataIn[0]), .B(1'b0), .CarryIn(n396), .Sum(n397), .CarryOut(n398));
  and and_287 (n413, n103, AddressModes[6]);
  and and_288 (n421, n420, n293);
  FullAdder fulladder_122 (.A(EA[6]), .B(1'b0), .CarryIn(n434), .Sum(n435), .CarryOut(n436));
  FullAdder fulladder_123 (.A(n833[2]), .B(n441[2]), .CarryIn(n445), .Sum(n446), .CarryOut(n447));
  FullAdder fulladder_124 (.A(DataIn[2]), .B(1'b0), .CarryIn(n461), .Sum(n462), .CarryOut(n463));
  and and_289 (n476, n115, n475);
  or or_277 (n486, n485, Mnemonics[23]);
  or or_278 (n494, n493, Mnemonics[25]);
  and and_290 (n509, Mnemonics[3], n508);
  or or_279 (n517, n516, n509);
  FullAdder fulladder_125 (.A(PC[4]), .B(B[4]), .CarryIn(n528), .Sum(n529), .CarryOut(n530));
  FullAdder fulladder_126 (.A(PC[12]), .B(B[7]), .CarryIn(n544), .Sum(n545), .CarryOut(n546));
  or or_280 (n562, n561, n163);
  or or_281 (n570, n569, DataIn[5]);
  FullAdder fulladder_127 (.A(n833[1]), .B(1'b0), .CarryIn(n578), .Sum(n579), .CarryOut(n580));
  FullAdder fulladder_128 (.A(DataIn[1]), .B(1'b0), .CarryIn(n594), .Sum(n595), .CarryOut(n596));
  assign n616 = 16'hfffa & {16{InterruptKind[0]}};  // AND_Gate and_291, 16 bits wide
  assign n622 = n616 | n619;  // OR_Gate or_282, 16 bits wide
  assign n628 = {16{1'b1}} & {16{n613}};  // AND_Gate and_292, 16 bits wide
  assign n634 = 16'hfffc & {16{n70}};  // AND_Gate and_293, 16 bits wide
  assign n640 = PC & {16{n610}};  // AND_Gate and_294, 16 bits wide
  assign n646 = {EA[15:8], n437, n435, n433, n431, n429, n427, n425, n423} & {16{n115}};  // AND_Gate and_295, 16 bits wide
  assign n652 = {8'h1, n242, n240, n238, n236, n234, n232, n230, n228} & {16{n564}};  // AND_Gate and_296, 16 bits wide
  assign n658 = n631 & {16{n191}};  // AND_Gate and_297, 16 bits wide
  assign n664 = n640 | n643;  // OR_Gate or_283, 16 bits wide
  assign n670 = n652 | n655;  // OR_Gate or_284, 16 bits wide
  assign n676 = n667 | n670;  // OR_Gate or_285, 16 bits wide
  assign Address = n679 | n658;  // OR_Gate or_286, 16 bits wide
  and and_298 (n688, n130, n300);
  not not_27 (n748, Reset);
  or or_287 (n755, n754, n70);
  assign n767 = DataIn & {8{n565}};  // AND_Gate and_299, 8 bits wide
  assign n778 = AluResult & {8{n500}};  // AND_Gate and_300, 8 bits wide
  assign n784 = X & {8{n501}};  // AND_Gate and_301, 8 bits wide
  assign n790 = {n242, n240, n238, n236, n234, n232, n230, n228} & {8{n564}};  // AND_Gate and_302, 8 bits wide
  assign n796 = n793 | n790;  // OR_Gate or_288, 8 bits wide
  or or_289 (n826, n825, n103);
  or or_290 (n906, n905, n325);
  or or_291 (n914, n913, n367);
  or or_292 (n922, n921, n109);
  or or_293 (n930, n929, n135);
  or or_294 (n938, n937, n171);
  or or_295 (n1252, n1251, n187);
  assign n1288 = {{7{1'b0}}, n303} & {8{n307}};  // AND_Gate and_303, 8 bits wide
  assign n1294 = n1288 | n1291;  // OR_Gate or_296, 8 bits wide

  // Other names for the same wires on the sheet: n682[15:0] = Address; n682_0 = Address[0]; n682_1 = Address[1];
  //   n682_2 = Address[2]; n682_3 = Address[3]; n682_4 = Address[4]; n682_5 = Address[5]; n682_6 = Address[6];
  //   n682_7 = Address[7]; n682_8 = Address[8]; n682_9 = Address[9]; n682_10 = Address[10]; n682_11 = Address[11];
  //   n682_12 = Address[12]; n682_13 = Address[13]; n682_14 = Address[14]; n682_15 = Address[15];
  //   AddressModes_0 = AddressModes[0]; AddressModes_3 = AddressModes[3]; AddressModes_4 = AddressModes[4];
  //   AddressModes_5 = AddressModes[5]; AddressModes_6 = AddressModes[6]; AddressModes_7 = AddressModes[7];
  //   AddressModes_9 = AddressModes[9]; AddressModes_10 = AddressModes[10]; AddressModes_11 = AddressModes[11];
  //   B_0 = B[0]; B_1 = B[1]; B_2 = B[2]; B_3 = B[3]; B_4 = B[4]; B_5 = B[5]; B_6 = B[6]; B_7 = B[7];
  //   n747[7:0] = DataOut; n747_0 = DataOut[0]; n747_1 = DataOut[1]; n747_2 = DataOut[2]; n747_3 = DataOut[3];
  //   n747_4 = DataOut[4]; n747_5 = DataOut[5]; n747_6 = DataOut[6]; n747_7 = DataOut[7];
  //   InterruptKind_1 = InterruptKind[1]; InterruptKind_2 = InterruptKind[2]; InterruptKind_3 = InterruptKind[3];
  //   InterruptKind_4 = InterruptKind[4]; InterruptKind_5 = InterruptKind[5]; InterruptKind_6 = InterruptKind[6];
  //   InterruptKind_7 = InterruptKind[7]; IR_0 = IR[0]; IR_1 = IR[1]; IR_2 = IR[2]; IR_3 = IR[3]; IR_4 = IR[4];
  //   IR_5 = IR[5]; IR_6 = IR[6]; IR_7 = IR[7]; Mnemonics_0 = Mnemonics[0]; Mnemonics_1 = Mnemonics[1];
  //   Mnemonics_2 = Mnemonics[2]; Mnemonics_3 = Mnemonics[3]; Mnemonics_4 = Mnemonics[4]; Mnemonics_5 = Mnemonics[5];
  //   Mnemonics_6 = Mnemonics[6]; Mnemonics_7 = Mnemonics[7]; Mnemonics_8 = Mnemonics[8]; Mnemonics_9 = Mnemonics[9];
  //   Mnemonics_10 = Mnemonics[10]; Mnemonics_11 = Mnemonics[11]; Mnemonics_12 = Mnemonics[12];
  //   Mnemonics_13 = Mnemonics[13]; Mnemonics_14 = Mnemonics[14]; Mnemonics_15 = Mnemonics[15];
  //   Mnemonics_16 = Mnemonics[16]; Mnemonics_17 = Mnemonics[17]; Mnemonics_18 = Mnemonics[18];
  //   Mnemonics_19 = Mnemonics[19]; Mnemonics_20 = Mnemonics[20]; Mnemonics_21 = Mnemonics[21];
  //   Mnemonics_22 = Mnemonics[22]; Mnemonics_23 = Mnemonics[23]; Mnemonics_24 = Mnemonics[24];
  //   Mnemonics_25 = Mnemonics[25]; Mnemonics_26 = Mnemonics[26]; Mnemonics_27 = Mnemonics[27];
  //   Mnemonics_28 = Mnemonics[28]; Mnemonics_29 = Mnemonics[29]; Mnemonics_30 = Mnemonics[30];
  //   Mnemonics_31 = Mnemonics[31]; Mnemonics_32 = Mnemonics[32]; Mnemonics_33 = Mnemonics[33];
  //   Mnemonics_34 = Mnemonics[34]; Mnemonics_35 = Mnemonics[35]; Mnemonics_36 = Mnemonics[36];
  //   Mnemonics_37 = Mnemonics[37]; Mnemonics_38 = Mnemonics[38]; Mnemonics_39 = Mnemonics[39];
  //   Mnemonics_40 = Mnemonics[40]; Mnemonics_41 = Mnemonics[41]; Mnemonics_42 = Mnemonics[42];
  //   Mnemonics_43 = Mnemonics[43]; Mnemonics_44 = Mnemonics[44]; Mnemonics_45 = Mnemonics[45];
  //   Mnemonics_46 = Mnemonics[46]; Mnemonics_47 = Mnemonics[47]; Mnemonics_48 = Mnemonics[48];
  //   Mnemonics_49 = Mnemonics[49]; Mnemonics_50 = Mnemonics[50]; Mnemonics_51 = Mnemonics[51];
  //   Mnemonics_52 = Mnemonics[52]; Mnemonics_53 = Mnemonics[53]; Mnemonics_54 = Mnemonics[54];
  //   Mnemonics_55 = Mnemonics[55]; n1297 = n309; n339[7:0] = X; n372[7:0] = X; n694[7:0] = X; n782[7:0] = X;
  //   X_0 = X[0]; X_1 = X[1]; X_2 = X[2]; X_3 = X[3]; X_4 = X[4]; X_5 = X[5]; X_6 = X[6]; X_7 = X[7];
  //   n340[7:0] = {8{n338}}; AddressModes_12 = AddressModes[12]; n343[7:0] = {8{AddressModes[12]}}; n344_0 = n344[0];
  //   n346[7:0] = n344; n344_1 = n344[1]; n344_2 = n344[2]; n344_3 = n344[3]; n344_4 = n344[4]; n344_5 = n344[5];
  //   n344_6 = n344[6]; n344_7 = n344[7]; n341_0 = n341[0]; n345[7:0] = n341; n341_1 = n341[1]; n341_2 = n341[2];
  //   n341_3 = n341[3]; n341_4 = n341[4]; n341_5 = n341[5]; n341_6 = n341[6]; n341_7 = n341[7]; n347_0 = n347[0];
  //   n347_1 = n347[1]; n347_2 = n347[2]; n347_3 = n347[3]; n347_4 = n347[4]; n347_5 = n347[5]; n347_6 = n347[6];
  //   n347_7 = n347[7]; AddressModes_1 = AddressModes[1]; n373[7:0] = {8{AddressModes[1]}}; n374_0 = n374[0];
  //   n378[7:0] = n374; n374_1 = n374[1]; n374_2 = n374[2]; n374_3 = n374[3]; n374_4 = n374[4]; n374_5 = n374[5];
  //   n374_6 = n374[6]; n374_7 = n374[7]; n342[7:0] = Y; n375[7:0] = Y; n439[7:0] = Y; n697[7:0] = Y; Y_0 = Y[0];
  //   Y_1 = Y[1]; Y_2 = Y[2]; Y_3 = Y[3]; Y_4 = Y[4]; Y_5 = Y[5]; Y_6 = Y[6]; Y_7 = Y[7];
  //   AddressModes_2 = AddressModes[2]; n376[7:0] = {8{AddressModes[2]}}; n377_0 = n377[0]; n379[7:0] = n377;
  //   n377_1 = n377[1]; n377_2 = n377[2]; n377_3 = n377[3]; n377_4 = n377[4]; n377_5 = n377[5]; n377_6 = n377[6];
  //   n377_7 = n377[7]; n380_0 = n380[0]; n380_1 = n380[1]; n380_2 = n380[2]; n380_3 = n380[3]; n380_4 = n380[4];
  //   n380_5 = n380[5]; n380_6 = n380[6]; n380_7 = n380[7]; AddressModes_8 = AddressModes[8];
  //   n440[7:0] = {8{AddressModes[8]}}; n441_0 = n441[0]; n441_1 = n441[1]; n441_2 = n441[2]; n441_3 = n441[3];
  //   n441_4 = n441[4]; n441_5 = n441[5]; n441_6 = n441[6]; n441_7 = n441[7]; InterruptKind_0 = InterruptKind[0];
  //   n615[15:0] = {16{InterruptKind[0]}}; n624[15:0] = {16{InterruptKind[0]}}; n616_0 = n616[0]; n620[15:0] = n616;
  //   n616_1 = n616[1]; n616_2 = n616[2]; n616_3 = n616[3]; n616_4 = n616[4]; n616_5 = n616[5]; n616_6 = n616[6];
  //   n616_7 = n616[7]; n616_8 = n616[8]; n616_9 = n616[9]; n616_10 = n616[10]; n616_11 = n616[11];
  //   n616_12 = n616[12]; n616_13 = n616[13]; n616_14 = n616[14]; n616_15 = n616[15]; n619_0 = n619[0];
  //   n621[15:0] = n619; n619_1 = n619[1]; n619_2 = n619[2]; n619_3 = n619[3]; n619_4 = n619[4]; n619_5 = n619[5];
  //   n619_6 = n619[6]; n619_7 = n619[7]; n619_8 = n619[8]; n619_9 = n619[9]; n619_10 = n619[10]; n619_11 = n619[11];
  //   n619_12 = n619[12]; n619_13 = n619[13]; n619_14 = n619[14]; n619_15 = n619[15]; n625_0 = n625[0];
  //   n629[15:0] = n625; n625_1 = n625[1]; n625_2 = n625[2]; n625_3 = n625[3]; n625_4 = n625[4]; n625_5 = n625[5];
  //   n625_6 = n625[6]; n625_7 = n625[7]; n625_8 = n625[8]; n625_9 = n625[9]; n625_10 = n625[10]; n625_11 = n625[11];
  //   n625_12 = n625[12]; n625_13 = n625[13]; n625_14 = n625[14]; n625_15 = n625[15]; n618[15:0] = {16{n613}};
  //   n627[15:0] = {16{n613}}; n628_0 = n628[0]; n630[15:0] = n628; n628_1 = n628[1]; n628_2 = n628[2];
  //   n628_3 = n628[3]; n628_4 = n628[4]; n628_5 = n628[5]; n628_6 = n628[6]; n628_7 = n628[7]; n628_8 = n628[8];
  //   n628_9 = n628[9]; n628_10 = n628[10]; n628_11 = n628[11]; n628_12 = n628[12]; n628_13 = n628[13];
  //   n628_14 = n628[14]; n628_15 = n628[15]; n637_0 = n637[0]; n660[15:0] = n637; n637_1 = n637[1]; n637_2 = n637[2];
  //   n637_3 = n637[3]; n637_4 = n637[4]; n637_5 = n637[5]; n637_6 = n637[6]; n637_7 = n637[7]; n637_8 = n637[8];
  //   n637_9 = n637[9]; n637_10 = n637[10]; n637_11 = n637[11]; n637_12 = n637[12]; n637_13 = n637[13];
  //   n637_14 = n637[14]; n637_15 = n637[15]; n638[15:0] = PC; n715[7:0] = PC[15:8]; PC_8 = PC[8]; PC_9 = PC[9];
  //   PC_10 = PC[10]; PC_11 = PC[11]; PC_12 = PC[12]; PC_13 = PC[13]; PC_14 = PC[14]; PC_15 = PC[15];
  //   n639[15:0] = {16{n610}}; n642[15:0] = {16{n612}};
  //   n644[15:0] = {EA[15:8], n437, n435, n433, n431, n429, n427, n425, n423}; n645[15:0] = {16{n115}};
  //   n1226[15:0] = {16{n115}}; n649_0 = n649[0]; n666[15:0] = n649; n649_1 = n649[1]; n649_2 = n649[2];
  //   n649_3 = n649[3]; n649_4 = n649[4]; n649_5 = n649[5]; n649_6 = n649[6]; n649_7 = n649[7]; n649_8 = n649[8];
  //   n649_9 = n649[9]; n649_10 = n649[10]; n649_11 = n649[11]; n649_12 = n649[12]; n649_13 = n649[13];
  //   n649_14 = n649[14]; n649_15 = n649[15]; n622_0 = n622[0]; n653[15:0] = n622; n622_1 = n622[1]; n622_2 = n622[2];
  //   n622_3 = n622[3]; n622_4 = n622[4]; n622_5 = n622[5]; n622_6 = n622[6]; n622_7 = n622[7]; n622_8 = n622[8];
  //   n622_9 = n622[9]; n622_10 = n622[10]; n622_11 = n622[11]; n622_12 = n622[12]; n622_13 = n622[13];
  //   n622_14 = n622[14]; n622_15 = n622[15]; n631_0 = n631[0]; n656[15:0] = n631; n631_1 = n631[1]; n631_2 = n631[2];
  //   n631_3 = n631[3]; n631_4 = n631[4]; n631_5 = n631[5]; n631_6 = n631[6]; n631_7 = n631[7]; n631_8 = n631[8];
  //   n631_9 = n631[9]; n631_10 = n631[10]; n631_11 = n631[11]; n631_12 = n631[12]; n631_13 = n631[13];
  //   n631_14 = n631[14]; n631_15 = n631[15]; n634_0 = n634[0]; n659[15:0] = n634; n634_1 = n634[1]; n634_2 = n634[2];
  //   n634_3 = n634[3]; n634_4 = n634[4]; n634_5 = n634[5]; n634_6 = n634[6]; n634_7 = n634[7]; n634_8 = n634[8];
  //   n634_9 = n634[9]; n634_10 = n634[10]; n634_11 = n634[11]; n634_12 = n634[12]; n634_13 = n634[13];
  //   n634_14 = n634[14]; n634_15 = n634[15]; n661_0 = n661[0]; n671[15:0] = n661; n661_1 = n661[1]; n661_2 = n661[2];
  //   n661_3 = n661[3]; n661_4 = n661[4]; n661_5 = n661[5]; n661_6 = n661[6]; n661_7 = n661[7]; n661_8 = n661[8];
  //   n661_9 = n661[9]; n661_10 = n661[10]; n661_11 = n661[11]; n661_12 = n661[12]; n661_13 = n661[13];
  //   n661_14 = n661[14]; n661_15 = n661[15]; n640_0 = n640[0]; n662[15:0] = n640; n640_1 = n640[1]; n640_2 = n640[2];
  //   n640_3 = n640[3]; n640_4 = n640[4]; n640_5 = n640[5]; n640_6 = n640[6]; n640_7 = n640[7]; n640_8 = n640[8];
  //   n640_9 = n640[9]; n640_10 = n640[10]; n640_11 = n640[11]; n640_12 = n640[12]; n640_13 = n640[13];
  //   n640_14 = n640[14]; n640_15 = n640[15]; n643_0 = n643[0]; n663[15:0] = n643; n643_1 = n643[1]; n643_2 = n643[2];
  //   n643_3 = n643[3]; n643_4 = n643[4]; n643_5 = n643[5]; n643_6 = n643[6]; n643_7 = n643[7]; n643_8 = n643[8];
  //   n643_9 = n643[9]; n643_10 = n643[10]; n643_11 = n643[11]; n643_12 = n643[12]; n643_13 = n643[13];
  //   n643_14 = n643[14]; n643_15 = n643[15]; n646_0 = n646[0]; n665[15:0] = n646; n646_1 = n646[1]; n646_2 = n646[2];
  //   n646_3 = n646[3]; n646_4 = n646[4]; n646_5 = n646[5]; n646_6 = n646[6]; n646_7 = n646[7]; n646_8 = n646[8];
  //   n646_9 = n646[9]; n646_10 = n646[10]; n646_11 = n646[11]; n646_12 = n646[12]; n646_13 = n646[13];
  //   n646_14 = n646[14]; n646_15 = n646[15]; n652_0 = n652[0]; n668[15:0] = n652; n652_1 = n652[1]; n652_2 = n652[2];
  //   n652_3 = n652[3]; n652_4 = n652[4]; n652_5 = n652[5]; n652_6 = n652[6]; n652_7 = n652[7]; n652_8 = n652[8];
  //   n652_9 = n652[9]; n652_10 = n652[10]; n652_11 = n652[11]; n652_12 = n652[12]; n652_13 = n652[13];
  //   n652_14 = n652[14]; n652_15 = n652[15]; n655_0 = n655[0]; n669[15:0] = n655; n655_1 = n655[1]; n655_2 = n655[2];
  //   n655_3 = n655[3]; n655_4 = n655[4]; n655_5 = n655[5]; n655_6 = n655[6]; n655_7 = n655[7]; n655_8 = n655[8];
  //   n655_9 = n655[9]; n655_10 = n655[10]; n655_11 = n655[11]; n655_12 = n655[12]; n655_13 = n655[13];
  //   n655_14 = n655[14]; n655_15 = n655[15]; n664_0 = n664[0]; n672[15:0] = n664; n664_1 = n664[1]; n664_2 = n664[2];
  //   n664_3 = n664[3]; n664_4 = n664[4]; n664_5 = n664[5]; n664_6 = n664[6]; n664_7 = n664[7]; n664_8 = n664[8];
  //   n664_9 = n664[9]; n664_10 = n664[10]; n664_11 = n664[11]; n664_12 = n664[12]; n664_13 = n664[13];
  //   n664_14 = n664[14]; n664_15 = n664[15]; n673_0 = n673[0]; n677[15:0] = n673; n673_1 = n673[1]; n673_2 = n673[2];
  //   n673_3 = n673[3]; n673_4 = n673[4]; n673_5 = n673[5]; n673_6 = n673[6]; n673_7 = n673[7]; n673_8 = n673[8];
  //   n673_9 = n673[9]; n673_10 = n673[10]; n673_11 = n673[11]; n673_12 = n673[12]; n673_13 = n673[13];
  //   n673_14 = n673[14]; n673_15 = n673[15]; n667_0 = n667[0]; n674[15:0] = n667; n667_1 = n667[1]; n667_2 = n667[2];
  //   n667_3 = n667[3]; n667_4 = n667[4]; n667_5 = n667[5]; n667_6 = n667[6]; n667_7 = n667[7]; n667_8 = n667[8];
  //   n667_9 = n667[9]; n667_10 = n667[10]; n667_11 = n667[11]; n667_12 = n667[12]; n667_13 = n667[13];
  //   n667_14 = n667[14]; n667_15 = n667[15]; n670_0 = n670[0]; n675[15:0] = n670; n670_1 = n670[1]; n670_2 = n670[2];
  //   n670_3 = n670[3]; n670_4 = n670[4]; n670_5 = n670[5]; n670_6 = n670[6]; n670_7 = n670[7]; n670_8 = n670[8];
  //   n670_9 = n670[9]; n670_10 = n670[10]; n670_11 = n670[11]; n670_12 = n670[12]; n670_13 = n670[13];
  //   n670_14 = n670[14]; n670_15 = n670[15]; n676_0 = n676[0]; n678[15:0] = n676; n676_1 = n676[1]; n676_2 = n676[2];
  //   n676_3 = n676[3]; n676_4 = n676[4]; n676_5 = n676[5]; n676_6 = n676[6]; n676_7 = n676[7]; n676_8 = n676[8];
  //   n676_9 = n676[9]; n676_10 = n676[10]; n676_11 = n676[11]; n676_12 = n676[12]; n676_13 = n676[13];
  //   n676_14 = n676[14]; n676_15 = n676[15]; n679_0 = n679[0]; n680[15:0] = n679; n679_1 = n679[1]; n679_2 = n679[2];
  //   n679_3 = n679[3]; n679_4 = n679[4]; n679_5 = n679[5]; n679_6 = n679[6]; n679_7 = n679[7]; n679_8 = n679[8];
  //   n679_9 = n679[9]; n679_10 = n679[10]; n679_11 = n679[11]; n679_12 = n679[12]; n679_13 = n679[13];
  //   n679_14 = n679[14]; n679_15 = n679[15]; n658_0 = n658[0]; n681[15:0] = n658; n658_1 = n658[1]; n658_2 = n658[2];
  //   n658_3 = n658[3]; n658_4 = n658[4]; n658_5 = n658[5]; n658_6 = n658[6]; n658_7 = n658[7]; n658_8 = n658[8];
  //   n658_9 = n658[9]; n658_10 = n658[10]; n658_11 = n658[11]; n658_12 = n658[12]; n658_13 = n658[13];
  //   n658_14 = n658[14]; n658_15 = n658[15]; n692[7:0] = {8{n685}}; n693_0 = n693[0]; n721[7:0] = n693;
  //   n693_1 = n693[1]; n693_2 = n693[2]; n693_3 = n693[3]; n693_4 = n693[4]; n693_5 = n693[5]; n693_6 = n693[6];
  //   n693_7 = n693[7]; n695[7:0] = {8{n686}}; n698[7:0] = {8{n687}}; RES[7:0] = n700; RES_0 = n700[0];
  //   RES_1 = n700[1]; RES_2 = n700[2]; RES_3 = n700[3]; RES_4 = n700[4]; RES_5 = n700[5]; RES_6 = n700[6];
  //   RES_7 = n700[7]; n701[7:0] = {8{n688}}; A_0 = A[0]; n691[7:0] = A; n703[7:0] = A; A_1 = A[1]; A_2 = A[2];
  //   A_3 = A[3]; A_4 = A[4]; A_5 = A[5]; A_6 = A[6]; A_7 = A[7]; n704[7:0] = {8{n689}}; n705_0 = n705[0];
  //   n727[7:0] = n705; n705_1 = n705[1]; n705_2 = n705[2]; n705_3 = n705[3]; n705_4 = n705[4]; n705_5 = n705[5];
  //   n705_6 = n705[6]; n705_7 = n705[7]; n706 (some bits) = {P[7:6], n684, P[3:0]};
  //   n804[7:0] = {DataIn[7], P[6:2], n573, P[0]}; n810 (some bits) = {P[7:3], P[1:0]}; P_0 = P[0]; P_1 = P[1];
  //   P_2 = P[2]; P_3 = P[3]; P_6 = P[6]; P_7 = P[7]; n707[7:0] = {8{n690}};
  //   n709[7:0] = {n290, n288, n286, n284, n282, n280, n278, n276};
  //   n712[7:0] = {n274, n272, n270, n268, n266, n264, n262, n260}; n717_0 = n717[0]; n733[7:0] = n717;
  //   n717_1 = n717[1]; n717_2 = n717[2]; n717_3 = n717[3]; n717_4 = n717[4]; n717_5 = n717[5]; n717_6 = n717[6];
  //   n717_7 = n717[7]; n718[7:0] = PC[7:0]; PC_0 = PC[0]; PC_1 = PC[1]; PC_2 = PC[2]; PC_3 = PC[3]; PC_4 = PC[4];
  //   PC_5 = PC[5]; PC_6 = PC[6]; PC_7 = PC[7]; n696_0 = n696[0]; n722[7:0] = n696; n696_1 = n696[1];
  //   n696_2 = n696[2]; n696_3 = n696[3]; n696_4 = n696[4]; n696_5 = n696[5]; n696_6 = n696[6]; n696_7 = n696[7];
  //   n699_0 = n699[0]; n724[7:0] = n699; n699_1 = n699[1]; n699_2 = n699[2]; n699_3 = n699[3]; n699_4 = n699[4];
  //   n699_5 = n699[5]; n699_6 = n699[6]; n699_7 = n699[7]; n702_0 = n702[0]; n725[7:0] = n702; n702_1 = n702[1];
  //   n702_2 = n702[2]; n702_3 = n702[3]; n702_4 = n702[4]; n702_5 = n702[5]; n702_6 = n702[6]; n702_7 = n702[7];
  //   n708_0 = n708[0]; n728[7:0] = n708; n708_1 = n708[1]; n708_2 = n708[2]; n708_3 = n708[3]; n708_4 = n708[4];
  //   n708_5 = n708[5]; n708_6 = n708[6]; n708_7 = n708[7]; n729_0 = n729[0]; n739[7:0] = n729; n729_1 = n729[1];
  //   n729_2 = n729[2]; n729_3 = n729[3]; n729_4 = n729[4]; n729_5 = n729[5]; n729_6 = n729[6]; n729_7 = n729[7];
  //   n711_0 = n711[0]; n730[7:0] = n711; n711_1 = n711[1]; n711_2 = n711[2]; n711_3 = n711[3]; n711_4 = n711[4];
  //   n711_5 = n711[5]; n711_6 = n711[6]; n711_7 = n711[7]; n714_0 = n714[0]; n731[7:0] = n714; n714_1 = n714[1];
  //   n714_2 = n714[2]; n714_3 = n714[3]; n714_4 = n714[4]; n714_5 = n714[5]; n714_6 = n714[6]; n714_7 = n714[7];
  //   n720_0 = n720[0]; n734[7:0] = n720; n720_1 = n720[1]; n720_2 = n720[2]; n720_3 = n720[3]; n720_4 = n720[4];
  //   n720_5 = n720[5]; n720_6 = n720[6]; n720_7 = n720[7]; n735_0 = n735[0]; n746[7:0] = n735; n735_1 = n735[1];
  //   n735_2 = n735[2]; n735_3 = n735[3]; n735_4 = n735[4]; n735_5 = n735[5]; n735_6 = n735[6]; n735_7 = n735[7];
  //   n723_0 = n723[0]; n736[7:0] = n723; n723_1 = n723[1]; n723_2 = n723[2]; n723_3 = n723[3]; n723_4 = n723[4];
  //   n723_5 = n723[5]; n723_6 = n723[6]; n723_7 = n723[7]; n726_0 = n726[0]; n737[7:0] = n726; n726_1 = n726[1];
  //   n726_2 = n726[2]; n726_3 = n726[3]; n726_4 = n726[4]; n726_5 = n726[5]; n726_6 = n726[6]; n726_7 = n726[7];
  //   n732_0 = n732[0]; n740[7:0] = n732; n732_1 = n732[1]; n732_2 = n732[2]; n732_3 = n732[3]; n732_4 = n732[4];
  //   n732_5 = n732[5]; n732_6 = n732[6]; n732_7 = n732[7]; n738_0 = n738[0]; n742[7:0] = n738; n738_1 = n738[1];
  //   n738_2 = n738[2]; n738_3 = n738[3]; n738_4 = n738[4]; n738_5 = n738[5]; n738_6 = n738[6]; n738_7 = n738[7];
  //   n741_0 = n741[0]; n743[7:0] = n741; n741_1 = n741[1]; n741_2 = n741[2]; n741_3 = n741[3]; n741_4 = n741[4];
  //   n741_5 = n741[5]; n741_6 = n741[6]; n741_7 = n741[7]; n744_0 = n744[0]; n745[7:0] = n744; n744_1 = n744[1];
  //   n744_2 = n744[2]; n744_3 = n744[3]; n744_4 = n744[4]; n744_5 = n744[5]; n744_6 = n744[6]; n744_7 = n744[7];
  //   n750 = Write; n759 = Read; n760 = Sync; n763[7:0] = {8{n491}}; n764_0 = n764[0]; n768[7:0] = n764;
  //   n764_1 = n764[1]; n764_2 = n764[2]; n764_3 = n764[3]; n764_4 = n764[4]; n764_5 = n764[5]; n764_6 = n764[6];
  //   n764_7 = n764[7]; n766[7:0] = {8{n565}}; n805[7:0] = {8{n565}}; n767_0 = n767[0]; n769[7:0] = n767;
  //   n767_1 = n767[1]; n767_2 = n767[2]; n767_3 = n767[3]; n767_4 = n767[4]; n767_5 = n767[5]; n767_6 = n767[6];
  //   n767_7 = n767[7]; n770_0 = n770[0]; n771[7:0] = n770; n770_1 = n770[1]; n770_2 = n770[2]; n770_3 = n770[3];
  //   n770_4 = n770[4]; n770_5 = n770[5]; n770_6 = n770[6]; n770_7 = n770[7]; AluResult_0 = AluResult[0];
  //   n762[7:0] = AluResult; n772[7:0] = AluResult; n776[7:0] = AluResult; n1281[7:0] = AluResult;
  //   AluResult_1 = AluResult[1]; AluResult_2 = AluResult[2]; AluResult_3 = AluResult[3]; AluResult_4 = AluResult[4];
  //   AluResult_5 = AluResult[5]; AluResult_6 = AluResult[6]; AluResult_7 = AluResult[7]; n773[7:0] = {8{n496}};
  //   n774_0 = n774[0]; n775[7:0] = n774; n774_1 = n774[1]; n774_2 = n774[2]; n774_3 = n774[3]; n774_4 = n774[4];
  //   n774_5 = n774[5]; n774_6 = n774[6]; n774_7 = n774[7]; n777[7:0] = {8{n500}}; n778_0 = n778[0]; n779[7:0] = n778;
  //   n778_1 = n778[1]; n778_2 = n778[2]; n778_3 = n778[3]; n778_4 = n778[4]; n778_5 = n778[5]; n778_6 = n778[6];
  //   n778_7 = n778[7]; n783[7:0] = {8{n501}}; n785[7:0] = {n258, n256, n254, n252, n250, n248, n246, n244};
  //   n648[15:0] = {16{n559}}; n786[7:0] = {8{n559}}; n787_0 = n787[0]; n792[7:0] = n787; n787_1 = n787[1];
  //   n787_2 = n787[2]; n787_3 = n787[3]; n787_4 = n787[4]; n787_5 = n787[5]; n787_6 = n787[6]; n787_7 = n787[7];
  //   n650[7:0] = {n242, n240, n238, n236, n234, n232, n230, n228};
  //   n788[7:0] = {n242, n240, n238, n236, n234, n232, n230, n228}; n651[15:0] = {16{n564}}; n789[7:0] = {8{n564}};
  //   n784_0 = n784[0]; n791[7:0] = n784; n784_1 = n784[1]; n784_2 = n784[2]; n784_3 = n784[3]; n784_4 = n784[4];
  //   n784_5 = n784[5]; n784_6 = n784[6]; n784_7 = n784[7]; n793_0 = n793[0]; n794[7:0] = n793; n793_1 = n793[1];
  //   n793_2 = n793[2]; n793_3 = n793[3]; n793_4 = n793[4]; n793_5 = n793[5]; n793_6 = n793[6]; n793_7 = n793[7];
  //   n790_0 = n790[0]; n795[7:0] = n790; n790_1 = n790[1]; n790_2 = n790[2]; n790_3 = n790[3]; n790_4 = n790[4];
  //   n790_5 = n790[5]; n790_6 = n790[6]; n790_7 = n790[7]; n796_0 = n796[0]; n797[7:0] = n796; n796_1 = n796[1];
  //   n796_2 = n796[2]; n796_3 = n796[3]; n796_4 = n796[4]; n796_5 = n796[5]; n796_6 = n796[6]; n796_7 = n796[7];
  //   AluFlags_0 = AluFlags[0]; n801[7:0] = AluFlags; AluFlags_1 = AluFlags[1]; AluFlags_2 = AluFlags[2];
  //   AluFlags_3 = AluFlags[3]; AluFlags_4 = AluFlags[4]; AluFlags_5 = AluFlags[5]; AluFlags_6 = AluFlags[6];
  //   AluFlags_7 = AluFlags[7]; n802[7:0] = {8{n125}}; n808[7:0] = {8{n575}}; n812_0 = n812[0]; n817[7:0] = n812;
  //   n812_1 = n812[1]; n812_2 = n812[2]; n812_3 = n812[3]; n812_4 = n812[4]; n812_5 = n812[5]; n812_6 = n812[6];
  //   n812_7 = n812[7]; n803_0 = n803[0]; n813[7:0] = n803; n803_1 = n803[1]; n803_2 = n803[2]; n803_3 = n803[3];
  //   n803_4 = n803[4]; n803_5 = n803[5]; n803_6 = n803[6]; n803_7 = n803[7]; n806_0 = n806[0]; n814[7:0] = n806;
  //   n806_1 = n806[1]; n806_2 = n806[2]; n806_3 = n806[3]; n806_4 = n806[4]; n806_5 = n806[5]; n806_6 = n806[6];
  //   n806_7 = n806[7]; n809_0 = n809[0]; n816[7:0] = n809; n809_1 = n809[1]; n809_2 = n809[2]; n809_3 = n809[3];
  //   n809_4 = n809[4]; n809_5 = n809[5]; n809_6 = n809[6]; n809_7 = n809[7]; n815_0 = n815[0]; n819[7:0] = n815;
  //   n815_1 = n815[1]; n815_2 = n815[2]; n815_3 = n815[3]; n815_4 = n815[4]; n815_5 = n815[5]; n815_6 = n815[6];
  //   n815_7 = n815[7]; n818_0 = n818[0]; n820[7:0] = n818; n818_1 = n818[1]; n818_2 = n818[2]; n818_3 = n818[3];
  //   n818_4 = n818[4]; n818_5 = n818[5]; n818_6 = n818[6]; n818_7 = n818[7]; n821_0 = n821[0]; n822[7:0] = n821;
  //   n821_1 = n821[1]; n821_2 = n821[2]; n821_3 = n821[3]; n821_4 = n821[4]; n821_5 = n821[5]; n821_6 = n821[6];
  //   n821_7 = n821[7]; n636[15:0] = {16{n77}}; n834[15:0] = {16{n77}}; n949[7:0] = {8{n77}}; n838_0 = n838[0];
  //   n867[15:0] = n838; n838_1 = n838[1]; n838_2 = n838[2]; n838_3 = n838[3]; n838_4 = n838[4]; n838_5 = n838[5];
  //   n838_6 = n838[6]; n838_7 = n838[7]; n838_8 = n838[8]; n838_9 = n838[9]; n838_10 = n838[10]; n838_11 = n838[11];
  //   n838_12 = n838[12]; n838_13 = n838[13]; n838_14 = n838[14]; n838_15 = n838[15]; n840[15:0] = {16{n331}};
  //   n979[7:0] = {8{n331}}; n1290[7:0] = {8{n331}}; n843[15:0] = {16{n97}};
  //   n836[15:0] = {n226, n224, n222, n220, n218, n216, n214, n212, n210, n208, n206, n204, n202, n200, n198, n196};
  //   n839[15:0] = {n226, n224, n222, n220, n218, n216, n214, n212, n210, n208, n206, n204, n202, n200, n198, n196};
  //   n842[15:0] = {n226, n224, n222, n220, n218, n216, n214, n212, n210, n208, n206, n204, n202, n200, n198, n196};
  //   n845[15:0] = {n226, n224, n222, n220, n218, n216, n214, n212, n210, n208, n206, n204, n202, n200, n198, n196};
  //   n846[15:0] = {16{n103}}; n1223[15:0] = {16{n103}};
  //   n848[15:0] = {n551, n549, n547, n545, n543, n541, n539, n537, n535, n533, n531, n529, n527, n525, n523, n521};
  //   n849[15:0] = {16{n553}}; n850_0 = n850[0]; n873[15:0] = n850; n850_1 = n850[1]; n850_2 = n850[2];
  //   n850_3 = n850[3]; n850_4 = n850[4]; n850_5 = n850[5]; n850_6 = n850[6]; n850_7 = n850[7]; n850_8 = n850[8];
  //   n850_9 = n850[9]; n850_10 = n850[10]; n850_11 = n850[11]; n850_12 = n850[12]; n850_13 = n850[13];
  //   n850_14 = n850[14]; n850_15 = n850[15]; EA_0 = EA[0]; n641[15:0] = EA; n851[15:0] = EA; n854[15:0] = EA;
  //   EA_1 = EA[1]; EA_2 = EA[2]; EA_3 = EA[3]; EA_4 = EA[4]; EA_5 = EA[5]; EA_6 = EA[6]; EA_7 = EA[7]; EA_8 = EA[8];
  //   EA_9 = EA[9]; EA_10 = EA[10]; EA_11 = EA[11]; EA_12 = EA[12]; EA_13 = EA[13]; EA_14 = EA[14]; EA_15 = EA[15];
  //   n852[15:0] = {16{n554}};
  //   n857[15:0] = {n607, n605, n603, n601, n599, n597, n595, n593, n591, n589, n587, n585, n583, n581, n579, n577};
  //   n858[15:0] = {16{n159}}; n1051[7:0] = {8{n159}}; n862_0 = n862[0]; n879[15:0] = n862; n862_1 = n862[1];
  //   n862_2 = n862[2]; n862_3 = n862[3]; n862_4 = n862[4]; n862_5 = n862[5]; n862_6 = n862[6]; n862_7 = n862[7];
  //   n862_8 = n862[8]; n862_9 = n862[9]; n862_10 = n862[10]; n862_11 = n862[11]; n862_12 = n862[12];
  //   n862_13 = n862[13]; n862_14 = n862[14]; n862_15 = n862[15]; n860[15:0] = {DataIn, n833};
  //   n863[15:0] = {DataIn, n833}; TMP[7:0] = n833; TMP_0 = n833[0]; TMP_1 = n833[1]; TMP_2 = n833[2];
  //   TMP_3 = n833[3]; TMP_4 = n833[4]; TMP_5 = n833[5]; TMP_6 = n833[6]; TMP_7 = n833[7]; n657[15:0] = {16{n191}};
  //   n864[15:0] = {16{n191}}; n1075[7:0] = {8{n191}}; n835_0 = n835[0]; n866[15:0] = n835; n835_1 = n835[1];
  //   n835_2 = n835[2]; n835_3 = n835[3]; n835_4 = n835[4]; n835_5 = n835[5]; n835_6 = n835[6]; n835_7 = n835[7];
  //   n835_8 = n835[8]; n835_9 = n835[9]; n835_10 = n835[10]; n835_11 = n835[11]; n835_12 = n835[12];
  //   n835_13 = n835[13]; n835_14 = n835[14]; n835_15 = n835[15]; n841_0 = n841[0]; n869[15:0] = n841;
  //   n841_1 = n841[1]; n841_2 = n841[2]; n841_3 = n841[3]; n841_4 = n841[4]; n841_5 = n841[5]; n841_6 = n841[6];
  //   n841_7 = n841[7]; n841_8 = n841[8]; n841_9 = n841[9]; n841_10 = n841[10]; n841_11 = n841[11];
  //   n841_12 = n841[12]; n841_13 = n841[13]; n841_14 = n841[14]; n841_15 = n841[15]; n844_0 = n844[0];
  //   n870[15:0] = n844; n844_1 = n844[1]; n844_2 = n844[2]; n844_3 = n844[3]; n844_4 = n844[4]; n844_5 = n844[5];
  //   n844_6 = n844[6]; n844_7 = n844[7]; n844_8 = n844[8]; n844_9 = n844[9]; n844_10 = n844[10]; n844_11 = n844[11];
  //   n844_12 = n844[12]; n844_13 = n844[13]; n844_14 = n844[14]; n844_15 = n844[15]; n847_0 = n847[0];
  //   n872[15:0] = n847; n847_1 = n847[1]; n847_2 = n847[2]; n847_3 = n847[3]; n847_4 = n847[4]; n847_5 = n847[5];
  //   n847_6 = n847[6]; n847_7 = n847[7]; n847_8 = n847[8]; n847_9 = n847[9]; n847_10 = n847[10]; n847_11 = n847[11];
  //   n847_12 = n847[12]; n847_13 = n847[13]; n847_14 = n847[14]; n847_15 = n847[15]; n874_0 = n874[0];
  //   n884[15:0] = n874; n874_1 = n874[1]; n874_2 = n874[2]; n874_3 = n874[3]; n874_4 = n874[4]; n874_5 = n874[5];
  //   n874_6 = n874[6]; n874_7 = n874[7]; n874_8 = n874[8]; n874_9 = n874[9]; n874_10 = n874[10]; n874_11 = n874[11];
  //   n874_12 = n874[12]; n874_13 = n874[13]; n874_14 = n874[14]; n874_15 = n874[15]; n853_0 = n853[0];
  //   n875[15:0] = n853; n853_1 = n853[1]; n853_2 = n853[2]; n853_3 = n853[3]; n853_4 = n853[4]; n853_5 = n853[5];
  //   n853_6 = n853[6]; n853_7 = n853[7]; n853_8 = n853[8]; n853_9 = n853[9]; n853_10 = n853[10]; n853_11 = n853[11];
  //   n853_12 = n853[12]; n853_13 = n853[13]; n853_14 = n853[14]; n853_15 = n853[15]; n856_0 = n856[0];
  //   n876[15:0] = n856; n856_1 = n856[1]; n856_2 = n856[2]; n856_3 = n856[3]; n856_4 = n856[4]; n856_5 = n856[5];
  //   n856_6 = n856[6]; n856_7 = n856[7]; n856_8 = n856[8]; n856_9 = n856[9]; n856_10 = n856[10]; n856_11 = n856[11];
  //   n856_12 = n856[12]; n856_13 = n856[13]; n856_14 = n856[14]; n856_15 = n856[15]; n859_0 = n859[0];
  //   n878[15:0] = n859; n859_1 = n859[1]; n859_2 = n859[2]; n859_3 = n859[3]; n859_4 = n859[4]; n859_5 = n859[5];
  //   n859_6 = n859[6]; n859_7 = n859[7]; n859_8 = n859[8]; n859_9 = n859[9]; n859_10 = n859[10]; n859_11 = n859[11];
  //   n859_12 = n859[12]; n859_13 = n859[13]; n859_14 = n859[14]; n859_15 = n859[15]; n868_0 = n868[0];
  //   n881[15:0] = n868; n868_1 = n868[1]; n868_2 = n868[2]; n868_3 = n868[3]; n868_4 = n868[4]; n868_5 = n868[5];
  //   n868_6 = n868[6]; n868_7 = n868[7]; n868_8 = n868[8]; n868_9 = n868[9]; n868_10 = n868[10]; n868_11 = n868[11];
  //   n868_12 = n868[12]; n868_13 = n868[13]; n868_14 = n868[14]; n868_15 = n868[15]; n871_0 = n871[0];
  //   n882[15:0] = n871; n871_1 = n871[1]; n871_2 = n871[2]; n871_3 = n871[3]; n871_4 = n871[4]; n871_5 = n871[5];
  //   n871_6 = n871[6]; n871_7 = n871[7]; n871_8 = n871[8]; n871_9 = n871[9]; n871_10 = n871[10]; n871_11 = n871[11];
  //   n871_12 = n871[12]; n871_13 = n871[13]; n871_14 = n871[14]; n871_15 = n871[15]; n877_0 = n877[0];
  //   n885[15:0] = n877; n877_1 = n877[1]; n877_2 = n877[2]; n877_3 = n877[3]; n877_4 = n877[4]; n877_5 = n877[5];
  //   n877_6 = n877[6]; n877_7 = n877[7]; n877_8 = n877[8]; n877_9 = n877[9]; n877_10 = n877[10]; n877_11 = n877[11];
  //   n877_12 = n877[12]; n877_13 = n877[13]; n877_14 = n877[14]; n877_15 = n877[15]; n886_0 = n886[0];
  //   n891[15:0] = n886; n886_1 = n886[1]; n886_2 = n886[2]; n886_3 = n886[3]; n886_4 = n886[4]; n886_5 = n886[5];
  //   n886_6 = n886[6]; n886_7 = n886[7]; n886_8 = n886[8]; n886_9 = n886[9]; n886_10 = n886[10]; n886_11 = n886[11];
  //   n886_12 = n886[12]; n886_13 = n886[13]; n886_14 = n886[14]; n886_15 = n886[15]; n880_0 = n880[0];
  //   n887[15:0] = n880; n880_1 = n880[1]; n880_2 = n880[2]; n880_3 = n880[3]; n880_4 = n880[4]; n880_5 = n880[5];
  //   n880_6 = n880[6]; n880_7 = n880[7]; n880_8 = n880[8]; n880_9 = n880[9]; n880_10 = n880[10]; n880_11 = n880[11];
  //   n880_12 = n880[12]; n880_13 = n880[13]; n880_14 = n880[14]; n880_15 = n880[15]; n865_0 = n865[0];
  //   n888[15:0] = n865; n865_1 = n865[1]; n865_2 = n865[2]; n865_3 = n865[3]; n865_4 = n865[4]; n865_5 = n865[5];
  //   n865_6 = n865[6]; n865_7 = n865[7]; n865_8 = n865[8]; n865_9 = n865[9]; n865_10 = n865[10]; n865_11 = n865[11];
  //   n865_12 = n865[12]; n865_13 = n865[13]; n865_14 = n865[14]; n865_15 = n865[15]; n883_0 = n883[0];
  //   n890[15:0] = n883; n883_1 = n883[1]; n883_2 = n883[2]; n883_3 = n883[3]; n883_4 = n883[4]; n883_5 = n883[5];
  //   n883_6 = n883[6]; n883_7 = n883[7]; n883_8 = n883[8]; n883_9 = n883[9]; n883_10 = n883[10]; n883_11 = n883[11];
  //   n883_12 = n883[12]; n883_13 = n883[13]; n883_14 = n883[14]; n883_15 = n883[15]; n892_0 = n892[0];
  //   n893[15:0] = n892; n892_1 = n892[1]; n892_2 = n892[2]; n892_3 = n892[3]; n892_4 = n892[4]; n892_5 = n892[5];
  //   n892_6 = n892[6]; n892_7 = n892[7]; n892_8 = n892[8]; n892_9 = n892[9]; n892_10 = n892[10]; n892_11 = n892[11];
  //   n892_12 = n892[12]; n892_13 = n892[13]; n892_14 = n892[14]; n892_15 = n892[15]; n889_0 = n889[0];
  //   n894[15:0] = n889; n889_1 = n889[1]; n889_2 = n889[2]; n889_3 = n889[3]; n889_4 = n889[4]; n889_5 = n889[5];
  //   n889_6 = n889[6]; n889_7 = n889[7]; n889_8 = n889[8]; n889_9 = n889[9]; n889_10 = n889[10]; n889_11 = n889[11];
  //   n889_12 = n889[12]; n889_13 = n889[13]; n889_14 = n889[14]; n889_15 = n889[15]; n895_0 = n895[0];
  //   n896[15:0] = n895; n895_1 = n895[1]; n895_2 = n895[2]; n895_3 = n895[3]; n895_4 = n895[4]; n895_5 = n895[5];
  //   n895_6 = n895[6]; n895_7 = n895[7]; n895_8 = n895[8]; n895_9 = n895[9]; n895_10 = n895[10]; n895_11 = n895[11];
  //   n895_12 = n895[12]; n895_13 = n895[13]; n895_14 = n895[14]; n895_15 = n895[15]; n837[15:0] = {16{n310}};
  //   n898[7:0] = {8{n310}}; n955[7:0] = {8{n310}}; n899_0 = n899[0]; n900[7:0] = n899; n899_1 = n899[1];
  //   n899_2 = n899[2]; n899_3 = n899[3]; n899_4 = n899[4]; n899_5 = n899[5]; n899_6 = n899[6]; n899_7 = n899[7];
  //   n633[15:0] = {16{n70}}; n946[7:0] = {8{n70}}; n1254[7:0] = {8{n70}}; n950_0 = n950[0]; n1081[7:0] = n950;
  //   n950_1 = n950[1]; n950_2 = n950[2]; n950_3 = n950[3]; n950_4 = n950[4]; n950_5 = n950[5]; n950_6 = n950[6];
  //   n950_7 = n950[7]; n952[7:0] = {8{n307}}; n1287[7:0] = {8{n307}}; n958[7:0] = {8{n312}}; n961[7:0] = {8{n322}};
  //   n962_0 = n962[0]; n1087[7:0] = n962; n962_1 = n962[1]; n962_2 = n962[2]; n962_3 = n962[3]; n962_4 = n962[4];
  //   n962_5 = n962[5]; n962_6 = n962[6]; n962_7 = n962[7]; n964[7:0] = {8{n325}}; n967[7:0] = {8{n326}};
  //   n970[7:0] = {8{n328}}; n973[7:0] = {8{n329}}; n974_0 = n974[0]; n1093[7:0] = n974; n974_1 = n974[1];
  //   n974_2 = n974[2]; n974_3 = n974[3]; n974_4 = n974[4]; n974_5 = n974[5]; n974_6 = n974[6]; n974_7 = n974[7];
  //   n976[7:0] = {8{n330}}; n986_0 = n986[0]; n1099[7:0] = n986; n986_1 = n986[1]; n986_2 = n986[2];
  //   n986_3 = n986[3]; n986_4 = n986[4]; n986_5 = n986[5]; n986_6 = n986[6]; n986_7 = n986[7]; n988[7:0] = {8{n367}};
  //   n991[7:0] = {8{n369}}; n994[7:0] = {8{n371}}; n1220[15:0] = {16{n371}}; n997[7:0] = {8{n413}}; n998_0 = n998[0];
  //   n1105[7:0] = n998; n998_1 = n998[1]; n998_2 = n998[2]; n998_3 = n998[3]; n998_4 = n998[4]; n998_5 = n998[5];
  //   n998_6 = n998[6]; n998_7 = n998[7]; n1000[7:0] = {8{n416}}; n1003[7:0] = {8{n417}}; n1006[7:0] = {8{n421}};
  //   n1009[7:0] = {8{n422}}; n1010_0 = n1010[0]; n1111[7:0] = n1010; n1010_1 = n1010[1]; n1010_2 = n1010[2];
  //   n1010_3 = n1010[3]; n1010_4 = n1010[4]; n1010_5 = n1010[5]; n1010_6 = n1010[6]; n1010_7 = n1010[7];
  //   n1012[7:0] = {8{n109}}; n1260[7:0] = {8{n109}}; n1015[7:0] = {8{n474}}; n1018[7:0] = {8{n477}};
  //   n1021[7:0] = {8{n478}}; n1022_0 = n1022[0]; n1117[7:0] = n1022; n1022_1 = n1022[1]; n1022_2 = n1022[2];
  //   n1022_3 = n1022[3]; n1022_4 = n1022[4]; n1022_5 = n1022[5]; n1022_6 = n1022[6]; n1022_7 = n1022[7];
  //   n1024[7:0] = {8{n120}}; n1243[7:0] = {8{n120}}; n1027[7:0] = {8{n130}}; n1033[7:0] = {8{n481}};
  //   n1034_0 = n1034[0]; n1123[7:0] = n1034; n1034_1 = n1034[1]; n1034_2 = n1034[2]; n1034_3 = n1034[3];
  //   n1034_4 = n1034[4]; n1034_5 = n1034[5]; n1034_6 = n1034[6]; n1034_7 = n1034[7]; n1036[7:0] = {8{n135}};
  //   n710[7:0] = {8{n145}}; n1039[7:0] = {8{n145}}; n713[7:0] = {8{n150}}; n855[15:0] = {16{n150}};
  //   n1042[7:0] = {8{n150}}; n1045[7:0] = {8{n140}}; n1046_0 = n1046[0]; n1129[7:0] = n1046; n1046_1 = n1046[1];
  //   n1046_2 = n1046[2]; n1046_3 = n1046[3]; n1046_4 = n1046[4]; n1046_5 = n1046[5]; n1046_6 = n1046[6];
  //   n1046_7 = n1046[7]; n1048[7:0] = {8{n155}}; n1054[7:0] = {8{n163}}; n1057[7:0] = {8{n167}}; n1058_0 = n1058[0];
  //   n1135[7:0] = n1058; n1058_1 = n1058[1]; n1058_2 = n1058[2]; n1058_3 = n1058[3]; n1058_4 = n1058[4];
  //   n1058_5 = n1058[5]; n1058_6 = n1058[6]; n1058_7 = n1058[7]; n861[15:0] = {16{n171}}; n1060[7:0] = {8{n171}};
  //   n716[7:0] = {8{n175}}; n1063[7:0] = {8{n175}}; n719[7:0] = {8{n179}}; n1066[7:0] = {8{n179}};
  //   n811[7:0] = {8{n183}}; n1069[7:0] = {8{n183}}; n1070_0 = n1070[0]; n1141[7:0] = n1070; n1070_1 = n1070[1];
  //   n1070_2 = n1070[2]; n1070_3 = n1070[3]; n1070_4 = n1070[4]; n1070_5 = n1070[5]; n1070_6 = n1070[6];
  //   n1070_7 = n1070[7]; n654[15:0] = {16{n187}}; n1072[7:0] = {8{n187}}; n1266[7:0] = {8{n187}}; n195 = Fault;
  //   n1078[7:0] = {8{Fault}}; n947_0 = n947[0]; n1080[7:0] = n947; n947_1 = n947[1]; n947_2 = n947[2];
  //   n947_3 = n947[3]; n947_4 = n947[4]; n947_5 = n947[5]; n947_6 = n947[6]; n947_7 = n947[7]; n1082_0 = n1082[0];
  //   n1146[7:0] = n1082; n1082_1 = n1082[1]; n1082_2 = n1082[2]; n1082_3 = n1082[3]; n1082_4 = n1082[4];
  //   n1082_5 = n1082[5]; n1082_6 = n1082[6]; n1082_7 = n1082[7]; n953_0 = n953[0]; n1083[7:0] = n953;
  //   n953_1 = n953[1]; n953_2 = n953[2]; n953_3 = n953[3]; n953_4 = n953[4]; n953_5 = n953[5]; n953_6 = n953[6];
  //   n953_7 = n953[7]; n956_0 = n956[0]; n1084[7:0] = n956; n956_1 = n956[1]; n956_2 = n956[2]; n956_3 = n956[3];
  //   n956_4 = n956[4]; n956_5 = n956[5]; n956_6 = n956[6]; n956_7 = n956[7]; n959_0 = n959[0]; n1086[7:0] = n959;
  //   n959_1 = n959[1]; n959_2 = n959[2]; n959_3 = n959[3]; n959_4 = n959[4]; n959_5 = n959[5]; n959_6 = n959[6];
  //   n959_7 = n959[7]; n965_0 = n965[0]; n1089[7:0] = n965; n965_1 = n965[1]; n965_2 = n965[2]; n965_3 = n965[3];
  //   n965_4 = n965[4]; n965_5 = n965[5]; n965_6 = n965[6]; n965_7 = n965[7]; n968_0 = n968[0]; n1090[7:0] = n968;
  //   n968_1 = n968[1]; n968_2 = n968[2]; n968_3 = n968[3]; n968_4 = n968[4]; n968_5 = n968[5]; n968_6 = n968[6];
  //   n968_7 = n968[7]; n971_0 = n971[0]; n1092[7:0] = n971; n971_1 = n971[1]; n971_2 = n971[2]; n971_3 = n971[3];
  //   n971_4 = n971[4]; n971_5 = n971[5]; n971_6 = n971[6]; n971_7 = n971[7]; n1094_0 = n1094[0]; n1152[7:0] = n1094;
  //   n1094_1 = n1094[1]; n1094_2 = n1094[2]; n1094_3 = n1094[3]; n1094_4 = n1094[4]; n1094_5 = n1094[5];
  //   n1094_6 = n1094[6]; n1094_7 = n1094[7]; n977_0 = n977[0]; n1095[7:0] = n977; n977_1 = n977[1]; n977_2 = n977[2];
  //   n977_3 = n977[3]; n977_4 = n977[4]; n977_5 = n977[5]; n977_6 = n977[6]; n977_7 = n977[7]; n980_0 = n980[0];
  //   n1096[7:0] = n980; n980_1 = n980[1]; n980_2 = n980[2]; n980_3 = n980[3]; n980_4 = n980[4]; n980_5 = n980[5];
  //   n980_6 = n980[6]; n980_7 = n980[7]; n983_0 = n983[0]; n1098[7:0] = n983; n983_1 = n983[1]; n983_2 = n983[2];
  //   n983_3 = n983[3]; n983_4 = n983[4]; n983_5 = n983[5]; n983_6 = n983[6]; n983_7 = n983[7]; n989_0 = n989[0];
  //   n1101[7:0] = n989; n989_1 = n989[1]; n989_2 = n989[2]; n989_3 = n989[3]; n989_4 = n989[4]; n989_5 = n989[5];
  //   n989_6 = n989[6]; n989_7 = n989[7]; n992_0 = n992[0]; n1102[7:0] = n992; n992_1 = n992[1]; n992_2 = n992[2];
  //   n992_3 = n992[3]; n992_4 = n992[4]; n992_5 = n992[5]; n992_6 = n992[6]; n992_7 = n992[7]; n995_0 = n995[0];
  //   n1104[7:0] = n995; n995_1 = n995[1]; n995_2 = n995[2]; n995_3 = n995[3]; n995_4 = n995[4]; n995_5 = n995[5];
  //   n995_6 = n995[6]; n995_7 = n995[7]; n1106_0 = n1106[0]; n1158[7:0] = n1106; n1106_1 = n1106[1];
  //   n1106_2 = n1106[2]; n1106_3 = n1106[3]; n1106_4 = n1106[4]; n1106_5 = n1106[5]; n1106_6 = n1106[6];
  //   n1106_7 = n1106[7]; n1001_0 = n1001[0]; n1107[7:0] = n1001; n1001_1 = n1001[1]; n1001_2 = n1001[2];
  //   n1001_3 = n1001[3]; n1001_4 = n1001[4]; n1001_5 = n1001[5]; n1001_6 = n1001[6]; n1001_7 = n1001[7];
  //   n1004_0 = n1004[0]; n1108[7:0] = n1004; n1004_1 = n1004[1]; n1004_2 = n1004[2]; n1004_3 = n1004[3];
  //   n1004_4 = n1004[4]; n1004_5 = n1004[5]; n1004_6 = n1004[6]; n1004_7 = n1004[7]; n1007_0 = n1007[0];
  //   n1110[7:0] = n1007; n1007_1 = n1007[1]; n1007_2 = n1007[2]; n1007_3 = n1007[3]; n1007_4 = n1007[4];
  //   n1007_5 = n1007[5]; n1007_6 = n1007[6]; n1007_7 = n1007[7]; n1013_0 = n1013[0]; n1113[7:0] = n1013;
  //   n1013_1 = n1013[1]; n1013_2 = n1013[2]; n1013_3 = n1013[3]; n1013_4 = n1013[4]; n1013_5 = n1013[5];
  //   n1013_6 = n1013[6]; n1013_7 = n1013[7]; n1016_0 = n1016[0]; n1114[7:0] = n1016; n1016_1 = n1016[1];
  //   n1016_2 = n1016[2]; n1016_3 = n1016[3]; n1016_4 = n1016[4]; n1016_5 = n1016[5]; n1016_6 = n1016[6];
  //   n1016_7 = n1016[7]; n1019_0 = n1019[0]; n1116[7:0] = n1019; n1019_1 = n1019[1]; n1019_2 = n1019[2];
  //   n1019_3 = n1019[3]; n1019_4 = n1019[4]; n1019_5 = n1019[5]; n1019_6 = n1019[6]; n1019_7 = n1019[7];
  //   n1118_0 = n1118[0]; n1164[7:0] = n1118; n1118_1 = n1118[1]; n1118_2 = n1118[2]; n1118_3 = n1118[3];
  //   n1118_4 = n1118[4]; n1118_5 = n1118[5]; n1118_6 = n1118[6]; n1118_7 = n1118[7]; n1025_0 = n1025[0];
  //   n1119[7:0] = n1025; n1025_1 = n1025[1]; n1025_2 = n1025[2]; n1025_3 = n1025[3]; n1025_4 = n1025[4];
  //   n1025_5 = n1025[5]; n1025_6 = n1025[6]; n1025_7 = n1025[7]; n1028_0 = n1028[0]; n1120[7:0] = n1028;
  //   n1028_1 = n1028[1]; n1028_2 = n1028[2]; n1028_3 = n1028[3]; n1028_4 = n1028[4]; n1028_5 = n1028[5];
  //   n1028_6 = n1028[6]; n1028_7 = n1028[7]; n1031_0 = n1031[0]; n1122[7:0] = n1031; n1031_1 = n1031[1];
  //   n1031_2 = n1031[2]; n1031_3 = n1031[3]; n1031_4 = n1031[4]; n1031_5 = n1031[5]; n1031_6 = n1031[6];
  //   n1031_7 = n1031[7]; n1037_0 = n1037[0]; n1125[7:0] = n1037; n1037_1 = n1037[1]; n1037_2 = n1037[2];
  //   n1037_3 = n1037[3]; n1037_4 = n1037[4]; n1037_5 = n1037[5]; n1037_6 = n1037[6]; n1037_7 = n1037[7];
  //   n1040_0 = n1040[0]; n1126[7:0] = n1040; n1040_1 = n1040[1]; n1040_2 = n1040[2]; n1040_3 = n1040[3];
  //   n1040_4 = n1040[4]; n1040_5 = n1040[5]; n1040_6 = n1040[6]; n1040_7 = n1040[7]; n1043_0 = n1043[0];
  //   n1128[7:0] = n1043; n1043_1 = n1043[1]; n1043_2 = n1043[2]; n1043_3 = n1043[3]; n1043_4 = n1043[4];
  //   n1043_5 = n1043[5]; n1043_6 = n1043[6]; n1043_7 = n1043[7]; n1130_0 = n1130[0]; n1170[7:0] = n1130;
  //   n1130_1 = n1130[1]; n1130_2 = n1130[2]; n1130_3 = n1130[3]; n1130_4 = n1130[4]; n1130_5 = n1130[5];
  //   n1130_6 = n1130[6]; n1130_7 = n1130[7]; n1049_0 = n1049[0]; n1131[7:0] = n1049; n1049_1 = n1049[1];
  //   n1049_2 = n1049[2]; n1049_3 = n1049[3]; n1049_4 = n1049[4]; n1049_5 = n1049[5]; n1049_6 = n1049[6];
  //   n1049_7 = n1049[7]; n1052_0 = n1052[0]; n1132[7:0] = n1052; n1052_1 = n1052[1]; n1052_2 = n1052[2];
  //   n1052_3 = n1052[3]; n1052_4 = n1052[4]; n1052_5 = n1052[5]; n1052_6 = n1052[6]; n1052_7 = n1052[7];
  //   n1055_0 = n1055[0]; n1134[7:0] = n1055; n1055_1 = n1055[1]; n1055_2 = n1055[2]; n1055_3 = n1055[3];
  //   n1055_4 = n1055[4]; n1055_5 = n1055[5]; n1055_6 = n1055[6]; n1055_7 = n1055[7]; n1061_0 = n1061[0];
  //   n1137[7:0] = n1061; n1061_1 = n1061[1]; n1061_2 = n1061[2]; n1061_3 = n1061[3]; n1061_4 = n1061[4];
  //   n1061_5 = n1061[5]; n1061_6 = n1061[6]; n1061_7 = n1061[7]; n1064_0 = n1064[0]; n1138[7:0] = n1064;
  //   n1064_1 = n1064[1]; n1064_2 = n1064[2]; n1064_3 = n1064[3]; n1064_4 = n1064[4]; n1064_5 = n1064[5];
  //   n1064_6 = n1064[6]; n1064_7 = n1064[7]; n1067_0 = n1067[0]; n1140[7:0] = n1067; n1067_1 = n1067[1];
  //   n1067_2 = n1067[2]; n1067_3 = n1067[3]; n1067_4 = n1067[4]; n1067_5 = n1067[5]; n1067_6 = n1067[6];
  //   n1067_7 = n1067[7]; n1142_0 = n1142[0]; n1176[7:0] = n1142; n1142_1 = n1142[1]; n1142_2 = n1142[2];
  //   n1142_3 = n1142[3]; n1142_4 = n1142[4]; n1142_5 = n1142[5]; n1142_6 = n1142[6]; n1142_7 = n1142[7];
  //   n1073_0 = n1073[0]; n1143[7:0] = n1073; n1073_1 = n1073[1]; n1073_2 = n1073[2]; n1073_3 = n1073[3];
  //   n1073_4 = n1073[4]; n1073_5 = n1073[5]; n1073_6 = n1073[6]; n1073_7 = n1073[7]; n1076_0 = n1076[0];
  //   n1144[7:0] = n1076; n1076_1 = n1076[1]; n1076_2 = n1076[2]; n1076_3 = n1076[3]; n1076_4 = n1076[4];
  //   n1076_5 = n1076[5]; n1076_6 = n1076[6]; n1076_7 = n1076[7]; n1085_0 = n1085[0]; n1147[7:0] = n1085;
  //   n1085_1 = n1085[1]; n1085_2 = n1085[2]; n1085_3 = n1085[3]; n1085_4 = n1085[4]; n1085_5 = n1085[5];
  //   n1085_6 = n1085[6]; n1085_7 = n1085[7]; n1088_0 = n1088[0]; n1149[7:0] = n1088; n1088_1 = n1088[1];
  //   n1088_2 = n1088[2]; n1088_3 = n1088[3]; n1088_4 = n1088[4]; n1088_5 = n1088[5]; n1088_6 = n1088[6];
  //   n1088_7 = n1088[7]; n1091_0 = n1091[0]; n1150[7:0] = n1091; n1091_1 = n1091[1]; n1091_2 = n1091[2];
  //   n1091_3 = n1091[3]; n1091_4 = n1091[4]; n1091_5 = n1091[5]; n1091_6 = n1091[6]; n1091_7 = n1091[7];
  //   n1097_0 = n1097[0]; n1153[7:0] = n1097; n1097_1 = n1097[1]; n1097_2 = n1097[2]; n1097_3 = n1097[3];
  //   n1097_4 = n1097[4]; n1097_5 = n1097[5]; n1097_6 = n1097[6]; n1097_7 = n1097[7]; n1154_0 = n1154[0];
  //   n1182[7:0] = n1154; n1154_1 = n1154[1]; n1154_2 = n1154[2]; n1154_3 = n1154[3]; n1154_4 = n1154[4];
  //   n1154_5 = n1154[5]; n1154_6 = n1154[6]; n1154_7 = n1154[7]; n1100_0 = n1100[0]; n1155[7:0] = n1100;
  //   n1100_1 = n1100[1]; n1100_2 = n1100[2]; n1100_3 = n1100[3]; n1100_4 = n1100[4]; n1100_5 = n1100[5];
  //   n1100_6 = n1100[6]; n1100_7 = n1100[7]; n1103_0 = n1103[0]; n1156[7:0] = n1103; n1103_1 = n1103[1];
  //   n1103_2 = n1103[2]; n1103_3 = n1103[3]; n1103_4 = n1103[4]; n1103_5 = n1103[5]; n1103_6 = n1103[6];
  //   n1103_7 = n1103[7]; n1109_0 = n1109[0]; n1159[7:0] = n1109; n1109_1 = n1109[1]; n1109_2 = n1109[2];
  //   n1109_3 = n1109[3]; n1109_4 = n1109[4]; n1109_5 = n1109[5]; n1109_6 = n1109[6]; n1109_7 = n1109[7];
  //   n1112_0 = n1112[0]; n1161[7:0] = n1112; n1112_1 = n1112[1]; n1112_2 = n1112[2]; n1112_3 = n1112[3];
  //   n1112_4 = n1112[4]; n1112_5 = n1112[5]; n1112_6 = n1112[6]; n1112_7 = n1112[7]; n1115_0 = n1115[0];
  //   n1162[7:0] = n1115; n1115_1 = n1115[1]; n1115_2 = n1115[2]; n1115_3 = n1115[3]; n1115_4 = n1115[4];
  //   n1115_5 = n1115[5]; n1115_6 = n1115[6]; n1115_7 = n1115[7]; n1121_0 = n1121[0]; n1165[7:0] = n1121;
  //   n1121_1 = n1121[1]; n1121_2 = n1121[2]; n1121_3 = n1121[3]; n1121_4 = n1121[4]; n1121_5 = n1121[5];
  //   n1121_6 = n1121[6]; n1121_7 = n1121[7]; n1166_0 = n1166[0]; n1188[7:0] = n1166; n1166_1 = n1166[1];
  //   n1166_2 = n1166[2]; n1166_3 = n1166[3]; n1166_4 = n1166[4]; n1166_5 = n1166[5]; n1166_6 = n1166[6];
  //   n1166_7 = n1166[7]; n1124_0 = n1124[0]; n1167[7:0] = n1124; n1124_1 = n1124[1]; n1124_2 = n1124[2];
  //   n1124_3 = n1124[3]; n1124_4 = n1124[4]; n1124_5 = n1124[5]; n1124_6 = n1124[6]; n1124_7 = n1124[7];
  //   n1127_0 = n1127[0]; n1168[7:0] = n1127; n1127_1 = n1127[1]; n1127_2 = n1127[2]; n1127_3 = n1127[3];
  //   n1127_4 = n1127[4]; n1127_5 = n1127[5]; n1127_6 = n1127[6]; n1127_7 = n1127[7]; n1133_0 = n1133[0];
  //   n1171[7:0] = n1133; n1133_1 = n1133[1]; n1133_2 = n1133[2]; n1133_3 = n1133[3]; n1133_4 = n1133[4];
  //   n1133_5 = n1133[5]; n1133_6 = n1133[6]; n1133_7 = n1133[7]; n1136_0 = n1136[0]; n1173[7:0] = n1136;
  //   n1136_1 = n1136[1]; n1136_2 = n1136[2]; n1136_3 = n1136[3]; n1136_4 = n1136[4]; n1136_5 = n1136[5];
  //   n1136_6 = n1136[6]; n1136_7 = n1136[7]; n1139_0 = n1139[0]; n1174[7:0] = n1139; n1139_1 = n1139[1];
  //   n1139_2 = n1139[2]; n1139_3 = n1139[3]; n1139_4 = n1139[4]; n1139_5 = n1139[5]; n1139_6 = n1139[6];
  //   n1139_7 = n1139[7]; n1145_0 = n1145[0]; n1177[7:0] = n1145; n1145_1 = n1145[1]; n1145_2 = n1145[2];
  //   n1145_3 = n1145[3]; n1145_4 = n1145[4]; n1145_5 = n1145[5]; n1145_6 = n1145[6]; n1145_7 = n1145[7];
  //   n1178_0 = n1178[0]; n1194[7:0] = n1178; n1178_1 = n1178[1]; n1178_2 = n1178[2]; n1178_3 = n1178[3];
  //   n1178_4 = n1178[4]; n1178_5 = n1178[5]; n1178_6 = n1178[6]; n1178_7 = n1178[7]; n1148_0 = n1148[0];
  //   n1179[7:0] = n1148; n1148_1 = n1148[1]; n1148_2 = n1148[2]; n1148_3 = n1148[3]; n1148_4 = n1148[4];
  //   n1148_5 = n1148[5]; n1148_6 = n1148[6]; n1148_7 = n1148[7]; n1151_0 = n1151[0]; n1180[7:0] = n1151;
  //   n1151_1 = n1151[1]; n1151_2 = n1151[2]; n1151_3 = n1151[3]; n1151_4 = n1151[4]; n1151_5 = n1151[5];
  //   n1151_6 = n1151[6]; n1151_7 = n1151[7]; n1157_0 = n1157[0]; n1183[7:0] = n1157; n1157_1 = n1157[1];
  //   n1157_2 = n1157[2]; n1157_3 = n1157[3]; n1157_4 = n1157[4]; n1157_5 = n1157[5]; n1157_6 = n1157[6];
  //   n1157_7 = n1157[7]; n1160_0 = n1160[0]; n1185[7:0] = n1160; n1160_1 = n1160[1]; n1160_2 = n1160[2];
  //   n1160_3 = n1160[3]; n1160_4 = n1160[4]; n1160_5 = n1160[5]; n1160_6 = n1160[6]; n1160_7 = n1160[7];
  //   n1163_0 = n1163[0]; n1186[7:0] = n1163; n1163_1 = n1163[1]; n1163_2 = n1163[2]; n1163_3 = n1163[3];
  //   n1163_4 = n1163[4]; n1163_5 = n1163[5]; n1163_6 = n1163[6]; n1163_7 = n1163[7]; n1169_0 = n1169[0];
  //   n1189[7:0] = n1169; n1169_1 = n1169[1]; n1169_2 = n1169[2]; n1169_3 = n1169[3]; n1169_4 = n1169[4];
  //   n1169_5 = n1169[5]; n1169_6 = n1169[6]; n1169_7 = n1169[7]; n1190_0 = n1190[0]; n1201[7:0] = n1190;
  //   n1190_1 = n1190[1]; n1190_2 = n1190[2]; n1190_3 = n1190[3]; n1190_4 = n1190[4]; n1190_5 = n1190[5];
  //   n1190_6 = n1190[6]; n1190_7 = n1190[7]; n1172_0 = n1172[0]; n1191[7:0] = n1172; n1172_1 = n1172[1];
  //   n1172_2 = n1172[2]; n1172_3 = n1172[3]; n1172_4 = n1172[4]; n1172_5 = n1172[5]; n1172_6 = n1172[6];
  //   n1172_7 = n1172[7]; n1175_0 = n1175[0]; n1192[7:0] = n1175; n1175_1 = n1175[1]; n1175_2 = n1175[2];
  //   n1175_3 = n1175[3]; n1175_4 = n1175[4]; n1175_5 = n1175[5]; n1175_6 = n1175[6]; n1175_7 = n1175[7];
  //   n1079_0 = n1079[0]; n1195[7:0] = n1079; n1079_1 = n1079[1]; n1079_2 = n1079[2]; n1079_3 = n1079[3];
  //   n1079_4 = n1079[4]; n1079_5 = n1079[5]; n1079_6 = n1079[6]; n1079_7 = n1079[7]; n1181_0 = n1181[0];
  //   n1197[7:0] = n1181; n1181_1 = n1181[1]; n1181_2 = n1181[2]; n1181_3 = n1181[3]; n1181_4 = n1181[4];
  //   n1181_5 = n1181[5]; n1181_6 = n1181[6]; n1181_7 = n1181[7]; n1184_0 = n1184[0]; n1198[7:0] = n1184;
  //   n1184_1 = n1184[1]; n1184_2 = n1184[2]; n1184_3 = n1184[3]; n1184_4 = n1184[4]; n1184_5 = n1184[5];
  //   n1184_6 = n1184[6]; n1184_7 = n1184[7]; n1187_0 = n1187[0]; n1200[7:0] = n1187; n1187_1 = n1187[1];
  //   n1187_2 = n1187[2]; n1187_3 = n1187[3]; n1187_4 = n1187[4]; n1187_5 = n1187[5]; n1187_6 = n1187[6];
  //   n1187_7 = n1187[7]; n1202_0 = n1202[0]; n1207[7:0] = n1202; n1202_1 = n1202[1]; n1202_2 = n1202[2];
  //   n1202_3 = n1202[3]; n1202_4 = n1202[4]; n1202_5 = n1202[5]; n1202_6 = n1202[6]; n1202_7 = n1202[7];
  //   n1193_0 = n1193[0]; n1203[7:0] = n1193; n1193_1 = n1193[1]; n1193_2 = n1193[2]; n1193_3 = n1193[3];
  //   n1193_4 = n1193[4]; n1193_5 = n1193[5]; n1193_6 = n1193[6]; n1193_7 = n1193[7]; n1196_0 = n1196[0];
  //   n1204[7:0] = n1196; n1196_1 = n1196[1]; n1196_2 = n1196[2]; n1196_3 = n1196[3]; n1196_4 = n1196[4];
  //   n1196_5 = n1196[5]; n1196_6 = n1196[6]; n1196_7 = n1196[7]; n1199_0 = n1199[0]; n1206[7:0] = n1199;
  //   n1199_1 = n1199[1]; n1199_2 = n1199[2]; n1199_3 = n1199[3]; n1199_4 = n1199[4]; n1199_5 = n1199[5];
  //   n1199_6 = n1199[6]; n1199_7 = n1199[7]; n1208_0 = n1208[0]; n1209[7:0] = n1208; n1208_1 = n1208[1];
  //   n1208_2 = n1208[2]; n1208_3 = n1208[3]; n1208_4 = n1208[4]; n1208_5 = n1208[5]; n1208_6 = n1208[6];
  //   n1208_7 = n1208[7]; n1205_0 = n1205[0]; n1210[7:0] = n1205; n1205_1 = n1205[1]; n1205_2 = n1205[2];
  //   n1205_3 = n1205[3]; n1205_4 = n1205[4]; n1205_5 = n1205[5]; n1205_6 = n1205[6]; n1205_7 = n1205[7];
  //   n1211_0 = n1211[0]; n1212[7:0] = n1211; n1211_1 = n1211[1]; n1211_2 = n1211[2]; n1211_3 = n1211[3];
  //   n1211_4 = n1211[4]; n1211_5 = n1211[5]; n1211_6 = n1211[6]; n1211_7 = n1211[7];
  //   n1216[7:0] = {n362, n360, n358, n356, n354, n352, n350, n348};
  //   n1219[7:0] = {n362, n360, n358, n356, n354, n352, n350, n348}; n1217[15:0] = {16{n366}}; n1221_0 = n1221[0];
  //   n1229[15:0] = n1221; n1221_1 = n1221[1]; n1221_2 = n1221[2]; n1221_3 = n1221[3]; n1221_4 = n1221[4];
  //   n1221_5 = n1221[5]; n1221_6 = n1221[6]; n1221_7 = n1221[7]; n1221_8 = n1221[8]; n1221_9 = n1221[9];
  //   n1221_10 = n1221[10]; n1221_11 = n1221[11]; n1221_12 = n1221[12]; n1221_13 = n1221[13]; n1221_14 = n1221[14];
  //   n1221_15 = n1221[15];
  //   n1222[15:0] = {n411, n409, n407, n405, n403, n401, n399, n397, n395, n393, n391, n389, n387, n385, n383, n381};
  //   n1225[15:0] = {n472, n470, n468, n466, n464, n462, n460, n458, n456, n454, n452, n450, n448, n446, n444, n442};
  //   n1227_0 = n1227[0]; n1232[15:0] = n1227; n1227_1 = n1227[1]; n1227_2 = n1227[2]; n1227_3 = n1227[3];
  //   n1227_4 = n1227[4]; n1227_5 = n1227[5]; n1227_6 = n1227[6]; n1227_7 = n1227[7]; n1227_8 = n1227[8];
  //   n1227_9 = n1227[9]; n1227_10 = n1227[10]; n1227_11 = n1227[11]; n1227_12 = n1227[12]; n1227_13 = n1227[13];
  //   n1227_14 = n1227[14]; n1227_15 = n1227[15]; n1218_0 = n1218[0]; n1228[15:0] = n1218; n1218_1 = n1218[1];
  //   n1218_2 = n1218[2]; n1218_3 = n1218[3]; n1218_4 = n1218[4]; n1218_5 = n1218[5]; n1218_6 = n1218[6];
  //   n1218_7 = n1218[7]; n1218_8 = n1218[8]; n1218_9 = n1218[9]; n1218_10 = n1218[10]; n1218_11 = n1218[11];
  //   n1218_12 = n1218[12]; n1218_13 = n1218[13]; n1218_14 = n1218[14]; n1218_15 = n1218[15]; n1224_0 = n1224[0];
  //   n1231[15:0] = n1224; n1224_1 = n1224[1]; n1224_2 = n1224[2]; n1224_3 = n1224[3]; n1224_4 = n1224[4];
  //   n1224_5 = n1224[5]; n1224_6 = n1224[6]; n1224_7 = n1224[7]; n1224_8 = n1224[8]; n1224_9 = n1224[9];
  //   n1224_10 = n1224[10]; n1224_11 = n1224[11]; n1224_12 = n1224[12]; n1224_13 = n1224[13]; n1224_14 = n1224[14];
  //   n1224_15 = n1224[15]; n1233_0 = n1233[0]; n1235[15:0] = n1233; n1233_1 = n1233[1]; n1233_2 = n1233[2];
  //   n1233_3 = n1233[3]; n1233_4 = n1233[4]; n1233_5 = n1233[5]; n1233_6 = n1233[6]; n1233_7 = n1233[7];
  //   n1233_8 = n1233[8]; n1233_9 = n1233[9]; n1233_10 = n1233[10]; n1233_11 = n1233[11]; n1233_12 = n1233[12];
  //   n1233_13 = n1233[13]; n1233_14 = n1233[14]; n1233_15 = n1233[15]; n1230_0 = n1230[0]; n1234[15:0] = n1230;
  //   n1230_1 = n1230[1]; n1230_2 = n1230[2]; n1230_3 = n1230[3]; n1230_4 = n1230[4]; n1230_5 = n1230[5];
  //   n1230_6 = n1230[6]; n1230_7 = n1230[7]; n1230_8 = n1230[8]; n1230_9 = n1230[9]; n1230_10 = n1230[10];
  //   n1230_11 = n1230[11]; n1230_12 = n1230[12]; n1230_13 = n1230[13]; n1230_14 = n1230[14]; n1230_15 = n1230[15];
  //   n1236_0 = n1236[0]; n1237[15:0] = n1236; n1236_1 = n1236[1]; n1236_2 = n1236[2]; n1236_3 = n1236[3];
  //   n1236_4 = n1236[4]; n1236_5 = n1236[5]; n1236_6 = n1236[6]; n1236_7 = n1236[7]; n1236_8 = n1236[8];
  //   n1236_9 = n1236[9]; n1236_10 = n1236[10]; n1236_11 = n1236[11]; n1236_12 = n1236[12]; n1236_13 = n1236[13];
  //   n1236_14 = n1236[14]; n1236_15 = n1236[15]; DataIn_0 = DataIn[0]; n765[7:0] = DataIn;
  //   n807 (some bits) = {DataIn[7:6], DataIn[3:0]}; n833[15:8] = DataIn; n897[7:0] = DataIn; n1239[7:0] = DataIn;
  //   n1242[7:0] = DataIn; n1253[7:0] = DataIn; n1256[7:0] = DataIn; n1259[7:0] = DataIn; n1262[7:0] = DataIn;
  //   n1265[7:0] = DataIn; DataIn_1 = DataIn[1]; DataIn_2 = DataIn[2]; DataIn_3 = DataIn[3]; DataIn_4 = DataIn[4];
  //   DataIn_5 = DataIn[5]; DataIn_6 = DataIn[6]; DataIn_7 = DataIn[7]; n982[7:0] = {8{n333}}; n1240[7:0] = {8{n333}};
  //   n1241_0 = n1241[0]; n1245[7:0] = n1241; n1241_1 = n1241[1]; n1241_2 = n1241[2]; n1241_3 = n1241[3];
  //   n1241_4 = n1241[4]; n1241_5 = n1241[5]; n1241_6 = n1241[6]; n1241_7 = n1241[7]; n1244_0 = n1244[0];
  //   n1246[7:0] = n1244; n1244_1 = n1244[1]; n1244_2 = n1244[2]; n1244_3 = n1244[3]; n1244_4 = n1244[4];
  //   n1244_5 = n1244[5]; n1244_6 = n1244[6]; n1244_7 = n1244[7]; n1247_0 = n1247[0]; n1248[7:0] = n1247;
  //   n1247_1 = n1247[1]; n1247_2 = n1247[2]; n1247_3 = n1247[3]; n1247_4 = n1247[4]; n1247_5 = n1247[5];
  //   n1247_6 = n1247[6]; n1247_7 = n1247[7]; n985[7:0] = {8{n337}}; n1257[7:0] = {8{n337}}; n1258_0 = n1258[0];
  //   n1269[7:0] = n1258; n1258_1 = n1258[1]; n1258_2 = n1258[2]; n1258_3 = n1258[3]; n1258_4 = n1258[4];
  //   n1258_5 = n1258[5]; n1258_6 = n1258[6]; n1258_7 = n1258[7]; n1261_0 = n1261[0]; n1271[7:0] = n1261;
  //   n1261_1 = n1261[1]; n1261_2 = n1261[2]; n1261_3 = n1261[3]; n1261_4 = n1261[4]; n1261_5 = n1261[5];
  //   n1261_6 = n1261[6]; n1261_7 = n1261[7]; n1263[7:0] = {8{n576}}; n1264_0 = n1264[0]; n1272[7:0] = n1264;
  //   n1264_1 = n1264[1]; n1264_2 = n1264[2]; n1264_3 = n1264[3]; n1264_4 = n1264[4]; n1264_5 = n1264[5];
  //   n1264_6 = n1264[6]; n1264_7 = n1264[7]; n1267_0 = n1267[0]; n1278[7:0] = n1267; n1267_1 = n1267[1];
  //   n1267_2 = n1267[2]; n1267_3 = n1267[3]; n1267_4 = n1267[4]; n1267_5 = n1267[5]; n1267_6 = n1267[6];
  //   n1267_7 = n1267[7]; n1255_0 = n1255[0]; n1268[7:0] = n1255; n1255_1 = n1255[1]; n1255_2 = n1255[2];
  //   n1255_3 = n1255[3]; n1255_4 = n1255[4]; n1255_5 = n1255[5]; n1255_6 = n1255[6]; n1255_7 = n1255[7];
  //   n1270_0 = n1270[0]; n1274[7:0] = n1270; n1270_1 = n1270[1]; n1270_2 = n1270[2]; n1270_3 = n1270[3];
  //   n1270_4 = n1270[4]; n1270_5 = n1270[5]; n1270_6 = n1270[6]; n1270_7 = n1270[7]; n1273_0 = n1273[0];
  //   n1275[7:0] = n1273; n1273_1 = n1273[1]; n1273_2 = n1273[2]; n1273_3 = n1273[3]; n1273_4 = n1273[4];
  //   n1273_5 = n1273[5]; n1273_6 = n1273[6]; n1273_7 = n1273[7]; n1276_0 = n1276[0]; n1277[7:0] = n1276;
  //   n1276_1 = n1276[1]; n1276_2 = n1276[2]; n1276_3 = n1276[3]; n1276_4 = n1276[4]; n1276_5 = n1276[5];
  //   n1276_6 = n1276[6]; n1276_7 = n1276[7]; n1279_0 = n1279[0]; n1280[7:0] = n1279; n1279_1 = n1279[1];
  //   n1279_2 = n1279[2]; n1279_3 = n1279[3]; n1279_4 = n1279[4]; n1279_5 = n1279[5]; n1279_6 = n1279[6];
  //   n1279_7 = n1279[7]; n1030[7:0] = {8{n479}}; n1282[7:0] = {8{n479}}; n1283_0 = n1283[0]; n1284[7:0] = n1283;
  //   n1283_1 = n1283[1]; n1283_2 = n1283[2]; n1283_3 = n1283[3]; n1283_4 = n1283[4]; n1283_5 = n1283[5];
  //   n1283_6 = n1283[6]; n1283_7 = n1283[7]; n1286[0] = n303; n1288_0 = n1288[0]; n1292[7:0] = n1288;
  //   n1288_1 = n1288[1]; n1288_2 = n1288[2]; n1288_3 = n1288[3]; n1288_4 = n1288[4]; n1288_5 = n1288[5];
  //   n1288_6 = n1288[6]; n1288_7 = n1288[7]; n1291_0 = n1291[0]; n1293[7:0] = n1291; n1291_1 = n1291[1];
  //   n1291_2 = n1291[2]; n1291_3 = n1291[3]; n1291_4 = n1291[4]; n1291_5 = n1291[5]; n1291_6 = n1291[6];
  //   n1291_7 = n1291[7]; n1294_0 = n1294[0]; n1295[7:0] = n1294; n1294_1 = n1294[1]; n1294_2 = n1294[2];
  //   n1294_3 = n1294[3]; n1294_4 = n1294[4]; n1294_5 = n1294[5]; n1294_6 = n1294[6]; n1294_7 = n1294[7]; n1296 = NMI;
  //   P_4 = P[4]; P_5 = P[5]; n647[7:0] = SP; SP_0 = SP[0]; SP_1 = SP[1]; SP_2 = SP[2]; SP_3 = SP[3]; SP_4 = SP[4];
  //   SP_5 = SP[5]; SP_6 = SP[6]; SP_7 = SP[7]; State_0 = State[0]; State_1 = State[1]; State_2 = State[2];
  //   State_3 = State[3]; State_4 = State[4]; State_5 = State[5]; State_6 = State[6]; State_7 = State[7]

  // Notes on the sheet:
  //   BITWRIGHT / original NMOS 6502 instruction behavior, hardwired multi-cycle gate CPU; storage also built from gates
  //   Rising edge: CPU reads / updates. Falling edge: external writes. Not cycle-accurate; unsupported opcodes fault.
  //   Program counter and stack pointer arithmetic
  //   Reset vector, fetch and instruction dispatch
  //   Addressing modes and operand reads
  //   ALU interface and destination register enables
  //   Conditional branches and jumps
  //   Stack, subroutines, BRK, IRQ and NMI
  //   External memory read / write bus
  //   State and register storage banks
endmodule
