// Logisim project foundations.circ as structural Verilog: 2 circuits, main circuit LoadBit
module GateAnd (
  input  A,
  input  B,
  output Y
);

  and and_1 (Y, A, B);

  // Notes on the sheet:
  //   M0 / AND truth table
endmodule

module LoadBit (
  input  Data,
  input  Load,
  input  Clock,
  input  Reset,
  output Q
);

  wire D, Hold, New, Old;

  not not_1 (Hold, Load);
  and and_1 (New, Data, Load);
  and and_2 (Old, Q, Hold);
  or or_1 (D, New, Old);
  D_Flip_Flop #(.trigger("rising")) \bit  (.clk(Clock), .D(D), .Q(Q), .preset(1'b0), .reset(Reset));  // open: Qn

  // Notes on the sheet:
  //   M0 / one bit: Q(next) = Load ? Data : Q; async Reset wins
  //   Selection uses NOT / AND / OR gates. Only the single-bit D flip-flop is a foundation.
  //   Use the ordinary Clock input pin in sequential vectors.
endmodule
