// Logisim project never-halt.circ as structural Verilog: 1 circuit, main circuit NeverHalt
module NeverHalt (
  output clock_seen,
  output halt
);

  Clock clock_1 (.out(clock_seen));

  assign halt = 1'b0;

  // Notes on the sheet:
  //   Intentional non-termination fixture: runner must enforce a timeout
endmodule
