// Logisim project ram-harness.circ as structural Verilog: 1 circuit, main circuit RamHarness
module RamHarness (
  output halt,
  output pass,
  output [7:0] signature
);

  wire Clock, highOK, lowOK, n1, n3, n4, n6, p0, p1, p2, p3, stage1;

  Clock #(.highDuration(1), .lowDuration(1)) clock_1 (.out(Clock));
  RAM #(.addrWidth(4), .dataWidth(8), .databus("bibus"), .enables("byte"), .asyncread("true"), .trigger("falling"), .clearpin("false")) M0_RAM (
    .addr(4'b0000), .we(1'b0), .oe(1'b1), .clk(Clock), .din({8{1'b0}}), .dout(signature));
  D_Flip_Flop #(.trigger("rising")) first_tick (
    .clk(Clock), .D(1'b1), .Q(stage1), .preset(1'b0), .reset(1'b0));  // open: Qn
  D_Flip_Flop #(.trigger("rising")) second_tick (
    .clk(Clock), .D(stage1), .Q(halt), .preset(1'b0), .reset(1'b0));  // open: Qn
  not not_1 (n1, signature[1]);
  not not_2 (n3, signature[3]);
  not not_3 (n4, signature[4]);
  not not_4 (n6, signature[6]);
  and and_1 (p0, signature[0], n1);
  and and_2 (p1, signature[2], n3);
  and and_3 (p2, n4, signature[5]);
  and and_4 (p3, n6, signature[7]);
  and and_5 (lowOK, p0, p1);
  and and_6 (highOK, p2, p3);
  and and_7 (pass, lowOK, highOK);

  // Other names for the same wires on the sheet: b0 = signature[0]; b1 = signature[1]; b2 = signature[2];
  //   b3 = signature[3]; b4 = signature[4]; b5 = signature[5]; b6 = signature[6]; b7 = signature[7]

  // Notes on the sheet:
  //   M0 / labelled RAM loading + bounded clocked result
  //   Load bank M0_RAM. Address 0 must be A5. halt after two rising edges; pass is a gate-built equality check.
endmodule
