// Logisim project terminal.circ as structural Verilog: 19 circuits, main circuit Apple1Console
module ConsoleMux1 (
  input  A,
  input  B,
  input  Select,
  output Y
);

  wire and_2, and_3, not_1;

  not u_not_1 (not_1, Select);
  and and_1 (and_2, A, not_1);
  and u_and_2 (and_3, B, Select);
  or or_1 (Y, and_2, and_3);

  // Notes on the sheet:
  //   ConsoleMux1 / gates, wiring, explicit single-bit flip-flops; bulk RAM and font ROM only
endmodule

module ConsoleMux3 (
  input  [2:0] A,
  input  [2:0] B,
  input  Select,
  output [2:0] Y
);

  wire [2:0] and_3, and_4, not_2;

  assign not_2 = ~{3{Select}};  // NOT_Gate not_1, 3 bits wide
  assign and_3 = A & not_2;  // AND_Gate and_1, 3 bits wide
  assign and_4 = B & {3{Select}};  // AND_Gate and_2, 3 bits wide
  assign Y = and_3 | and_4;  // OR_Gate or_1, 3 bits wide

  // Other names for the same wires on the sheet: bus_1[2:0] = {3{Select}}

  // Notes on the sheet:
  //   ConsoleMux3 / gates, wiring, explicit single-bit flip-flops; bulk RAM and font ROM only
endmodule

module ConsoleMux5 (
  input  [4:0] A,
  input  [4:0] B,
  input  Select,
  output [4:0] Y
);

  wire [4:0] and_3, and_4, not_2;

  assign not_2 = ~{5{Select}};  // NOT_Gate not_1, 5 bits wide
  assign and_3 = A & not_2;  // AND_Gate and_1, 5 bits wide
  assign and_4 = B & {5{Select}};  // AND_Gate and_2, 5 bits wide
  assign Y = and_3 | and_4;  // OR_Gate or_1, 5 bits wide

  // Other names for the same wires on the sheet: bus_1[4:0] = {5{Select}}

  // Notes on the sheet:
  //   ConsoleMux5 / gates, wiring, explicit single-bit flip-flops; bulk RAM and font ROM only
endmodule

module ConsoleMux6 (
  input  [5:0] A,
  input  [5:0] B,
  input  Select,
  output [5:0] Y
);

  wire [5:0] and_3, and_4, not_2;

  assign not_2 = ~{6{Select}};  // NOT_Gate not_1, 6 bits wide
  assign and_3 = A & not_2;  // AND_Gate and_1, 6 bits wide
  assign and_4 = B & {6{Select}};  // AND_Gate and_2, 6 bits wide
  assign Y = and_3 | and_4;  // OR_Gate or_1, 6 bits wide

  // Other names for the same wires on the sheet: bus_1[5:0] = {6{Select}}

  // Notes on the sheet:
  //   ConsoleMux6 / gates, wiring, explicit single-bit flip-flops; bulk RAM and font ROM only
endmodule

module ConsoleMux7 (
  input  [6:0] A,
  input  [6:0] B,
  input  Select,
  output [6:0] Y
);

  wire [6:0] and_3, and_4, not_2;

  assign not_2 = ~{7{Select}};  // NOT_Gate not_1, 7 bits wide
  assign and_3 = A & not_2;  // AND_Gate and_1, 7 bits wide
  assign and_4 = B & {7{Select}};  // AND_Gate and_2, 7 bits wide
  assign Y = and_3 | and_4;  // OR_Gate or_1, 7 bits wide

  // Other names for the same wires on the sheet: bus_1[6:0] = {7{Select}}

  // Notes on the sheet:
  //   ConsoleMux7 / gates, wiring, explicit single-bit flip-flops; bulk RAM and font ROM only
endmodule

module ConsoleMux8 (
  input  [7:0] A,
  input  [7:0] B,
  input  Select,
  output [7:0] Y
);

  wire [7:0] and_3, and_4, not_2;

  assign not_2 = ~{8{Select}};  // NOT_Gate not_1, 8 bits wide
  assign and_3 = A & not_2;  // AND_Gate and_1, 8 bits wide
  assign and_4 = B & {8{Select}};  // AND_Gate and_2, 8 bits wide
  assign Y = and_3 | and_4;  // OR_Gate or_1, 8 bits wide

  // Other names for the same wires on the sheet: bus_1[7:0] = {8{Select}}

  // Notes on the sheet:
  //   ConsoleMux8 / gates, wiring, explicit single-bit flip-flops; bulk RAM and font ROM only
endmodule

module ConsoleMux11 (
  input  [10:0] A,
  input  [10:0] B,
  input  Select,
  output [10:0] Y
);

  wire [10:0] and_3, and_4, not_2;

  assign not_2 = ~{11{Select}};  // NOT_Gate not_1, 11 bits wide
  assign and_3 = A & not_2;  // AND_Gate and_1, 11 bits wide
  assign and_4 = B & {11{Select}};  // AND_Gate and_2, 11 bits wide
  assign Y = and_3 | and_4;  // OR_Gate or_1, 11 bits wide

  // Other names for the same wires on the sheet: bus_1[10:0] = {11{Select}}

  // Notes on the sheet:
  //   ConsoleMux11 / gates, wiring, explicit single-bit flip-flops; bulk RAM and font ROM only
endmodule

module ConsoleAdd3 (
  input  [2:0] A,
  input  [2:0] B,
  output [2:0] Y
);

  wire and_10, and_11, and_15, and_16, and_20, and_21, or_12, or_17, or_22, xor_8, xor_13, xor_18;

  and and_1 (and_11, xor_8, 1'b0);
  or or_1 (or_17, and_15, and_16);
  or or_2 (or_12, and_10, and_11);
  xor xor_1 (xor_18, A[2], B[2]);
  xor xor_2 (xor_13, A[1], B[1]);
  xor xor_3 (Y[2], xor_18, or_17);
  xor xor_4 (xor_8, A[0], B[0]);
  xor xor_5 (Y[1], xor_13, or_12);
  and and_2 (and_20, A[2], B[2]);
  xor xor_6 (Y[0], xor_8, 1'b0);
  and and_3 (and_15, A[1], B[1]);
  and and_4 (and_21, xor_18, or_17);
  and and_5 (and_10, A[0], B[0]);
  and and_6 (and_16, xor_13, or_12);
  or or_3 (or_22, and_20, and_21);

  // Other names for the same wires on the sheet: bit_1 = A[0]; bit_2 = A[1]; bit_3 = A[2]; bit_4 = B[0]; bit_5 = B[1];
  //   bit_6 = B[2]; xor_9 = Y[0]; xor_14 = Y[1]; xor_19 = Y[2]

  // Notes on the sheet:
  //   ConsoleAdd3 / gates, wiring, explicit single-bit flip-flops; bulk RAM and font ROM only
endmodule

module ConsoleAdd5 (
  input  [4:0] A,
  input  [4:0] B,
  output [4:0] Y
);

  wire and_14, and_15, and_19, and_20, and_24, and_25, and_29, and_30, and_34, and_35, or_16, or_21, or_26,
       or_31, or_36, xor_12, xor_17, xor_22, xor_27, xor_32;

  and and_1 (and_15, xor_12, 1'b0);
  or or_1 (or_21, and_19, and_20);
  xor xor_1 (xor_27, A[3], B[3]);
  xor xor_2 (Y[4], xor_32, or_31);
  or or_2 (or_16, and_14, and_15);
  xor xor_3 (xor_22, A[2], B[2]);
  xor xor_4 (Y[3], xor_27, or_26);
  and and_2 (and_34, A[4], B[4]);
  xor xor_5 (xor_17, A[1], B[1]);
  xor xor_6 (Y[2], xor_22, or_21);
  and and_3 (and_29, A[3], B[3]);
  and and_4 (and_35, xor_32, or_31);
  xor xor_7 (xor_12, A[0], B[0]);
  xor xor_8 (Y[1], xor_17, or_16);
  and and_5 (and_24, A[2], B[2]);
  and and_6 (and_30, xor_27, or_26);
  or or_3 (or_36, and_34, and_35);
  xor xor_9 (Y[0], xor_12, 1'b0);
  and and_7 (and_19, A[1], B[1]);
  and and_8 (and_25, xor_22, or_21);
  or or_4 (or_31, and_29, and_30);
  and and_9 (and_14, A[0], B[0]);
  and and_10 (and_20, xor_17, or_16);
  or or_5 (or_26, and_24, and_25);
  xor xor_10 (xor_32, A[4], B[4]);

  // Other names for the same wires on the sheet: bit_1 = A[0]; bit_2 = A[1]; bit_3 = A[2]; bit_4 = A[3]; bit_5 = A[4];
  //   bit_6 = B[0]; bit_7 = B[1]; bit_8 = B[2]; bit_9 = B[3]; bit_10 = B[4]; xor_13 = Y[0]; xor_18 = Y[1];
  //   xor_23 = Y[2]; xor_28 = Y[3]; xor_33 = Y[4]

  // Notes on the sheet:
  //   ConsoleAdd5 / gates, wiring, explicit single-bit flip-flops; bulk RAM and font ROM only
endmodule

module ConsoleAdd6 (
  input  [5:0] A,
  input  [5:0] B,
  output [5:0] Y
);

  wire and_16, and_17, and_21, and_22, and_26, and_27, and_31, and_32, and_36, and_37, and_41, and_42, or_18,
       or_23, or_28, or_33, or_38, or_43, xor_14, xor_19, xor_24, xor_29, xor_34, xor_39;

  and and_1 (and_17, xor_14, 1'b0);
  or or_1 (or_23, and_21, and_22);
  xor xor_1 (xor_29, A[3], B[3]);
  xor xor_2 (Y[4], xor_34, or_33);
  and and_2 (and_41, A[5], B[5]);
  or or_2 (or_18, and_16, and_17);
  xor xor_3 (xor_24, A[2], B[2]);
  xor xor_4 (Y[3], xor_29, or_28);
  and and_3 (and_36, A[4], B[4]);
  and and_4 (and_42, xor_39, or_38);
  xor xor_5 (xor_19, A[1], B[1]);
  xor xor_6 (Y[2], xor_24, or_23);
  and and_5 (and_31, A[3], B[3]);
  and and_6 (and_37, xor_34, or_33);
  or or_3 (or_43, and_41, and_42);
  xor xor_7 (xor_14, A[0], B[0]);
  xor xor_8 (Y[1], xor_19, or_18);
  and and_7 (and_26, A[2], B[2]);
  and and_8 (and_32, xor_29, or_28);
  or or_4 (or_38, and_36, and_37);
  xor xor_9 (Y[0], xor_14, 1'b0);
  and and_9 (and_21, A[1], B[1]);
  and and_10 (and_27, xor_24, or_23);
  or or_5 (or_33, and_31, and_32);
  xor xor_10 (xor_39, A[5], B[5]);
  and and_11 (and_16, A[0], B[0]);
  and and_12 (and_22, xor_19, or_18);
  or or_6 (or_28, and_26, and_27);
  xor xor_11 (xor_34, A[4], B[4]);
  xor xor_12 (Y[5], xor_39, or_38);

  // Other names for the same wires on the sheet: bit_1 = A[0]; bit_2 = A[1]; bit_3 = A[2]; bit_4 = A[3]; bit_5 = A[4];
  //   bit_6 = A[5]; bit_7 = B[0]; bit_8 = B[1]; bit_9 = B[2]; bit_10 = B[3]; bit_11 = B[4]; bit_12 = B[5];
  //   xor_15 = Y[0]; xor_20 = Y[1]; xor_25 = Y[2]; xor_30 = Y[3]; xor_35 = Y[4]; xor_40 = Y[5]

  // Notes on the sheet:
  //   ConsoleAdd6 / gates, wiring, explicit single-bit flip-flops; bulk RAM and font ROM only
endmodule

module ConsoleAdd8 (
  input  [7:0] A,
  input  [7:0] B,
  output [7:0] Y
);

  wire and_20, and_21, and_25, and_26, and_30, and_31, and_35, and_36, and_40, and_41, and_45, and_46,
       and_50, and_51, and_55, and_56, or_22, or_27, or_32, or_37, or_42, or_47, or_52, or_57, xor_18,
       xor_23, xor_28, xor_33, xor_38, xor_43, xor_48, xor_53;

  and and_1 (and_21, xor_18, 1'b0);
  or or_1 (or_27, and_25, and_26);
  xor xor_1 (xor_33, A[3], B[3]);
  xor xor_2 (Y[4], xor_38, or_37);
  and and_2 (and_45, A[5], B[5]);
  and and_3 (and_51, xor_48, or_47);
  or or_2 (or_57, and_55, and_56);
  or or_3 (or_22, and_20, and_21);
  xor xor_3 (xor_28, A[2], B[2]);
  xor xor_4 (Y[3], xor_33, or_32);
  and and_4 (and_40, A[4], B[4]);
  and and_5 (and_46, xor_43, or_42);
  or or_4 (or_52, and_50, and_51);
  xor xor_5 (xor_23, A[1], B[1]);
  xor xor_6 (Y[2], xor_28, or_27);
  and and_6 (and_35, A[3], B[3]);
  and and_7 (and_41, xor_38, or_37);
  or or_5 (or_47, and_45, and_46);
  xor xor_7 (xor_53, A[7], B[7]);
  xor xor_8 (xor_18, A[0], B[0]);
  xor xor_9 (Y[1], xor_23, or_22);
  and and_8 (and_30, A[2], B[2]);
  and and_9 (and_36, xor_33, or_32);
  or or_6 (or_42, and_40, and_41);
  xor xor_10 (xor_48, A[6], B[6]);
  xor xor_11 (Y[7], xor_53, or_52);
  xor xor_12 (Y[0], xor_18, 1'b0);
  and and_10 (and_25, A[1], B[1]);
  and and_11 (and_31, xor_28, or_27);
  or or_7 (or_37, and_35, and_36);
  xor xor_13 (xor_43, A[5], B[5]);
  xor xor_14 (Y[6], xor_48, or_47);
  and and_12 (and_55, A[7], B[7]);
  and and_13 (and_20, A[0], B[0]);
  and and_14 (and_26, xor_23, or_22);
  or or_8 (or_32, and_30, and_31);
  xor xor_15 (xor_38, A[4], B[4]);
  xor xor_16 (Y[5], xor_43, or_42);
  and and_15 (and_50, A[6], B[6]);
  and and_16 (and_56, xor_53, or_52);

  // Other names for the same wires on the sheet: bit_1 = A[0]; bit_2 = A[1]; bit_3 = A[2]; bit_4 = A[3]; bit_5 = A[4];
  //   bit_6 = A[5]; bit_7 = A[6]; bit_8 = A[7]; bit_9 = B[0]; bit_10 = B[1]; bit_11 = B[2]; bit_12 = B[3];
  //   bit_13 = B[4]; bit_14 = B[5]; bit_15 = B[6]; bit_16 = B[7]; xor_19 = Y[0]; xor_24 = Y[1]; xor_29 = Y[2];
  //   xor_34 = Y[3]; xor_39 = Y[4]; xor_44 = Y[5]; xor_49 = Y[6]; xor_54 = Y[7]

  // Notes on the sheet:
  //   ConsoleAdd8 / gates, wiring, explicit single-bit flip-flops; bulk RAM and font ROM only
endmodule

module ConsoleRegister1 (
  input  Data,
  input  Load,
  input  Clock,
  input  Reset,
  output Q
);

  wire mux_1;

  ConsoleMux1 consolemux1_1 (.A(Q), .B(Data), .Select(Load), .Y(mux_1));
  D_Flip_Flop #(.trigger("rising")) bit0 (.clk(Clock), .D(mux_1), .Q(Q), .preset(1'b0), .reset(Reset));  // open: Qn

  // Other names for the same wires on the sheet: q_2 = Q

  // Notes on the sheet:
  //   ConsoleRegister1 / gates, wiring, explicit single-bit flip-flops; bulk RAM and font ROM only
endmodule

module ConsoleRegister3 (
  input  [2:0] Data,
  input  Load,
  input  Clock,
  input  Reset,
  output [2:0] Q
);

  wire bit_2, bit_3, bit_4;

  ConsoleMux3 consolemux3_1 (.A(Q), .B(Data), .Select(Load), .Y({bit_4, bit_3, bit_2}));
  D_Flip_Flop #(.trigger("rising")) bit0 (.clk(Clock), .D(bit_2), .Q(Q[0]), .preset(1'b0), .reset(Reset));  // open: Qn
  D_Flip_Flop #(.trigger("rising")) bit1 (.clk(Clock), .D(bit_3), .Q(Q[1]), .preset(1'b0), .reset(Reset));  // open: Qn
  D_Flip_Flop #(.trigger("rising")) bit2 (.clk(Clock), .D(bit_4), .Q(Q[2]), .preset(1'b0), .reset(Reset));  // open: Qn

  // Other names for the same wires on the sheet: mux_1[2:0] = {bit_4, bit_3, bit_2}; q_5 = Q[0]; q_6 = Q[1];
  //   q_7 = Q[2]

  // Notes on the sheet:
  //   ConsoleRegister3 / gates, wiring, explicit single-bit flip-flops; bulk RAM and font ROM only
endmodule

module ConsoleRegister5 (
  input  [4:0] Data,
  input  Load,
  input  Clock,
  input  Reset,
  output [4:0] Q
);

  wire bit_2, bit_3, bit_4, bit_5, bit_6;

  ConsoleMux5 consolemux5_1 (.A(Q), .B(Data), .Select(Load), .Y({bit_6, bit_5, bit_4, bit_3, bit_2}));
  D_Flip_Flop #(.trigger("rising")) bit4 (.clk(Clock), .D(bit_6), .Q(Q[4]), .preset(1'b0), .reset(Reset));  // open: Qn
  D_Flip_Flop #(.trigger("rising")) bit0 (.clk(Clock), .D(bit_2), .Q(Q[0]), .preset(1'b0), .reset(Reset));  // open: Qn
  D_Flip_Flop #(.trigger("rising")) bit1 (.clk(Clock), .D(bit_3), .Q(Q[1]), .preset(1'b0), .reset(Reset));  // open: Qn
  D_Flip_Flop #(.trigger("rising")) bit2 (.clk(Clock), .D(bit_4), .Q(Q[2]), .preset(1'b0), .reset(Reset));  // open: Qn
  D_Flip_Flop #(.trigger("rising")) bit3 (.clk(Clock), .D(bit_5), .Q(Q[3]), .preset(1'b0), .reset(Reset));  // open: Qn

  // Other names for the same wires on the sheet: mux_1[4:0] = {bit_6, bit_5, bit_4, bit_3, bit_2}; q_7 = Q[0];
  //   q_8 = Q[1]; q_9 = Q[2]; q_10 = Q[3]; q_11 = Q[4]

  // Notes on the sheet:
  //   ConsoleRegister5 / gates, wiring, explicit single-bit flip-flops; bulk RAM and font ROM only
endmodule

module ConsoleRegister6 (
  input  [5:0] Data,
  input  Load,
  input  Clock,
  input  Reset,
  output [5:0] Q
);

  wire bit_2, bit_3, bit_4, bit_5, bit_6, bit_7;

  ConsoleMux6 consolemux6_1 (.A(Q), .B(Data), .Select(Load), .Y({bit_7, bit_6, bit_5, bit_4, bit_3, bit_2}));
  D_Flip_Flop #(.trigger("rising")) bit4 (.clk(Clock), .D(bit_6), .Q(Q[4]), .preset(1'b0), .reset(Reset));  // open: Qn
  D_Flip_Flop #(.trigger("rising")) bit5 (.clk(Clock), .D(bit_7), .Q(Q[5]), .preset(1'b0), .reset(Reset));  // open: Qn
  D_Flip_Flop #(.trigger("rising")) bit0 (.clk(Clock), .D(bit_2), .Q(Q[0]), .preset(1'b0), .reset(Reset));  // open: Qn
  D_Flip_Flop #(.trigger("rising")) bit1 (.clk(Clock), .D(bit_3), .Q(Q[1]), .preset(1'b0), .reset(Reset));  // open: Qn
  D_Flip_Flop #(.trigger("rising")) bit2 (.clk(Clock), .D(bit_4), .Q(Q[2]), .preset(1'b0), .reset(Reset));  // open: Qn
  D_Flip_Flop #(.trigger("rising")) bit3 (.clk(Clock), .D(bit_5), .Q(Q[3]), .preset(1'b0), .reset(Reset));  // open: Qn

  // Other names for the same wires on the sheet: mux_1[5:0] = {bit_7, bit_6, bit_5, bit_4, bit_3, bit_2}; q_8 = Q[0];
  //   q_9 = Q[1]; q_10 = Q[2]; q_11 = Q[3]; q_12 = Q[4]; q_13 = Q[5]

  // Notes on the sheet:
  //   ConsoleRegister6 / gates, wiring, explicit single-bit flip-flops; bulk RAM and font ROM only
endmodule

module ConsoleRegister7 (
  input  [6:0] Data,
  input  Load,
  input  Clock,
  input  Reset,
  output [6:0] Q
);

  wire bit_2, bit_3, bit_4, bit_5, bit_6, bit_7, bit_8;

  ConsoleMux7 consolemux7_1 (.A(Q), .B(Data), .Select(Load), .Y({bit_8, bit_7, bit_6, bit_5, bit_4, bit_3, bit_2}));
  D_Flip_Flop #(.trigger("rising")) bit4 (.clk(Clock), .D(bit_6), .Q(Q[4]), .preset(1'b0), .reset(Reset));  // open: Qn
  D_Flip_Flop #(.trigger("rising")) bit5 (.clk(Clock), .D(bit_7), .Q(Q[5]), .preset(1'b0), .reset(Reset));  // open: Qn
  D_Flip_Flop #(.trigger("rising")) bit0 (.clk(Clock), .D(bit_2), .Q(Q[0]), .preset(1'b0), .reset(Reset));  // open: Qn
  D_Flip_Flop #(.trigger("rising")) bit6 (.clk(Clock), .D(bit_8), .Q(Q[6]), .preset(1'b0), .reset(Reset));  // open: Qn
  D_Flip_Flop #(.trigger("rising")) bit1 (.clk(Clock), .D(bit_3), .Q(Q[1]), .preset(1'b0), .reset(Reset));  // open: Qn
  D_Flip_Flop #(.trigger("rising")) bit2 (.clk(Clock), .D(bit_4), .Q(Q[2]), .preset(1'b0), .reset(Reset));  // open: Qn
  D_Flip_Flop #(.trigger("rising")) bit3 (.clk(Clock), .D(bit_5), .Q(Q[3]), .preset(1'b0), .reset(Reset));  // open: Qn

  // Other names for the same wires on the sheet: mux_1[6:0] = {bit_8, bit_7, bit_6, bit_5, bit_4, bit_3, bit_2};
  //   q_9 = Q[0]; q_10 = Q[1]; q_11 = Q[2]; q_12 = Q[3]; q_13 = Q[4]; q_14 = Q[5]; q_15 = Q[6]

  // Notes on the sheet:
  //   ConsoleRegister7 / gates, wiring, explicit single-bit flip-flops; bulk RAM and font ROM only
endmodule

module ConsoleRegister8 (
  input  [7:0] Data,
  input  Load,
  input  Clock,
  input  Reset,
  output [7:0] Q
);

  wire bit_2, bit_3, bit_4, bit_5, bit_6, bit_7, bit_8, bit_9;

  ConsoleMux8 consolemux8_1 (
    .A(Q), .B(Data), .Select(Load), .Y({bit_9, bit_8, bit_7, bit_6, bit_5, bit_4, bit_3, bit_2}));
  D_Flip_Flop #(.trigger("rising")) bit4 (.clk(Clock), .D(bit_6), .Q(Q[4]), .preset(1'b0), .reset(Reset));  // open: Qn
  D_Flip_Flop #(.trigger("rising")) bit5 (.clk(Clock), .D(bit_7), .Q(Q[5]), .preset(1'b0), .reset(Reset));  // open: Qn
  D_Flip_Flop #(.trigger("rising")) bit0 (.clk(Clock), .D(bit_2), .Q(Q[0]), .preset(1'b0), .reset(Reset));  // open: Qn
  D_Flip_Flop #(.trigger("rising")) bit6 (.clk(Clock), .D(bit_8), .Q(Q[6]), .preset(1'b0), .reset(Reset));  // open: Qn
  D_Flip_Flop #(.trigger("rising")) bit1 (.clk(Clock), .D(bit_3), .Q(Q[1]), .preset(1'b0), .reset(Reset));  // open: Qn
  D_Flip_Flop #(.trigger("rising")) bit7 (.clk(Clock), .D(bit_9), .Q(Q[7]), .preset(1'b0), .reset(Reset));  // open: Qn
  D_Flip_Flop #(.trigger("rising")) bit2 (.clk(Clock), .D(bit_4), .Q(Q[2]), .preset(1'b0), .reset(Reset));  // open: Qn
  D_Flip_Flop #(.trigger("rising")) bit3 (.clk(Clock), .D(bit_5), .Q(Q[3]), .preset(1'b0), .reset(Reset));  // open: Qn

  // Other names for the same wires on the sheet: mux_1[7:0] = {bit_9, bit_8, bit_7, bit_6, bit_5, bit_4, bit_3, bit_2};
  //   q_10 = Q[0]; q_11 = Q[1]; q_12 = Q[2]; q_13 = Q[3]; q_14 = Q[4]; q_15 = Q[5]; q_16 = Q[6]; q_17 = Q[7]

  // Notes on the sheet:
  //   ConsoleRegister8 / gates, wiring, explicit single-bit flip-flops; bulk RAM and font ROM only
endmodule

module ConsoleLogic (
  input  [15:0] Address,
  input  [7:0] DataIn,
  input  Write,
  input  Read,
  input  SysClock,
  input  Reset,
  input  HostValid,
  input  [6:0] HostASCII,
  output [7:0] DataOut,
  output Ready,
  output Busy,
  output [5:0] CursorX,
  output [4:0] CursorY,
  output [4:0] Origin,
  output HostAck,
  output [5:0] PixelColumn,
  output [7:0] PixelY,
  output [7:0] PixelBits,
  output PixelDraw
);

  wire and_36, and_37, and_38, and_39, and_40, and_41, and_42, and_43, and_44, and_45, and_46, and_47,
       and_48, and_49, and_50, and_78, and_79, and_80, and_81, and_82, and_83, and_84, and_85, and_86,
       and_87, and_88, and_89, and_90, and_91, and_92, and_120, and_121, and_122, and_123, and_124, and_125,
       and_126, and_127, and_128, and_129, and_130, and_131, and_132, and_133, and_134, and_135, and_136,
       and_137, and_139, and_142, and_176, and_177, and_178, and_179, and_180, and_181, and_194, and_195,
       and_196, and_197, and_198, and_199, and_213, and_214, and_215, and_216, and_217, and_218, and_220,
       and_221, and_222, and_231, and_232, and_233, and_234, and_235, and_236, and_238, and_239, and_248,
       and_249, and_250, and_251, and_252, and_253, and_254, and_256, and_271, and_272, and_273, and_274,
       and_275, and_276, and_289, and_290, and_291, and_292, and_293, and_295, and_296, and_303, and_304,
       and_305, and_306, and_307, and_319, and_328, and_329, and_330, and_331, and_341, and_342, and_343,
       and_344, and_345, and_347, and_352, and_356, and_357, and_359, and_376, and_377, and_378, and_379,
       and_380, and_390, and_391, and_392, and_393, and_394, and_395, and_396, and_437, and_474, and_511,
       bit_144, bit_145, bit_146, bit_147, bit_148, bit_149, bit_150, bit_333, bit_334, bit_335, bit_336,
       bit_337, bit_338, bit_353, bit_354, bit_355, bit_368, bit_369, bit_370, bit_371, bit_372, bit_373,
       bit_381, bit_382, bit_383, bit_384, bit_385, bit_386, bit_387, bit_388, bit_431, bit_432, bit_433,
       bit_434, bit_435, bit_436, bit_442, bit_443, bit_444, bit_445, bit_446, bit_447, bit_468, bit_469,
       bit_470, bit_471, bit_472, bit_473, bit_479, bit_480, bit_481, bit_482, bit_483, bit_484, bit_505,
       bit_506, bit_507, bit_508, bit_509, bit_510, bit_516, bit_517, bit_518, bit_519, bit_520, bit_521,
       bit_531, bit_532, bit_533, bit_534, bit_535, bit_536, bit_537, bit_538, bit_539, bit_540, bit_547,
       bit_548, bit_549, bit_550, bit_551, ClearPulse, not_6, not_7, not_24, not_25, not_26, not_27, not_28,
       not_29, not_30, not_31, not_32, not_33, not_34, not_35, not_67, not_68, not_69, not_70, not_71,
       not_72, not_73, not_74, not_75, not_76, not_77, not_109, not_110, not_111, not_112, not_113, not_114,
       not_115, not_116, not_117, not_118, not_119, not_138, not_141, not_172, not_173, not_174, not_175,
       not_189, not_190, not_191, not_192, not_193, not_208, not_209, not_210, not_211, not_212, not_219,
       not_237, not_246, not_247, not_265, not_266, not_267, not_268, not_269, not_270, not_283, not_284,
       not_285, not_286, not_287, not_288, not_294, not_302, not_318, not_327, not_339, not_340, not_346,
       not_351, not_358, not_374, not_375, not_389, not_542, or_143, or_200, or_223, or_255, or_257, or_314,
       or_315, or_348, or_349, or_360, or_438, or_475, or_512, or_524, RenderBusy, ScrollBusy;
  wire [2:0] mux_364, sum_362;
  wire [4:0] mux_332, sum_317, sum_321;
  wire [5:0] mux_310, mux_313, mux_367, mux_399, RenderColumn, sum_309, sum_312, sum_366, sum_398, sum_440,
       sum_477, sum_514;
  wire [6:0] mux_527, ReadCharacter, RenderCharacter;
  wire [7:0] mux_154, mux_155, mux_402, sum_401;
  wire [10:0] mux_523, mux_525;

  not not_1 (not_7, SysClock);
  not not_2 (not_28, Address[5]);
  not not_3 (not_34, Address[11]);
  and and_1 (and_40, and_39, not_28);
  and and_2 (and_46, and_45, not_34);
  not not_4 (not_67, Address[1]);
  not not_5 (not_73, Address[8]);
  and and_3 (and_79, and_78, not_68);
  and and_4 (and_85, and_84, not_73);
  and and_5 (and_91, and_90, Address[14]);
  not u_not_6 (not_112, Address[5]);
  not u_not_7 (not_118, Address[11]);
  and and_6 (and_124, and_123, not_112);
  and and_7 (and_130, and_129, not_118);
  and and_8 (and_136, and_135, Ready);
  and and_9 (and_142, Ready, not_141);
  not not_8 (not_175, DataIn[6]);
  and and_10 (and_181, and_180, not_175);
  not not_9 (not_193, DataIn[6]);
  and and_11 (and_199, and_198, not_193);
  not not_10 (not_211, DataIn[5]);
  and and_12 (and_217, and_216, not_211);
  or or_1 (or_223, DataIn[5], DataIn[6]);
  and and_13 (and_235, and_234, DataIn[5]);
  not not_11 (not_246, CursorX[3]);
  and and_14 (and_252, and_251, CursorX[5]);
  or or_2 (or_257, Reset, ClearPulse);
  not not_12 (not_269, DataIn[5]);
  and and_15 (and_275, and_274, not_269);
  not not_13 (not_286, CursorX[3]);
  and and_16 (and_292, and_291, not_287);
  not not_14 (not_302, CursorY[3]);
  or or_3 (or_314, and_239, or_255);
  and and_17 (and_319, or_255, not_318);
  and and_18 (and_328, Origin[0], Origin[1]);
  and and_19 (and_344, and_343, not_340);
  or or_4 (or_349, ScrollBusy, ClearPulse);
  and and_20 (and_356, bit_353, bit_354);
  ConsoleRegister7 consoleregister7_1 (
    .Data(DataIn[6:0]), .Load(and_352), .Clock(not_7), .Reset(or_257), .Q(RenderCharacter));
  ConsoleMux3 consolemux3_1 (.A(sum_362), .B(3'b000), .Select(and_357), .Y(mux_364));
  and and_21 (and_379, and_378, not_375);
  and and_22 (and_392, and_391, bit_384);
  ConsoleAdd6 consoleadd6_1 (.A({bit_373, bit_372, bit_371, bit_370, bit_369, bit_368}), .B(6'b000001), .Y(sum_398));
  ConsoleRegister8 consoleregister8_1 (
    .Data(mux_402), .Load(and_380), .Clock(not_7), .Reset(Reset),
    .Q({bit_388, bit_387, bit_386, bit_385, bit_384, bit_383, bit_382, bit_381}));
  and and_23 (and_474, bit_472, bit_471);
  ConsoleAdd6 consoleadd6_2 (
    .A({1'b0, CursorY}), .B({1'b0, Origin}), .Y({bit_510, bit_509, bit_508, bit_507, bit_506, bit_505}));
  ConsoleMux6 consolemux6_1 (
    .A({bit_510, bit_509, bit_508, bit_507, bit_506, bit_505}), .B(sum_514), .Select(or_512),
    .Y({bit_521, bit_520, bit_519, bit_518, bit_517, bit_516}));
  not not_15 (not_29, Address[6]);
  not not_16 (not_35, Address[13]);
  and and_24 (and_41, and_40, not_29);
  and and_25 (and_47, and_46, Address[12]);
  not not_17 (not_68, Address[2]);
  not not_18 (not_74, Address[9]);
  and and_26 (and_80, and_79, not_69);
  and and_27 (and_86, and_85, not_74);
  and and_28 (and_92, and_91, Address[15]);
  not not_19 (not_113, Address[6]);
  not not_20 (not_119, Address[13]);
  and and_29 (and_125, and_124, not_113);
  and and_30 (and_131, and_130, Address[12]);
  and and_31 (and_137, and_136, not_6);
  or or_5 (or_143, and_142, HostAck);
  and and_32 (and_176, DataIn[0], not_172);
  and and_33 (and_194, not_189, DataIn[1]);
  or or_6 (or_200, and_181, and_199);
  not not_21 (not_212, DataIn[6]);
  and and_34 (and_218, and_217, not_212);
  and and_35 (and_236, and_235, DataIn[6]);
  not not_22 (not_247, CursorX[4]);
  and u_and_36 (and_253, and_239, and_252);
  not not_23 (not_270, DataIn[6]);
  and u_and_37 (and_276, and_275, not_270);
  not u_not_24 (not_287, CursorX[4]);
  and u_and_38 (and_293, and_292, not_288);
  and u_and_39 (and_303, CursorY[0], CursorY[1]);
  ConsoleAdd6 consoleadd6_3 (.A(CursorX), .B(6'b000001), .Y(sum_309));
  or or_7 (or_315, or_314, and_296);
  ConsoleRegister5 consoleregister5_1 (.Data(sum_317), .Load(and_319), .Clock(not_7), .Reset(or_257), .Q(CursorY));
  and u_and_40 (and_329, and_328, Origin[2]);
  not u_not_25 (not_339, bit_336);
  and u_and_41 (and_345, and_344, bit_338);
  or or_8 (Busy, or_349, RenderBusy);
  and u_and_42 (and_357, and_356, bit_355);
  ConsoleRegister6 consoleregister6_1 (.Data(CursorX), .Load(and_352), .Clock(not_7), .Reset(or_257), .Q(RenderColumn));
  ConsoleRegister3 consoleregister3_1 (
    .Data(mux_364), .Load(RenderBusy), .Clock(not_7), .Reset(or_257), .Q({bit_355, bit_354, bit_353}));
  not u_not_26 (not_374, bit_371);
  and u_and_43 (and_380, and_379, bit_373);
  and u_and_44 (and_393, and_392, bit_385);
  ConsoleMux6 consolemux6_2 (.A(sum_398), .B({6{1'b0}}), .Select(and_380), .Y(mux_399));
  ConsoleAdd6 consoleadd6_4 (.A({bit_436, bit_435, bit_434, bit_433, bit_432, bit_431}), .B(6'b101000), .Y(sum_440));
  or or_9 (or_475, bit_473, and_474);
  ConsoleMux7 consolemux7_1 (.A(DataIn[6:0]), .B(7'b0100000), .Select(ScrollBusy), .Y(mux_527));
  ConsoleMux6 consolemux6_3 (
    .A({bit_373, bit_372, bit_371, bit_370, bit_369, bit_368}), .B(RenderColumn), .Select(RenderBusy),
    .Y(PixelColumn));
  not u_not_27 (not_24, Address[0]);
  not u_not_28 (not_30, Address[7]);
  and u_and_45 (and_36, not_24, not_25);
  and u_and_46 (and_42, and_41, not_30);
  and u_and_47 (and_48, and_47, not_35);
  not u_not_29 (not_69, Address[3]);
  not u_not_30 (not_75, Address[10]);
  and u_and_48 (and_81, and_80, Address[4]);
  and u_and_49 (and_87, and_86, not_75);
  not u_not_31 (not_114, Address[7]);
  and u_and_50 (and_120, not_109, Address[1]);
  and and_51 (and_126, and_125, not_114);
  and and_52 (and_132, and_131, not_119);
  not u_not_32 (not_138, Ready);
  ConsoleRegister1 consoleregister1_1 (.Data(or_143), .Load(1'b1), .Clock(SysClock), .Reset(Reset), .Q(Ready));
  and and_53 (and_177, and_176, DataIn[2]);
  not u_not_33 (not_189, DataIn[0]);
  and and_54 (and_195, and_194, not_190);
  and and_55 (and_213, not_208, not_209);
  not u_not_34 (not_219, Busy);
  and and_56 (and_231, DataIn[0], DataIn[1]);
  not u_not_35 (not_237, and_236);
  and and_57 (and_248, CursorX[0], CursorX[1]);
  and and_58 (and_254, and_222, or_200);
  not not_36 (not_265, DataIn[0]);
  and and_59 (and_271, not_265, not_266);
  not not_37 (not_288, CursorX[5]);
  not not_38 (not_294, and_293);
  and and_60 (and_304, and_303, CursorY[2]);
  ConsoleMux6 consolemux6_4 (.A(sum_309), .B({6{1'b0}}), .Select(or_255), .Y(mux_310));
  ConsoleRegister6 consoleregister6_2 (.Data(mux_313), .Load(or_315), .Clock(not_7), .Reset(or_257), .Q(CursorX));
  and and_61 (and_330, and_329, not_327);
  not not_39 (not_340, bit_337);
  not not_40 (not_346, and_345);
  not not_41 (not_358, and_357);
  ConsoleRegister5 consoleregister5_2 (
    .Data(CursorY), .Load(and_352), .Clock(not_7), .Reset(or_257),
    .Q({bit_551, bit_550, bit_549, bit_548, bit_547}));
  not not_42 (not_375, bit_372);
  and and_62 (and_394, and_393, bit_386);
  ConsoleRegister6 consoleregister6_3 (
    .Data(mux_399), .Load(1'b1), .Clock(not_7), .Reset(Reset),
    .Q({bit_373, bit_372, bit_371, bit_370, bit_369, bit_368}));
  ConsoleAdd6 consoleadd6_5 (
    .A({1'b0, bit_388, bit_387, bit_386, bit_385, bit_384}), .B({1'b0, Origin}),
    .Y({bit_436, bit_435, bit_434, bit_433, bit_432, bit_431}));
  ConsoleMux6 consolemux6_5 (
    .A({bit_436, bit_435, bit_434, bit_433, bit_432, bit_431}), .B(sum_440), .Select(or_438),
    .Y({bit_447, bit_446, bit_445, bit_444, bit_443, bit_442}));
  and and_63 (and_511, bit_509, bit_508);
  RAM #(.addrWidth(11), .dataWidth(7), .databus("bibus"), .enables("byte"), .asyncread("true"), .trigger("falling"), .clearpin("true")) TEXT_RAM (
    .addr(mux_525), .we(or_524), .oe(1'b1), .clk(SysClock), .din(mux_527), .dout(ReadCharacter), .clr(or_257));
  not not_43 (not_25, Address[1]);
  not not_44 (not_31, Address[8]);
  and and_64 (and_37, and_36, not_26);
  and and_65 (and_43, and_42, not_31);
  and and_66 (and_49, and_48, Address[14]);
  not not_45 (not_70, Address[5]);
  not not_46 (not_76, Address[11]);
  and and_67 (and_82, and_81, not_70);
  and and_68 (and_88, and_87, not_76);
  not not_47 (not_109, Address[0]);
  not not_48 (not_115, Address[8]);
  and and_69 (and_121, and_120, not_110);
  and and_70 (and_127, and_126, not_115);
  and and_71 (and_133, and_132, Address[14]);
  and and_72 (and_139, not_138, HostValid);
  ConsoleRegister7 consoleregister7_2 (
    .Data(HostASCII), .Load(HostAck), .Clock(SysClock), .Reset(Reset),
    .Q({bit_150, bit_149, bit_148, bit_147, bit_146, bit_145, bit_144}));
  ConsoleMux8 consolemux8_1 (
    .A({8{1'b0}}), .B({Ready, bit_150, bit_149, bit_148, bit_147, bit_146, bit_145, bit_144}),
    .Select(and_50), .Y(mux_154));
  not not_49 (not_172, DataIn[1]);
  and and_73 (and_178, and_177, DataIn[3]);
  not not_50 (not_190, DataIn[2]);
  and and_74 (and_196, and_195, DataIn[3]);
  not not_51 (not_208, DataIn[0]);
  and and_75 (and_214, and_213, DataIn[2]);
  and and_76 (and_220, Write, and_134);
  and and_77 (and_232, and_231, DataIn[2]);
  and u_and_78 (and_238, or_223, not_237);
  and u_and_79 (and_249, and_248, CursorX[2]);
  or or_10 (or_255, and_254, and_253);
  not not_52 (not_266, DataIn[1]);
  and u_and_80 (and_272, and_271, not_267);
  not not_53 (not_283, CursorX[0]);
  and u_and_81 (and_289, not_283, not_284);
  and u_and_82 (and_295, and_222, and_276);
  and u_and_83 (and_305, and_304, not_302);
  ConsoleAdd5 consoleadd5_1 (.A(Origin), .B(5'b00001), .Y(sum_321));
  and u_and_84 (and_331, and_330, Origin[4]);
  and u_and_85 (and_341, bit_333, bit_334);
  and u_and_86 (and_347, ScrollBusy, not_346);
  not not_54 (not_351, and_307);
  and u_and_87 (and_359, RenderBusy, not_358);
  ConsoleAdd6 consoleadd6_6 (.A({bit_338, bit_337, bit_336, bit_335, bit_334, bit_333}), .B(6'b000001), .Y(sum_366));
  and u_and_88 (and_376, bit_368, bit_369);
  not not_55 (not_389, bit_387);
  and u_and_89 (and_395, and_394, not_389);
  ConsoleAdd6 consoleadd6_7 (.A({bit_473, bit_472, bit_471, bit_470, bit_469, bit_468}), .B(6'b101000), .Y(sum_477));
  or or_11 (or_512, bit_510, and_511);
  ConsoleMux11 consolemux11_1 (
    .A({bit_483, bit_482, bit_481, bit_480, bit_479, CursorX}),
    .B({bit_520, bit_519, bit_518, bit_517, bit_516, bit_338, bit_337, bit_336, bit_335, bit_334, bit_333}),
    .Select(ScrollBusy), .Y(mux_523));
  ROM #(.addrWidth(10), .dataWidth(8)) ORIGINAL_5x7_FONT (
    .addr({bit_540, bit_539, bit_538, bit_537, bit_536, bit_535, bit_534, bit_533, bit_532, bit_531}),
    .data(PixelBits));
  not not_56 (not_26, Address[2]);
  not not_57 (not_32, Address[9]);
  and u_and_90 (and_38, and_37, not_27);
  and u_and_91 (and_44, and_43, not_32);
  and u_and_92 (and_50, and_49, Address[15]);
  not not_58 (not_71, Address[6]);
  not not_59 (not_77, Address[13]);
  and and_93 (and_83, and_82, not_71);
  and and_94 (and_89, and_88, Address[12]);
  not not_60 (not_110, Address[2]);
  not not_61 (not_116, Address[9]);
  and and_95 (and_122, and_121, not_111);
  and and_96 (and_128, and_127, not_116);
  and and_97 (and_134, and_133, Address[15]);
  and and_98 (HostAck, and_139, not_6);
  ConsoleMux8 consolemux8_2 (.A(mux_154), .B({Ready, {7{1'b0}}}), .Select(and_92), .Y(mux_155));
  not not_62 (not_173, DataIn[4]);
  and and_99 (and_179, and_178, not_173);
  not not_63 (not_191, DataIn[4]);
  and and_100 (and_197, and_196, not_191);
  not not_64 (not_209, DataIn[1]);
  and and_101 (and_215, and_214, DataIn[3]);
  and and_102 (and_221, and_220, not_219);
  and and_103 (and_233, and_232, DataIn[3]);
  and and_104 (and_239, and_222, and_238);
  and and_105 (and_250, and_249, not_246);
  and and_106 (and_256, and_222, and_218);
  not not_65 (not_267, DataIn[2]);
  and and_107 (and_273, and_272, DataIn[3]);
  not not_66 (not_284, CursorX[1]);
  and and_108 (and_290, and_289, not_285);
  and and_109 (and_296, and_295, not_294);
  and and_110 (and_306, and_305, CursorY[4]);
  ConsoleAdd6 consoleadd6_8 (.A(CursorX), .B({6{1'b1}}), .Y(sum_312));
  ConsoleAdd5 consoleadd5_2 (.A(CursorY), .B(5'b00001), .Y(sum_317));
  ConsoleMux5 consolemux5_1 (.A(sum_321), .B({5{1'b0}}), .Select(and_331), .Y(mux_332));
  and and_111 (and_342, and_341, bit_335);
  or or_12 (or_348, and_307, and_347);
  and and_112 (and_352, and_239, not_351);
  or or_13 (or_360, and_352, and_359);
  ConsoleAdd3 consoleadd3_1 (.A({bit_355, bit_354, bit_353}), .B(3'b001), .Y(sum_362));
  ConsoleMux6 consolemux6_6 (.A(sum_366), .B({6{1'b0}}), .Select(and_345), .Y(mux_367));
  and and_113 (and_377, and_376, bit_370);
  and and_114 (and_390, bit_381, bit_382);
  and and_115 (and_396, and_395, bit_388);
  ConsoleAdd8 consoleadd8_1 (
    .A({bit_388, bit_387, bit_386, bit_385, bit_384, bit_383, bit_382, bit_381}), .B(8'h1), .Y(sum_401));
  and and_116 (and_437, bit_435, bit_434);
  ConsoleAdd6 consoleadd6_9 (
    .A({1'b0, CursorY}), .B({1'b0, Origin}), .Y({bit_473, bit_472, bit_471, bit_470, bit_469, bit_468}));
  ConsoleMux6 consolemux6_7 (
    .A({bit_473, bit_472, bit_471, bit_470, bit_469, bit_468}), .B(sum_477), .Select(or_475),
    .Y({bit_484, bit_483, bit_482, bit_481, bit_480, bit_479}));
  or or_14 (or_524, and_239, ScrollBusy);
  ConsoleMux3 consolemux3_2 (
    .A({bit_383, bit_382, bit_381}), .B({bit_355, bit_354, bit_353}), .Select(RenderBusy),
    .Y({bit_533, bit_532, bit_531}));
  not u_not_67 (not_542, or_524);
  not u_not_68 (not_6, Reset);
  not u_not_69 (not_27, Address[3]);
  not u_not_70 (not_33, Address[10]);
  and and_117 (and_39, and_38, Address[4]);
  and and_118 (and_45, and_44, not_33);
  not u_not_71 (not_72, Address[7]);
  and and_119 (and_78, Address[0], not_67);
  and u_and_120 (and_84, and_83, not_72);
  and u_and_121 (and_90, and_89, not_77);
  not u_not_72 (not_111, Address[3]);
  not u_not_73 (not_117, Address[10]);
  and u_and_122 (and_123, and_122, Address[4]);
  and u_and_123 (and_129, and_128, not_117);
  and u_and_124 (and_135, and_50, Read);
  not u_not_74 (not_141, and_137);
  ConsoleMux8 consolemux8_3 (.A(mux_155), .B({Busy, {7{1'b0}}}), .Select(and_134), .Y(DataOut));
  not u_not_75 (not_174, DataIn[5]);
  and u_and_125 (and_180, and_179, not_174);
  not u_not_76 (not_192, DataIn[5]);
  and u_and_126 (and_198, and_197, not_192);
  not u_not_77 (not_210, DataIn[4]);
  and u_and_127 (and_216, and_215, not_210);
  and u_and_128 (and_222, and_221, not_6);
  and u_and_129 (and_234, and_233, DataIn[4]);
  and u_and_130 (and_251, and_250, not_247);
  ConsoleRegister1 consoleregister1_2 (.Data(and_256), .Load(1'b1), .Clock(not_7), .Reset(Reset), .Q(ClearPulse));
  not not_78 (not_268, DataIn[4]);
  and u_and_131 (and_274, and_273, not_268);
  not not_79 (not_285, CursorX[2]);
  and u_and_132 (and_291, and_290, not_286);
  and u_and_133 (and_307, or_255, and_306);
  ConsoleMux6 consolemux6_8 (.A(mux_310), .B(sum_312), .Select(and_296), .Y(mux_313));
  not not_80 (not_318, and_306);
  not not_81 (not_327, Origin[3]);
  ConsoleRegister5 consoleregister5_3 (.Data(mux_332), .Load(and_307), .Clock(not_7), .Reset(or_257), .Q(Origin));
  and u_and_134 (and_343, and_342, not_339);
  ConsoleRegister1 consoleregister1_3 (.Data(or_348), .Load(1'b1), .Clock(not_7), .Reset(or_257), .Q(ScrollBusy));
  ConsoleRegister1 consoleregister1_4 (.Data(or_360), .Load(1'b1), .Clock(not_7), .Reset(or_257), .Q(RenderBusy));
  ConsoleRegister6 consoleregister6_4 (
    .Data(mux_367), .Load(ScrollBusy), .Clock(not_7), .Reset(or_257),
    .Q({bit_338, bit_337, bit_336, bit_335, bit_334, bit_333}));
  and u_and_135 (and_378, and_377, not_374);
  and u_and_136 (and_391, and_390, bit_383);
  ConsoleMux8 consolemux8_4 (.A(sum_401), .B({8{1'b0}}), .Select(and_396), .Y(mux_402));
  or or_15 (or_438, bit_436, and_437);
  ConsoleAdd6 consoleadd6_10 (.A({bit_510, bit_509, bit_508, bit_507, bit_506, bit_505}), .B(6'b101000), .Y(sum_514));
  ConsoleMux11 consolemux11_2 (
    .A({bit_446, bit_445, bit_444, bit_443, bit_442, bit_373, bit_372, bit_371, bit_370, bit_369, bit_368}),
    .B(mux_523), .Select(or_524), .Y(mux_525));
  ConsoleMux7 consolemux7_2 (
    .A(ReadCharacter), .B(RenderCharacter), .Select(RenderBusy),
    .Y({bit_540, bit_539, bit_538, bit_537, bit_536, bit_535, bit_534}));
  and u_and_137 (PixelDraw, not_542, not_6);
  ConsoleMux8 consolemux8_5 (
    .A({bit_388, bit_387, bit_386, bit_385, bit_384, bit_383, bit_382, bit_381}),
    .B({bit_551, bit_550, bit_549, bit_548, bit_547, bit_355, bit_354, bit_353}), .Select(RenderBusy),
    .Y(PixelY));

  // Other names for the same wires on the sheet: bit_8 = Address[0]; bit_51 = Address[0]; bit_93 = Address[0];
  //   bit_9 = Address[1]; bit_52 = Address[1]; bit_94 = Address[1]; bit_10 = Address[2]; bit_53 = Address[2];
  //   bit_95 = Address[2]; bit_11 = Address[3]; bit_54 = Address[3]; bit_96 = Address[3]; bit_12 = Address[4];
  //   bit_55 = Address[4]; bit_97 = Address[4]; bit_13 = Address[5]; bit_56 = Address[5]; bit_98 = Address[5];
  //   bit_14 = Address[6]; bit_57 = Address[6]; bit_99 = Address[6]; bit_15 = Address[7]; bit_58 = Address[7];
  //   bit_100 = Address[7]; bit_16 = Address[8]; bit_59 = Address[8]; bit_101 = Address[8]; bit_17 = Address[9];
  //   bit_60 = Address[9]; bit_102 = Address[9]; bit_18 = Address[10]; bit_61 = Address[10]; bit_103 = Address[10];
  //   bit_19 = Address[11]; bit_62 = Address[11]; bit_104 = Address[11]; bit_20 = Address[12]; bit_63 = Address[12];
  //   bit_105 = Address[12]; bit_21 = Address[13]; bit_64 = Address[13]; bit_106 = Address[13]; bit_22 = Address[14];
  //   bit_65 = Address[14]; bit_107 = Address[14]; bit_23 = Address[15]; bit_66 = Address[15]; bit_108 = Address[15];
  //   and_140 = HostAck; and_543 = PixelDraw;
  //   bus_151[7:0] = {Ready, bit_150, bit_149, bit_148, bit_147, bit_146, bit_145, bit_144}; bus_152[7] = Ready;
  //   bus_153[7] = Busy; or_350 = Busy; bit_156 = DataIn[0]; bit_165 = DataIn[0]; bit_182 = DataIn[0];
  //   bit_201 = DataIn[0]; bit_224 = DataIn[0]; bit_258 = DataIn[0]; bus_164[6:0] = DataIn[6:0]; bit_157 = DataIn[1];
  //   bit_166 = DataIn[1]; bit_183 = DataIn[1]; bit_202 = DataIn[1]; bit_225 = DataIn[1]; bit_259 = DataIn[1];
  //   bit_158 = DataIn[2]; bit_167 = DataIn[2]; bit_184 = DataIn[2]; bit_203 = DataIn[2]; bit_226 = DataIn[2];
  //   bit_260 = DataIn[2]; bit_159 = DataIn[3]; bit_168 = DataIn[3]; bit_185 = DataIn[3]; bit_204 = DataIn[3];
  //   bit_227 = DataIn[3]; bit_261 = DataIn[3]; bit_160 = DataIn[4]; bit_169 = DataIn[4]; bit_186 = DataIn[4];
  //   bit_205 = DataIn[4]; bit_228 = DataIn[4]; bit_262 = DataIn[4]; bit_161 = DataIn[5]; bit_170 = DataIn[5];
  //   bit_187 = DataIn[5]; bit_206 = DataIn[5]; bit_229 = DataIn[5]; bit_263 = DataIn[5]; bit_162 = DataIn[6];
  //   bit_171 = DataIn[6]; bit_188 = DataIn[6]; bit_207 = DataIn[6]; bit_230 = DataIn[6]; bit_264 = DataIn[6];
  //   bit_406 = bit_384; bit_418 = bit_384; bus_411[4:0] = {bit_388, bit_387, bit_386, bit_385, bit_384};
  //   bus_428[4:0] = {bit_388, bit_387, bit_386, bit_385, bit_384};
  //   ScanY[7:0] = {bit_388, bit_387, bit_386, bit_385, bit_384, bit_383, bit_382, bit_381}; bit_407 = bit_385;
  //   bit_419 = bit_385; bit_408 = bit_386; bit_420 = bit_386; bit_409 = bit_387; bit_421 = bit_387;
  //   bit_410 = bit_388; bit_422 = bit_388; bit_412 = bit_368;
  //   bus_448[10:0] = {bit_446, bit_445, bit_444, bit_443, bit_442, bit_373, bit_372, bit_371, bit_370, bit_369, bit_368};
  //   ScanColumn[5:0] = {bit_373, bit_372, bit_371, bit_370, bit_369, bit_368}; bit_413 = bit_369; bit_414 = bit_370;
  //   bit_415 = bit_371; bit_416 = bit_372; bit_417 = bit_373;
  //   mux_441[5:0] = {bit_447, bit_446, bit_445, bit_444, bit_443, bit_442}; bit_297 = CursorY[0];
  //   bit_455 = CursorY[0]; bit_492 = CursorY[0]; bus_465[4:0] = CursorY; bus_502[4:0] = CursorY;
  //   bit_298 = CursorY[1]; bit_456 = CursorY[1]; bit_493 = CursorY[1]; bit_299 = CursorY[2]; bit_457 = CursorY[2];
  //   bit_494 = CursorY[2]; bit_300 = CursorY[3]; bit_458 = CursorY[3]; bit_495 = CursorY[3]; bit_301 = CursorY[4];
  //   bit_459 = CursorY[4]; bit_496 = CursorY[4]; bit_322 = Origin[0]; bit_423 = Origin[0]; bit_460 = Origin[0];
  //   bit_497 = Origin[0]; bus_429[4:0] = Origin; bus_466[4:0] = Origin; bus_503[4:0] = Origin; bit_323 = Origin[1];
  //   bit_424 = Origin[1]; bit_461 = Origin[1]; bit_498 = Origin[1]; bit_324 = Origin[2]; bit_425 = Origin[2];
  //   bit_462 = Origin[2]; bit_499 = Origin[2]; bit_325 = Origin[3]; bit_426 = Origin[3]; bit_463 = Origin[3];
  //   bit_500 = Origin[3]; bit_326 = Origin[4]; bit_427 = Origin[4]; bit_464 = Origin[4]; bit_501 = Origin[4];
  //   bit_486 = bit_333;
  //   bus_522[10:0] = {bit_520, bit_519, bit_518, bit_517, bit_516, bit_338, bit_337, bit_336, bit_335, bit_334, bit_333};
  //   ClearColumn[5:0] = {bit_338, bit_337, bit_336, bit_335, bit_334, bit_333}; bit_487 = bit_334; bit_488 = bit_335;
  //   bit_489 = bit_336; bit_490 = bit_337; bit_491 = bit_338;
  //   mux_515[5:0] = {bit_521, bit_520, bit_519, bit_518, bit_517, bit_516}; bit_403 = bit_381;
  //   bus_528[2:0] = {bit_383, bit_382, bit_381}; bit_404 = bit_382; bit_405 = bit_383;
  //   bus_541[9:0] = {bit_540, bit_539, bit_538, bit_537, bit_536, bit_535, bit_534, bit_533, bit_532, bit_531};
  //   mux_529[2:0] = {bit_533, bit_532, bit_531};
  //   mux_530[6:0] = {bit_540, bit_539, bit_538, bit_537, bit_536, bit_535, bit_534}; bit_544 = bit_353;
  //   bus_552[7:0] = {bit_551, bit_550, bit_549, bit_548, bit_547, bit_355, bit_354, bit_353};
  //   RenderRow[2:0] = {bit_355, bit_354, bit_353}; bit_545 = bit_354; bit_546 = bit_355;
  //   RenderCellRow[4:0] = {bit_551, bit_550, bit_549, bit_548, bit_547}; bit_240 = CursorX[0]; bit_277 = CursorX[0];
  //   bit_449 = CursorX[0]; bus_485[10:0] = {bit_483, bit_482, bit_481, bit_480, bit_479, CursorX};
  //   bit_241 = CursorX[1]; bit_278 = CursorX[1]; bit_450 = CursorX[1]; bit_242 = CursorX[2]; bit_279 = CursorX[2];
  //   bit_451 = CursorX[2]; bit_243 = CursorX[3]; bit_280 = CursorX[3]; bit_452 = CursorX[3]; bit_244 = CursorX[4];
  //   bit_281 = CursorX[4]; bit_453 = CursorX[4]; bit_245 = CursorX[5]; bit_282 = CursorX[5]; bit_454 = CursorX[5];
  //   bit_163 = DataIn[7]; KeyboardByte[6:0] = {bit_150, bit_149, bit_148, bit_147, bit_146, bit_145, bit_144};
  //   mux_478[5:0] = {bit_484, bit_483, bit_482, bit_481, bit_480, bit_479};
  //   sum_430[5:0] = {bit_436, bit_435, bit_434, bit_433, bit_432, bit_431};
  //   sum_467[5:0] = {bit_473, bit_472, bit_471, bit_470, bit_469, bit_468};
  //   sum_504[5:0] = {bit_510, bit_509, bit_508, bit_507, bit_506, bit_505}

  // Notes on the sheet:
  //   ConsoleLogic / gates, wiring, explicit single-bit flip-flops; bulk RAM and font ROM only
  //   contents of ORIGINAL_5x7_FONT (hex, n*v repeats v):
  //   00 00 00 00 00 00 00 00 00 00 00 00 00 00 00 00 00 00 00 00 00 00 00 00 00 00 00 00 00 00 00 00 00
  //   00 00 00 00 00 00 00 00 00 00 00 00 00 00 00 00 00 00 00 00 00 00 00 00 00 00 00 00 00 00 00 00 00
  //   00 00 00 00 00 00 00 00 00 00 00 00 00 00 00 00 00 00 00 00 00 00 00 00 00 00 00 00 00 00 00 00 00
  //   00 00 00 00 00 00 00 00 00 00 00 00 00 00 00 00 00 00 00 00 00 00 00 00 00 00 00 00 00 00 00 00 00
  //   00 00 00 00 00 00 00 00 00 00 00 00 00 00 00 00 00 00 00 00 00 00 00 00 00 00 00 00 00 00 00 00 00
  //   00 00 00 00 00 00 00 00 00 00 00 00 00 00 00 00 00 00 00 00 00 00 00 00 00 00 00 00 00 00 00 00 00
  //   00 00 00 00 00 00 00 00 00 00 00 00 00 00 00 00 00 00 00 00 00 00 00 00 00 00 00 00 00 00 00 00 00
  //   00 00 00 00 00 00 00 00 00 00 00 00 00 00 00 00 00 00 00 00 00 00 00 00 00 00 00 00 00 00 00 00 00
  //   08 08 08 08 08 00 08 00 14 14 14 00 00 00 00 00 14 3e 14 14 3e 14 00 00 08 3c 0a 1c 28 1e 08 00 26
  //   16 10 08 04 34 32 00 0c 12 0a 04 2a 12 2c 00 08 08 04 00 00 00 00 00 10 08 04 04 04 08 10 00 04 08
  //   10 10 10 08 04 00 00 2a 1c 3e 1c 2a 00 00 00 08 08 3e 08 08 00 00 00 00 00 00 18 18 08 00 00 00 00
  //   3e 00 00 00 00 00 00 00 00 00 18 18 00 20 20 10 08 04 02 02 00 1c 22 32 2a 26 22 1c 00 08 0c 08 08
  //   08 08 1c 00 1c 22 20 10 08 04 3e 00 1e 20 20 1c 20 20 1e 00 10 18 14 12 3e 10 10 00 3e 02 02 1e 20
  //   20 1e 00 1c 02 02 1e 22 22 1c 00 3e 20 10 08 04 04 04 00 1c 22 22 1c 22 22 1c 00 1c 22 22 3c 20 20
  //   1c 00 00 18 18 00 18 18 00 00 00 18 18 00 18 18 08 00 20 10 08 04 08 10 20 00 00 00 3e 00 3e 00 00
  //   00 02 04 08 10 08 04 02 00 1c 22 20 10 08 00 08 00 1c 22 3a 2a 3a 02 1c 00 1c 22 22 3e 22 22 22 00
  //   1e 22 22 1e 22 22 1e 00 3c 02 02 02 02 02 3c 00 1e 22 22 22 22 22 1e 00 3e 02 02 1e 02 02 3e 00 3e
  //   02 02 1e 02 02 02 00 3c 02 02 3a 22 22 3c 00 22 22 22 3e 22 22 22 00 3e 08 08 08 08 08 3e 00 38 10
  //   10 10 12 12 0c 00 22 12 0a 06 0a 12 22 00 02 02 02 02 02 02 3e 00 22 36 2a 2a 22 22 22 00 22 26 26
  //   2a 32 32 22 00 1c 22 22 22 22 22 1c 00 1e 22 22 1e 02 02 02 00 1c 22 22 22 2a 12 2c 00 1e 22 22 1e
  //   0a 12 22 00 3c 02 02 1c 20 20 1e 00 3e 08 08 08 08 08 08 00 22 22 22 22 22 22 1c 00 22 22 22 22 22
  //   14 08 00 22 22 22 2a 2a 2a 14 00 22 22 14 08 14 22 22 00 22 22 14 08 08 08 08 00 3e 20 10 08 04 02
  //   3e 00 1c 04 04 04 04 04 1c 00 02 02 04 08 10 20 20 00 1c 10 10 10 10 10 1c 00 08 14 22 00 00 00 00
  //   00 00 00 00 00 00 00 3e 00 04 08 10 00 00 00 00 00 1c 22 22 3e 22 22 22 00 1e 22 22 1e 22 22 1e 00
  //   3c 02 02 02 02 02 3c 00 1e 22 22 22 22 22 1e 00 3e 02 02 1e 02 02 3e 00 3e 02 02 1e 02 02 02 00 3c
  //   02 02 3a 22 22 3c 00 22 22 22 3e 22 22 22 00 3e 08 08 08 08 08 3e 00 38 10 10 10 12 12 0c 00 22 12
  //   0a 06 0a 12 22 00 02 02 02 02 02 02 3e 00 22 36 2a 2a 22 22 22 00 22 26 26 2a 32 32 22 00 1c 22 22
  //   22 22 22 1c 00 1e 22 22 1e 02 02 02 00 1c 22 22 22 2a 12 2c 00 1e 22 22 1e 0a 12 22 00 3c 02 02 1c
  //   20 20 1e 00 3e 08 08 08 08 08 08 00 22 22 22 22 22 22 1c 00 22 22 22 22 22 14 08 00 22 22 22 2a 2a
  //   2a 14 00 22 22 14 08 14 22 22 00 22 22 14 08 08 08 08 00 3e 20 10 08 04 02 3e 00 30 08 08 04 08 08
  //   30 00 08 08 08 08 08 08 08 00 06 08 08 10 08 08 06 00 00 00 24 1a 00 00 00 00 00 00 00 00 00 00 00
  //   00
endmodule

module Apple1Console (
  input  [15:0] Address,
  input  [7:0] DataIn,
  input  Write,
  input  Read,
  input  SysClock,
  input  Reset,
  output [7:0] DataOut,
  output Ready,
  output Busy,
  output [5:0] CursorX,
  output [4:0] CursorY,
  output [4:0] Origin,
  output HostOverflow
);

  wire HostAck, HostValid, PixelDraw;
  wire [5:0] PixelColumn;
  wire [6:0] HostASCII;
  wire [7:0] PixelBits, PixelY;

  // ConsoleHost consolehost_1: pin names not known; wires that end beside it: SysClock, Reset, HostAck, PixelDraw, PixelColumn, PixelY, PixelBits
  ConsoleLogic consolelogic_1 (
    .Address(Address), .DataIn(DataIn), .Write(Write), .Read(Read), .SysClock(SysClock), .Reset(Reset),
    .HostValid(HostValid), .HostASCII(HostASCII), .DataOut(DataOut), .Ready(Ready), .Busy(Busy),
    .CursorX(CursorX), .CursorY(CursorY), .Origin(Origin), .HostAck(HostAck), .PixelColumn(PixelColumn),
    .PixelY(PixelY), .PixelBits(PixelBits), .PixelDraw(PixelDraw));

  // Notes on the sheet:
  //   BITWRIGHT / GATE-BUILT 40 x 24 TERMINAL
  //   Poke the screen to type. Load .mon files through the button. CPU firmware consumes the ASCII stream.
  //   Open ConsoleLogic below to inspect MMIO, keyboard latch, cursor, wrapping, scrolling, RAM scan and font lookup.
  //   Display: original 5x7 glyphs in 8x8 cells; digital scan. No NTSC or cycle-exact Apple-1 claim.
  //   HOST ADAPTER: ASCII capture and raw retained pixels only.
endmodule
