// Logisim project terminal-bench.circ as structural Verilog: 2 circuits, main circuit M0Workbench
module M0Workbench (
  input  Run,
  input  Clear,
  input  Reset,
  output Available,
  output [6:0] ASCII,
  output Transfer,
  output TtyClear,
  output KeyboardClear,
  output ClockSeen
);

  Clock #(.highDuration(1), .lowDuration(1)) HostClock (.out(ClockSeen));
  Keyboard #(.buflen(32), .trigger("rising")) keyboard_1 (
    .clk(ClockSeen), .re(Transfer), .clr(KeyboardClear), .avail(Available), .data(ASCII));
  TerminalControl terminalcontrol_1 (
    .Run(Run), .Clear(Clear), .Reset(Reset), .Available(Available), .Transfer(Transfer), .TtyClear(TtyClear),
    .KeyboardClear(KeyboardClear));
  TTY #(.rows(8), .cols(32), .trigger("rising")) tty_1 (.data(ASCII), .clk(ClockSeen), .we(Transfer), .clr(TtyClear));

  // Other names for the same wires on the sheet: KClear = KeyboardClear; SysClock = ClockSeen

  // Notes on the sheet:
  //   Run: initial=0x1
  //   BITWRIGHT / M0 KEYBOARD TERMINAL
  //   Use Poke, enable clock ticks, click the Keyboard, and type ASCII. Run=1 forwards characters.
  //   Stock host adapters + gate-built control. No CPU or machine FIFO yet. No Java library required.
  //   Run=0: hold queued input.
  //   Clear=1: clear screen, hold queued input.
  //   Reset=1: clear screen and input queue.
  //   64 ticks/s; 32 transfers/s.
  //   Clock keeps running.
  //   KEYBOARD / click here, then type
  //   Inspect TerminalControl to see the gates.
  //   TEXT MONITOR / 32 columns x 8 rows
  //   Observable circuit pins
  //   ASCII stays at the queued front byte.
  //   Available=1 means input is waiting.
endmodule

module TerminalControl (
  input  Run,
  input  Clear,
  input  Reset,
  input  Available,
  output Transfer,
  output TtyClear,
  output KeyboardClear
);

  wire NotClear, Ready;

  and and_1 (Ready, Run, Available);
  or or_1 (TtyClear, Clear, Reset);
  not not_1 (NotClear, TtyClear);
  and and_2 (Transfer, Ready, NotClear);

  assign KeyboardClear = Reset;

  // Notes on the sheet:
  //   Terminal control / Run and Available permit one transfer; Clear or Reset inhibits it
  //   No gated clock: Run and clear controls gate data transfer, while the source clock keeps running.
endmodule
